# Fritzing sketch buffer_ex_bb (saved by Fritzing 0.9.3b)
breadboards: 1

parts:
  U1 = AD8561 - Ultrafast 7ns Single Supply Comparator [part_number=AD8541]
  C1 = Electrolytic Capacitor [capacitance=0.1µF package="100 mil [THT, electrolytic]"]
  R1 = Resistor [tolerance=±5% resistance=4.7k package=THT]
  R2 = Resistor [tolerance=±5% resistance=4.7k package=THT]
  R3 = Resistor [tolerance=±5% resistance=10k package=THT]

nets:
  N1: U1.+IN, U1.GND, R2.Pin_0, R3.Pin_0
  N2: U1.-IN, R1.Pin_1
  N3: U1.V-, C1.-
  N4: U1.OUT, C1.+
  N5: R2.Pin_1, R3.Pin_1

notes:
  CA-V
  5V
  CB-H
  GND
  2.5V
