# Fritzing sketch summing_amp_config_bb (saved by Fritzing 0.9.3b)
breadboards: 1

parts:
  U1 = AD8561 - Ultrafast 7ns Single Supply Comparator [part_number=AD8541]
  C1 = Electrolytic Capacitor [capacitance=0.1µF package="100 mil [THT, electrolytic]"]
  R1 = Resistor [tolerance=±5% resistance=4.7k package=THT]
  R3 = Resistor [tolerance=±5% resistance=10k package=THT]
  R4 = Resistor [tolerance=±5% resistance=1k package=THT]
  R5 = Resistor [tolerance=±5% resistance=4.7k package=THT]
  R6 = Resistor [tolerance=±5% resistance=20k package=THT]
  R8 = Resistor [tolerance=±5% resistance=10k package=THT]
  R9 = Resistor [tolerance=±5% resistance=4.7k package=THT]

nets:
  N1: U1.+IN, R1.Pin_1, R4.Pin_0, R5.Pin_1, R6.Pin_1, R8.Pin_1, R9.Pin_1
  N2: U1.-IN, R3.Pin_1
  N3: U1.V-, C1.-
  N4: U1.GND, R3.Pin_0, R4.Pin_1
  N5: U1.OUT, C1.+
  N6: R1.Pin_0, R5.Pin_0

notes:
  5V
  CB-H
  GND
  2.5V
  PIO0
  PIO1
  PIO2
  PIO3
