# Fritzing sketch unity_gain_follower_bb (saved by Fritzing 0.9.3b)
breadboards: 1

parts:
  U1 = AD8561 - Ultrafast 7ns Single Supply Comparator [part_number=AD8541]
  C1 = Electrolytic Capacitor [capacitance=0.1µF package="100 mil [THT, electrolytic]"]

nets:
  N1: U1.+IN, U1.GND
  N2: U1.OUTB, C1.+

notes:
  CA-V
  5V
  CB-H
  GND
