# Fritzing sketch lower_forward_voltage_drop_bb (saved by Fritzing 0.9.3b)
breadboards: 1

parts:
  R1 = Resistor [tolerance=±5% resistance=1k package=THT]
  2N3904 = NPN-Transistor [package="TO92 [THT]"]
  2N2906 = PNP-Transistor [package="TO92 [THT]"]
  R2 = Resistor [tolerance=±5% resistance=150k package=THT]

nets:
  N1: R1.Pin_0, 2N3904.C, 2N2906.B
  N2: 2N3904.E, 2N2906.C
  N3: 2N3904.B, 2N2906.E, R2.Pin_1

notes:
  CB-H
  CA-V
  GND
  +5V
