# Fritzing sketch npn_diode_conn_bb (saved by Fritzing 0.9.3b)
breadboards: 1

parts:
  R1 = Resistor [tolerance=±5% resistance=470 package=THT]
  2N3904 = NPN-Transistor [package="TO92 [THT]"]

nets:
  N1: R1.Pin_0, 2N3904.B, 2N3904.C

notes:
  CB-H
  CA-V
  GND
