# Fritzing sketch pnp_emitter_base_rev_bdconfig_bb (saved by Fritzing 0.9.3b)
breadboards: 1

parts:
  2N3906 = PNP-Transistor [package="TO92 [THT]"]
  R1 = Resistor [tolerance=±5% resistance=100 package=THT]

nets:
  N1: 2N3906.B, 2N3906.C, R1.Pin_0

notes:
  (-) battery
  CB-H
  CA-V
