# Fritzing sketch vbe_multiplier_config_bb (saved by Fritzing 0.9.3b)
breadboards: 1

parts:
  R1 = Resistor [tolerance=±5% resistance=2.2k package=THT]
  2N3904 = NPN-Transistor [package="TO92 [THT]"]
  R2 = Resistor [tolerance=±5% resistance=2.2k package=THT]
  U1 = POT [package=3362u]
  R3 = Resistor [tolerance=±5% resistance=150k package=THT]

nets:
  N1: R1.Pin_0, U1.A
  N2: R1.Pin_1, 2N3904.C, R2.Pin_1, R3.Pin_0
  N3: 2N3904.E, R2.Pin_0, U1.E
  N4: 2N3904.B, U1.S

notes:
  CB-H
  CA-V
  GND
