# Fritzing sketch npn_led_switch_bb (saved by Fritzing 0.9.3b)
breadboards: 1

parts:
  Q1 = NPN-Transistor [package="TO92 [THT]"]
  LED1 = LED - 5mm [color="Red (633nm)" package="5 mm [THT]"]
  R1 = Resistor [tolerance=±5% resistance=100 package=THT]
  R2 = Resistor [tolerance=±5% resistance=6.8k package=THT]

nets:
  N1: Q1.B, R2.Pin_1
  N2: Q1.C, LED1.cathode
  N3: LED1.anode, R1.Pin_0

notes:
  CA-V
  GND
  +5V
  CB-H
