# Fritzing sketch res_npn_xnor_gate_bb (saved by Fritzing 0.9.3b)
breadboards: 1

parts:
  Q1 = NPN-Transistor [package="TO92 [THT]"]
  Q2 = NPN-Transistor [package="TO92 [THT]"]
  Q3 = NPN-Transistor [package="TO92 [THT]"]
  Q4 = NPN-Transistor [package="TO92 [THT]"]
  Q5 = NPN-Transistor [package="TO92 [THT]"]
  R1 = Resistor [tolerance=±5% resistance=10k package=THT]
  R2 = Resistor [tolerance=±5% resistance=6.8k package=THT]
  R3 = Resistor [tolerance=±5% resistance=6.8k package=THT]
  R4 = Resistor [tolerance=±5% resistance=10k package=THT]
  R5 = Resistor [tolerance=±5% resistance=1k package=THT]
  R7 = Resistor [tolerance=±5% resistance=1k package=THT]
  LED1 = LED - 5mm [color="Red (633nm)" package="5 mm [THT]"]
  R8 = Resistor [tolerance=±5% resistance=6.8k package=THT]
  R9 = Resistor [tolerance=±5% resistance=1k package=THT]
  R10 = Resistor [tolerance=±5% resistance=1k package=THT]
  R11 = Resistor [tolerance=±5% resistance=6.8k package=THT]
  R6 = Resistor [tolerance=±5% resistance=4.7k package=THT]
  R12 = Resistor [tolerance=±5% resistance=4.7k package=THT]

nets:
  N1: Q1.E, Q2.E, Q3.E, Q4.E, Q5.E, LED1.cathode
  N2: Q1.B, R1.Pin_1
  N3: Q1.C, R2.Pin_0, R5.Pin_0
  N4: Q2.B, R2.Pin_1, R3.Pin_0
  N5: Q2.C, R7.Pin_0, R6.Pin_0
  N6: Q3.B, R6.Pin_1, R12.Pin_0
  N7: Q3.C, LED1.anode
  N8: Q4.B, R4.Pin_1
  N9: Q4.C, R8.Pin_0, R9.Pin_0
  N10: Q5.B, R8.Pin_1, R11.Pin_0
  N11: Q5.C, R10.Pin_0, R12.Pin_1
  N12: R1.Pin_0, R11.Pin_1
  N13: R3.Pin_1, R4.Pin_0
  N14: R5.Pin_1, R7.Pin_1, R9.Pin_1, R10.Pin_1

notes:
  PIO1
  PIO0
  +5V
  CB-H
  GND
