# Fritzing sketch two_switches_parallel_bb (saved by Fritzing 0.9.3b)
breadboards: 1

parts:
  Q1 = NPN-Transistor [part_number=2N3904 package="TO92 [THT]"]
  LED1 = LED - 5mm [color="Red (633nm)" package="5 mm [THT]"]
  R1 = Resistor [tolerance=±5% resistance=100 package=THT]
  Q2 = NPN-Transistor [part_number=2N3904 package="TO92 [THT]"]
  R2 = Resistor [tolerance=±5% resistance=6.8k package=THT]
  R3 = Resistor [tolerance=±5% resistance=6.8k package=THT]

nets:
  N1: Q1.E, Q2.E
  N2: Q1.B, R3.Pin_1
  N3: Q1.C, LED1.cathode, Q2.C
  N4: LED1.anode, R1.Pin_0
  N5: Q2.B, R2.Pin_1

notes:
  PIO1
  GND
  +5V
  CB-H
  PIO0
