# Fritzing sketch npn_char_curve_bb (saved by Fritzing 0.9.3b)
breadboards: 1

parts:
  2N3904 = NPN-Transistor [package="TO92 [THT]"]
  R1 = Resistor [tolerance=±5% resistance=10k package=THT]

nets:
  N1: 2N3904.B, R1.Pin_1

notes:
  CB-V
  GND
  CA-V
