# Fritzing sketch pnp_char_curve_bb (saved by Fritzing 0.9.3b)
breadboards: 1

parts:
  R1 = Resistor [tolerance=±5% resistance=10k package=THT]
  2N3906 = PNP-Transistor [package="TO92 [THT]"]

nets:
  N1: R1.Pin_1, 2N3906.B

notes:
  CB-V
  +5V
  CA-V
