# Fritzing sketch bpf_bb (saved by Fritzing 0.9.3b)
breadboards: 1

parts:
  R1 = Resistor [tolerance=±5% resistance=1k package="2010 [SMD]"]
  L1 = Inductors [package=cr54-kit]
  C1 = Capacitor Polarized [package=cpol-radial-10uf-25v]

nets:
  N1: R1.Pin_1, L1.2, C1.-
  N2: L1.1, C1.+

notes:
  CA-V
  CB-V
  2.5V
  1kΩ
  0.047μF
  47mH
  10mH
