# Fritzing sketch bsf_bb (saved by Fritzing 0.9.3b)
breadboards: 1

parts:
  R1 = Resistor [tolerance=±5% resistance=1k package="2512 [SMD]"]
  C1 = Electrolytic Capacitor [capacitance=1μF package="0405 [SMD, electrolytic]"]
  L1 = Inductors [package=cr54]

nets:
  N1: R1.Pin_1, L1.1
  N2: C1.-, L1.2

notes:
  CA-V
  CB-V
  2.5V
  1kΩ
  0.1μF
  20mH
