# Fritzing sketch cascaded_rc_bb (saved by Fritzing 0.9.3b)
breadboards: 1

parts:
  C1 = Electrolytic Capacitor [capacitance=10μF package="0605 [SMD, electrolytic]"]
  R1 = Resistor [tolerance=±5% resistance=1k package="0603 [SMD]"]
  R2 = Resistor [tolerance=±5% resistance=1k package="0603 [SMD]"]
  C2 = Electrolytic Capacitor [capacitance=10μF package="0605 [SMD, electrolytic]"]
  R3 = Resistor [tolerance=±5% resistance=1k package="0603 [SMD]"]
  C3 = Electrolytic Capacitor [capacitance=10μF package="0605 [SMD, electrolytic]"]

nets:
  N1: C1.-, R2.Pin_1, R3.Pin_0
  N2: C1.+, C2.+, C3.+
  N3: R1.Pin_1, R2.Pin_0, C2.-
  N4: R3.Pin_1, C3.-

notes:
  GND
  CB-H
  CA-V
  1kΩ
  0.1μF
