# Fritzing sketch inc_ac_gain_bb (saved by Fritzing 0.9.3b)
breadboards: 1

parts:
  R1 = Resistor [tolerance=±5% resistance=470 package=THT]
  R2 = Resistor [tolerance=±5% resistance=68 package=THT]
  C1 = Ceramic Capacitor [capacitance=4.7µF package="100 mil [THT, multilayer]"]
  R4 = TRIMPOT [package=3362u-2]
  R7 = Resistor [tolerance=±5% resistance=100 package=THT]
  R8 = TRIMPOT [package=3362u-2]
  C2 = Ceramic Capacitor [capacitance=100nF package="100 mil [THT, multilayer]"]
  Q1 = NPN-Transistor [part_number=ZVN2110 package="TO92 [THT]"]

nets:
  N1: R1.Pin_1, R2.Pin_0, C1.0
  N2: R2.Pin_1, R4.CW, R8.CW, C2.0
  N3: C1.1, R4.WIPER, Q1.B
  N4: R4.CCW, R7.Pin_1
  N5: R7.Pin_0, Q1.E
  N6: R8.CCW, R8.WIPER, C2.1, Q1.C

notes:
  CA-V
  +5V
  CB-H
  GND
