# Fritzing sketch self_biased_config_bb (saved by Fritzing 0.9.3b)
breadboards: 1

parts:
  R1 = Resistor [tolerance=±5% resistance=470 package=THT]
  R2 = Resistor [tolerance=±5% resistance=68 package=THT]
  C1 = Ceramic Capacitor [capacitance=4.7µF package="100 mil [THT, multilayer]"]
  R5 = Resistor [tolerance=±5% resistance=4.7k package=THT]
  R6 = Resistor [tolerance=±5% resistance=1.5k package=THT]
  R7 = Resistor [tolerance=±5% resistance=47 package=THT]
  Q1 = NPN-Transistor [part_number=ZVN2110A package="TO92 [THT]"]

nets:
  N1: R1.Pin_1, R2.Pin_0, C1.0
  N2: R2.Pin_1, R6.Pin_1, Q1.C
  N3: C1.1, R5.Pin_0, R6.Pin_0, Q1.B
  N4: R5.Pin_1, R7.Pin_0, Q1.E

notes:
  CA-V
  +5V
  CB-H
  GND
