# Fritzing sketch measuring_current_ind_load-bb (saved by Fritzing 0.9.3b)
breadboards: 1

parts:
  IC1 = IC, DIP package, 14 pins [chip_label=OP484]
  R1 = Resistor [tolerance=±5% resistance=100k package=THT]
  R2 = Resistor [tolerance=±5% resistance=10k package=THT]
  R3 = Resistor [tolerance=±5% resistance=10k package=THT]
  R4 = Resistor [tolerance=±5% resistance=100k package=THT]
  R5 = Resistor [tolerance=±5% resistance=10 package=THT]
  R6 = Resistor [tolerance=±5% resistance=220 package=THT]
  L1 = Inductors [part_number=4.7mH package=cr54-kit]

nets:
  N1: IC1.pin5, R3.Pin_0, R4.Pin_0
  N2: IC1.pin6, R1.Pin_1, R2.Pin_0
  N3: IC1.pin7, R1.Pin_0, R6.Pin_0
  N4: R2.Pin_1, R5.Pin_1, L1.2
  N5: R3.Pin_1, R5.Pin_0
  N6: R4.Pin_1, L1.1

notes:
  +2.5V
  CB-H
  CA-V
  GND
  +5V
