# Fritzing sketch dc-dc_boost_converter_bb (saved by Fritzing 0.9.3b)
breadboards: 1

parts:
  L1 = Inductors [package=cr54-kit]
  D1 = Rectifier Diode [part_number=1N914 package="300 mil [THT]"]
  Q1 = NPN-Transistor [part_number=ZVN3310 package="TO92 [THT]"]
  D2 = Rectifier Diode [part_number=1N914 package="300 mil [THT]"]
  C1 = Tantalum Capacitor [capacitance=47µF package="100 mil [THT, tantalum]"]
  LED1 = LED - 5mm [color="Red (633nm)" package="5 mm [THT]"]
  LED2 = LED - 5mm [color="Yellow (585nm)" package="5 mm [THT]"]
  R1 = Resistor [tolerance=±5% resistance=100 package=THT]
  C2 = Tantalum Capacitor [capacitance=0.1µF package="100 mil [THT, tantalum]"]

nets:
  N1: L1.1, D1.cathode, Q1.E, D2.anode
  N2: D1.anode, Q1.C, C1.+, R1.Pin_1, C2.-
  N3: D2.cathode, C1.-, LED1.anode, C2.+
  N4: LED1.cathode, LED2.anode
  N5: LED2.cathode, R1.Pin_0

notes:
  CA-V
  GND
  +1.5V
  Vout
