# Fritzing sketch volt_power_supply_bb (saved by Fritzing 0.9.3b)
breadboards: 1

parts:
  Q1 = NPN-Transistor [part_number=2N3904 package="TO92 [THT]"]
  R1 = Resistor [tolerance=±5% resistance=47 package=THT]
  C1 = Tantalum Capacitor [capacitance=47µF package="100 mil [THT, tantalum]"]
  C2 = Tantalum Capacitor [capacitance=0.1µF package="100 mil [THT, tantalum]"]
  R2 = TRIMPOT [part_number="Potentiometer - 1kΩ" package=trimpot_pth_s3_lock]
  R3 = Resistor [tolerance=±5% resistance=1k package=THT]

nets:
  N1: Q1.E, R1.Pin_1, C1.+, C2.+
  N2: Q1.B, R2.WIPER
  N3: R1.Pin_0, C1.-, C2.-, R3.Pin_0
  N4: R2.CW, R3.Pin_1

notes:
  +2.5V
  +1.5V
  GND
