# Fritzing sketch diff_delayed_undelayed_signal_bb (saved by Fritzing 0.9.3b)
breadboards: 1

parts:
  U1 = OP482 - Low Power, High Speed JFET Quad Operational Amplifier [part_number=OP484]
  R1 = Resistor [tolerance=±5% resistance=10k package=THT]
  R2 = Resistor [tolerance=±5% resistance=10k package=THT]
  R3 = Resistor [tolerance=±5% resistance=6.8k package=THT]
  C1 = Electrolytic Capacitor [capacitance=0.1µF package="100 mil [THT, electrolytic]"]
  R4 = Resistor [tolerance=±5% resistance=100k package=THT]
  R5 = Resistor [tolerance=±5% resistance=100k package=THT]
  R6 = Resistor [tolerance=±5% resistance=100k package=THT]
  R7 = Resistor [tolerance=±5% resistance=220 package=THT]
  R8 = Resistor [tolerance=±5% resistance=100k package=THT]

nets:
  N1: U1.OUTA, R1.Pin_0, R5.Pin_0
  N2: U1.-INA, R1.Pin_1, R2.Pin_1
  N3: U1.+INA, R3.Pin_1, C1.-
  N4: U1.+INB, R4.Pin_0, R5.Pin_1
  N5: U1.-INB, R6.Pin_0, R8.Pin_1
  N6: U1.OUTB, R6.Pin_1, R7.Pin_0
  N7: R2.Pin_0, C1.+, R8.Pin_0
  N8: R3.Pin_0, R4.Pin_1

notes:
  +2.5V
  CH-A
  +5V
  GND
  CH-B
