# Fritzing sketch difference_amp_cha_v1andv2_bb (saved by Fritzing 0.9.3b)
breadboards: 1

parts:
  U1 = OP482 - Low Power, High Speed JFET Quad Operational Amplifier [part_number=OP484]
  R1 = Resistor [tolerance=±5% resistance=100k package=THT]
  R2 = Resistor [tolerance=±5% resistance=100k package=THT]
  R3 = Resistor [tolerance=±5% resistance=220 package=THT]
  R4 = Resistor [tolerance=±5% resistance=100k package=THT]
  R5 = Resistor [tolerance=±5% resistance=100k package=THT]
  R6 = Resistor [tolerance=±5% resistance=470 package=THT]
  C1 = Electrolytic Capacitor [capacitance=1µF package="100 mil [THT, electrolytic]"]

nets:
  N1: U1.+INB, R4.Pin_1, R5.Pin_1
  N2: U1.-INB, R1.Pin_0, R2.Pin_1, R6.Pin_0
  N3: U1.OUTB, R2.Pin_0, R3.Pin_0
  N4: R4.Pin_0, R6.Pin_1, C1.-
  N5: R5.Pin_0, C1.+

notes:
  CH-A
  +2.5V
  +5V
  GND
  CH-B
