# Fritzing sketch diode_conn_i_vs_v_bb (saved by Fritzing 0.9.3b)
breadboards: 1

parts:
  R1 = Resistor [tolerance=±5% resistance=47 package=THT]
  diode = Rectifier Diode [part_number=1N4001 package="300 mil [THT]"]

nets:
  N1: R1.Pin_1, diode.anode

notes:
  CA-V
  CB-H
  GND
