# Fritzing sketch diode_bridge_rectifier_bb (saved by Fritzing 0.9.3b)
breadboards: 1

parts:
  D1 = Rectifier Diode [part_number=1N914 package="300 mil [THT]"]
  R1 = Resistor [tolerance=±5% resistance=220 package=THT]
  D5 = Rectifier Diode [part_number=1N914 package="300 mil [THT]"]
  D6 = Rectifier Diode [part_number=1N914 package="300 mil [THT]"]
  D7 = Rectifier Diode [part_number=1N914 package="300 mil [THT]"]

nets:
  N1: D1.cathode, D5.anode
  N2: D1.anode, R1.Pin_0, D6.anode
  N3: R1.Pin_1, D5.cathode, D7.cathode
  N4: D6.cathode, D7.anode

notes:
  +2.5V
  CA-V
