# Fritzing sketch full_wave_diode_rectifier_bb (saved by Fritzing 0.9.3b)
breadboards: 1

parts:
  D1 = Rectifier Diode [part_number=1N4001 package="300 mil [THT]"]
  R1 = Resistor [tolerance=±5% resistance=100 package=THT]
  D2 = Rectifier Diode [part_number=1N4001 package="300 mil [THT]"]

nets:
  N1: D1.cathode, R1.Pin_0, D2.cathode

notes:
  +2.5V
  CB-V
  CA-V
