# Fritzing sketch imp_meas_bb (saved by Fritzing 0.9.3b)
breadboards: 1

parts:
  R1 = Resistor [tolerance=±5% resistance=1k package=THT]
  R2 = Resistor [tolerance=±5% resistance=470 package=THT]
  C1 = Capacitor Polarized [package=cpol-radial-100uf-25v]
  L1 = Inductors [package=cr54-kit]

nets:
  N1: R1.Pin_1, R2.Pin_0
  N2: R2.Pin_1, C1.-
  N3: C1.+, L1.2

notes:
  2.5V
  CA-V
  CB-V
  1kΩ
  470Ω
  20mH
  1uF
