# Fritzing sketch loudspeaker_imp_bb (saved by Fritzing 0.9.3b)
breadboards: 1

parts:
  SP1 = SPEAKER [package=pcb_mount_speaker]
  R1 = Resistor [tolerance=±5% resistance=100 package="0402 [SMD]"]
  R2 = Resistor [tolerance=±5% resistance=100 package="0402 [SMD]"]

nets:
  N1: SP1.-, R1.Pin_0, R2.Pin_0
  N2: R1.Pin_1, R2.Pin_1

notes:
  CB-V
  CA-V
  100Ω
