# Fritzing sketch rc_lpf_bb (saved by Fritzing 0.9.3b)
breadboards: 1

parts:
  R1 = Resistor [tolerance=±5% resistance=1k package="2010 [SMD]"]
  C1 = Electrolytic Capacitor [capacitance=1μF package="0405 [SMD, electrolytic]"]

nets:
  N1: R1.Pin_1, C1.-

notes:
  CA-V
  CB-V
  2.5V
  1kΩ
  1μF
  47mH
