# Fritzing sketch rl_hpf_bb (saved by Fritzing 0.9.3b)
breadboards: 1

parts:
  R1 = Resistor [tolerance=±5% resistance=1k package="2010 [SMD]"]
  L1 = Inductors [package=cr54-kit]

nets:
  N1: R1.Pin_1, L1.2

notes:
  CA-V
  CB-V
  2.5V
  1kΩ
  1μF
  47mH
  20mH
