# Fritzing sketch nmos_diode_conn_bb (saved by Fritzing 0.9.3b)
breadboards: 1

parts:
  IC1 = IC, DIP package, 14 pins [chip_label=CD4007]
  R1 = Resistor [tolerance=±5% resistance=100 package=THT]

nets:
  N1: IC1.pin6, IC1.pin8, R1.Pin_0

notes:
  +5V
  CA-V
  CB-H
  GND
