# Fritzing sketch two_switches_parallel_bb (saved by Fritzing 0.9.3b)
breadboards: 1

parts:
  Q1 = NPN-Transistor [part_number=NMOS package="TO92 [THT]"]
  LED1 = LED - 5mm [color="Red (633nm)" package="5 mm [THT]"]
  R1 = Resistor [tolerance=±5% resistance=100 package=THT]
  Q2 = NPN-Transistor [part_number=NMOS package="TO92 [THT]"]

nets:
  N1: Q1.E, Q2.E
  N2: Q1.C, LED1.cathode, Q2.C
  N3: LED1.anode, R1.Pin_0

notes:
  PIO1
  GND
  +5V
  CB-H
  PIO0
