# Fritzing sketch inv_amp_gain_1000-bb (saved by Fritzing 0.9.3b)
breadboards: 1

parts:
  U1 = OP37 - Low Noise, Precision, High Speed Op Amp [part_number=OP37]
  R1 = Resistor [tolerance=±5% resistance=100 package=THT]
  R2 = Resistor [tolerance=±5% resistance=100 package=THT]
  R3 = Resistor [tolerance=±5% resistance=47k package=THT]
  R4 = Resistor [tolerance=±5% resistance=100k package=THT]
  R5 = Resistor [tolerance=±5% resistance=220 package=THT]

nets:
  N1: U1.-IN, R1.Pin_1, R4.Pin_0
  N2: U1.+IN, R2.Pin_1
  N3: U1.OUT, R4.Pin_1, R5.Pin_1
  N4: R1.Pin_0, R2.Pin_0, R3.Pin_1

notes:
  +2.5V
  CH-B
  CH-A
  GND
  +5V
