# Fritzing sketch open_loop_gain_test_ckt2_bb (saved by Fritzing 0.9.3b)
breadboards: 1

parts:
  U1 = OP37 - Low Noise, Precision, High Speed Op Amp [part_number=OP97]
  R1 = Resistor [tolerance=±5% resistance=1M package=THT]
  R2 = Resistor [tolerance=±5% resistance=100 package=THT]
  R3 = Resistor [tolerance=±5% resistance=470k package=THT]
  R4 = Resistor [tolerance=±5% resistance=100 package=THT]
  U2 = POT [part_number=potentiometer package=3362u]
  R5 = Resistor [tolerance=±5% resistance=4.7k package=THT]
  R6 = Resistor [tolerance=±5% resistance=4.7k package=THT]

nets:
  N1: U1.-IN, R1.Pin_1, R2.Pin_0
  N2: U1.+IN, R3.Pin_1, R4.Pin_0
  N3: U1.-V, U2.A
  N4: U1.OUT, R6.Pin_1
  N5: U1.V+, U2.E
  N6: R1.Pin_0, R5.Pin_1, R6.Pin_0
  N7: R2.Pin_1, R4.Pin_1
  N8: R3.Pin_0, U2.S

notes:
  CA-V
  5V
  CB-H
  2.5V
  GND
