# Fritzing sketch diode_test_bb (saved by Fritzing 0.9.3b)
breadboards: 1

parts:
  D1 = Rectifier Diode [part_number=1N4001 package="300 mil [THT]"]
  R1 = Resistor [tolerance=±5% resistance=1k package="2010 [SMD]"]

nets:
  N1: D1.cathode, R1.Pin_0

notes:
  CA-V
  CB-V
  2.5V
  1N914
  1kΩ
