# Fritzing sketch lc_res_bb (saved by Fritzing 0.9.3b)
breadboards: 1

parts:
  D1 = Rectifier Diode [part_number=1N4001 package="300 mil [THT]"]
  C2 = Capacitor Polarized [package=cpol-radial-10uf-25v]
  L1 = Inductors [package=cr54-kit]

nets:
  N1: D1.cathode, C2.-, L1.1
  N2: C2.+, L1.2

notes:
  CA-V
  CB-H
  2.5V
  1N914
  10μF
  4.7mH
