# Fritzing sketch parallel_res_bb (saved by Fritzing 0.9.3b)
breadboards: 1

parts:
  C2 = Capacitor Polarized [package=cpol-radial-10uf-25v]
  L1 = Inductors [package=cr54-kit]
  R1 = Resistor [tolerance=±5% resistance=100 package="2512 [SMD]"]
  R2 = Resistor [tolerance=±5% resistance=1k package="2512 [SMD]"]

nets:
  N1: C2.+, L1.2, R2.Pin_1
  N2: C2.-, L1.1, R1.Pin_1, R2.Pin_0

notes:
  CA-V
  CB-V
  2.5V
  100Ω
  1μF
  20mH
  1kΩ
