# Fritzing sketch r_to_r_bb (saved by Fritzing 0.9.3b)
breadboards: 1

parts:
  R1 = Resistor [tolerance=±5% resistance=470 package="1206 [SMD]"]
  R2 = Resistor [tolerance=±5% resistance=470 package="1206 [SMD]"]

nets:
  N1: R1.Pin_0, R2.Pin_1

notes:
  CB-V
  CA-V
  GND
  470Ω
