# Fritzing sketch rc_cir_bb (saved by Fritzing 0.9.3b)
breadboards: 1

parts:
  R1 = Resistor [tolerance=±5% resistance=470 package="1206 [SMD]"]
  C1 = Electrolytic Capacitor [capacitance=1µF package="100 mil [THT, electrolytic]"]

nets:
  N1: R1.Pin_0, C1.-

notes:
  CB-V
  CA-V
  GND
  470Ω
  1µF
