# Fritzing sketch power_factor_rl_bb (saved by Fritzing 0.9.3b)
breadboards: 1

parts:
  R1 = Resistor [tolerance=±5% resistance=47 package="2010 [SMD]"]
  L1 = Inductors [package=cr54-kit]
  C1 = Electrolytic Capacitor [capacitance=1μF package="0405 [SMD, electrolytic]"]

nets:
  N1: R1.Pin_0, L1.1, C1.+
  N2: L1.2, C1.-

notes:
  CA-V
  CB-H
  2.5V
  47Ω
  10μF
  47mH
