# Fritzing sketch rc_load_bb (saved by Fritzing 0.9.3b)
breadboards: 1

parts:
  C2 = Capacitor Polarized [package=cpol-radial-10uf-25v]
  R1 = Resistor [tolerance=±5% resistance=100 package="2010 [SMD]"]

nets:
  N1: C2.+, R1.Pin_0

notes:
  CA-V
  CB-H
  2.5V
  100Ω
  10μF
