# Fritzing sketch rl_load_bb (saved by Fritzing 0.9.3b)
breadboards: 1

parts:
  R1 = Resistor [tolerance=±5% resistance=47 package="2010 [SMD]"]
  L1 = Inductors [package=cr54-kit]

nets:
  N1: R1.Pin_0, L1.1

notes:
  CA-V
  CB-H
  2.5V
  47Ω
  47mH
