# Fritzing sketch precision_full_wave_rect_bb (saved by Fritzing 0.9.3b)
breadboards: 1

parts:
  U1 = OP482 - Low Power, High Speed JFET Quad Operational Amplifier [part_number=OP484]
  R1 = Resistor [tolerance=±5% resistance=10k package=THT]
  D1 = Rectifier Diode [part_number=1N914 package="300 mil [THT]"]
  R2 = Resistor [tolerance=±5% resistance=10k package=THT]
  D2 = Rectifier Diode [part_number=1N914 package="300 mil [THT]"]
  R3 = Resistor [tolerance=±5% resistance=10k package=THT]
  R4 = Resistor [tolerance=±5% resistance=10k package=THT]
  R5 = Resistor [tolerance=±5% resistance=10k package=THT]

nets:
  N1: U1.OUTA, D1.cathode, D2.anode
  N2: U1.+INB, D2.cathode, R5.Pin_1
  N3: U1.-INB, R3.Pin_1, R4.Pin_0
  N4: U1.OUTB, R3.Pin_0
  N5: R1.Pin_1, R2.Pin_1, R5.Pin_0
  N6: D1.anode, R2.Pin_0, R4.Pin_1

notes:
  CA-V
  CB-H
  GND
  +5V
  +2.5V
