# Fritzing sketch rc_filt_bb (saved by Fritzing 0.9.3b)
breadboards: 1

parts:
  C1 = Electrolytic Capacitor [capacitance=10μF package="0605 [SMD, electrolytic]"]
  R1 = Resistor [tolerance=±5% resistance=2.2k package="0603 [SMD]"]

nets:
  N1: C1.+, R1.Pin_0

notes:
  2.5V
  CB-V
  CA-V
  2.2kΩ
  1μF
