# Fritzing sketch rl_filt_bb (saved by Fritzing 0.9.3b)
breadboards: 1

parts:
  R1 = Resistor [tolerance=±5% resistance=220 package="0603 [SMD]"]
  L1 = Inductors [package=cr54]

nets:
  N1: R1.Pin_1, L1.2

notes:
  2.5V
  CB-V
  CA-V
  220Ω
  20mH
