# Fritzing sketch adding_var_res_to_adjust_freq_bb (saved by Fritzing 0.9.3b)
breadboards: 1

parts:
  HPH1-1400L_Placeholder_1 = BMA180 [package=lga12]
  Q1 = NPN-Transistor [part_number=2N3904 package="TO92 [THT]"]
  R1 = TRIMPOT [part_number="Potentiometer - 5kΩ" package=trimpot_pth_s3_lock]
  R2 = Resistor [tolerance=±5% resistance=470 package=THT]
  LED1 = LED - 5mm [color="Red (633nm)" package="5 mm [THT]"]
  LED2 = LED - 5mm [color="Yellow (585nm)" package="5 mm [THT]"]

nets:
  N1: HPH1-1400L_Placeholder_1.NC, HPH1-1400L_Placeholder_1.NC3
  N2: HPH1-1400L_Placeholder_1.VDD, HPH1-1400L_Placeholder_1.INT
  N3: HPH1-1400L_Placeholder_1.VSS, HPH1-1400L_Placeholder_1.CSB
  N4: HPH1-1400L_Placeholder_1.NC1, R1.WIPER
  N5: HPH1-1400L_Placeholder_1.SCK, Q1.C, LED1.anode
  N6: HPH1-1400L_Placeholder_1.SDO, HPH1-1400L_Placeholder_1.VDDIO
  N7: HPH1-1400L_Placeholder_1.SDI, HPH1-1400L_Placeholder_1.NC2
  N8: Q1.E, LED2.cathode
  N9: Q1.B, R2.Pin_1
  N10: R1.CW, R2.Pin_0
  N11: LED1.cathode, LED2.anode

notes:
  CB-H
  +1.5V
  GND
