# Fritzing sketch configured_to_measure_Q1_base_current_bb (saved by Fritzing 0.9.3b)
breadboards: 1

parts:
  HPH1-1400L_Placeholder_1 = BMA180 [package=lga12]
  Q1 = NPN-Transistor [part_number=2N3904 package="TO92 [THT]"]
  C1 = Tantalum Capacitor [capacitance=1μF package="100 mil [THT, tantalum]"]
  D1 = Rectifier Diode [part_number=1N914 package="300 mil [THT]"]
  R1 = TRIMPOT [part_number="Potentiometer - 5kΩ" package=trimpot_pth_s3_lock]
  R2 = Resistor [tolerance=±5% resistance=1k package=THT]
  LED1 = LED - 5mm [color="Red (633nm)" package="5 mm [THT]"]
  LED2 = LED - 5mm [color="Blue (470nm)" package="5 mm [THT]"]

nets:
  N1: HPH1-1400L_Placeholder_1.NC, HPH1-1400L_Placeholder_1.NC3
  N2: HPH1-1400L_Placeholder_1.VDD, HPH1-1400L_Placeholder_1.INT
  N3: HPH1-1400L_Placeholder_1.VSS, HPH1-1400L_Placeholder_1.CSB
  N4: HPH1-1400L_Placeholder_1.NC1, C1.-
  N5: HPH1-1400L_Placeholder_1.SCK, Q1.C, LED1.anode
  N6: HPH1-1400L_Placeholder_1.SDO, HPH1-1400L_Placeholder_1.VDDIO
  N7: HPH1-1400L_Placeholder_1.SDI, HPH1-1400L_Placeholder_1.NC2
  N8: Q1.E, R1.CCW, LED2.cathode
  N9: Q1.B, R2.Pin_0
  N10: C1.+, D1.cathode
  N11: D1.anode, R1.WIPER
  N12: LED1.cathode, LED2.anode

notes:
  CB-H
  +1.5V
  GND
  +5V
  CA-V
