# Fritzing sketch dc-dc_boost_converter_bb (saved by Fritzing 0.9.3b)
breadboards: 1

parts:
  HPH1-1400L_Placeholder_1 = BMA180 [package=lga12]
  Q1 = NPN-Transistor [package="TO92 [THT]"]
  R1 = Resistor [tolerance=±5% resistance=1k package=THT]
  LED1 = LED - 5mm [color="Red (633nm)" package="5 mm [THT]"]
  LED2 = LED - 5mm [color="Yellow (585nm)" package="5 mm [THT]"]

nets:
  N1: HPH1-1400L_Placeholder_1.NC, HPH1-1400L_Placeholder_1.NC3
  N2: HPH1-1400L_Placeholder_1.VDD, HPH1-1400L_Placeholder_1.INT
  N3: HPH1-1400L_Placeholder_1.VSS, HPH1-1400L_Placeholder_1.CSB
  N4: HPH1-1400L_Placeholder_1.NC1, R1.Pin_0
  N5: HPH1-1400L_Placeholder_1.SCK, Q1.C, LED1.cathode
  N6: HPH1-1400L_Placeholder_1.SDO, HPH1-1400L_Placeholder_1.VDDIO
  N7: HPH1-1400L_Placeholder_1.SDI, HPH1-1400L_Placeholder_1.NC2
  N8: Q1.E, LED2.anode
  N9: Q1.B, R1.Pin_1
  N10: LED1.anode, LED2.cathode

notes:
  CB-H
  +1.5V
  GND
