# Fritzing sketch improved_follower_1v5_bb (saved by Fritzing 0.9.3b)
breadboards: 1

parts:
  Q1 = NPN-Transistor [part_number=2N3904 package="TO92 [THT]"]
  Q2 = PNP-Transistor [part_number=2N3906 package="TO92 [THT]"]
  R1 = Resistor [tolerance=±5% resistance=470 package=THT]
  R2 = TRIMPOT [part_number="Potentiometer - 1kΩ" package=trimpot_pth_s3_lock]
  R3 = Resistor [tolerance=±5% resistance=1k package=THT]
  R4 = Resistor [tolerance=±5% resistance=47 package=THT]
  C1 = Tantalum Capacitor [capacitance=47µF package="100 mil [THT, tantalum]"]
  C2 = Tantalum Capacitor [capacitance=0.1µF package="100 mil [THT, tantalum]"]

nets:
  N1: Q1.E, Q2.E, R4.Pin_0, C1.+, C2.+
  N2: Q1.B, R2.WIPER
  N3: Q1.C, Q2.B, R1.Pin_0
  N4: Q2.C, R1.Pin_1, R2.CCW
  N5: R2.CW, R3.Pin_0
  N6: R3.Pin_1, R4.Pin_1, C1.-, C2.-

notes:
  +2.5V
  GND
  +1.5V
