# Fritzing sketch precision_follower_bb (saved by Fritzing 0.9.3b)
breadboards: 1

parts:
  U1 = ADTL082 - Dual JFET Input Op Amps [part_number=ADTL082]
  U1_1 = AnalogDevices_ADTL082ARZ_subpart1 [part_number=ADTL082]  # not connected
  U1_2 = AnalogDevices_ADTL082ARZ_subpart2 [part_number=ADTL082]  # not connected
  Q1 = NPN-Transistor [part_number=2N3904 package="TO92 [THT]"]
  R1 = Resistor [tolerance=±5% resistance=47 package=THT]
  U2 = POT [part_number="Potentiometer - 10kΩ" package=3362u]

nets:
  N1: U1.connector2, Q1.E, R1.Pin_0
  N2: U1.connector3, U2.S
  N3: U1.connector4, R1.Pin_1, U2.A
  N4: U1.connector7, Q1.B
  N5: U1.connector8, Q1.C

notes:
  +2.5V
  GND
  +1.5V
  +5V
