# Fritzing sketch simple_dc_dc_booster_circuit_bb (saved by Fritzing 0.9.3b)
breadboards: 1

parts:
  L1 = Inductors [package=cr54]
  Q1 = NPN-Transistor [part_number=2N3904 package="TO92 [THT]"]
  D2 = Rectifier Diode [part_number=1N914 package="300 mil [THT]"]
  D3 = Rectifier Diode [part_number=1N914 package="300 mil [THT]"]
  C2 = Tantalum Capacitor [capacitance=47µF package="100 mil [THT, tantalum]"]
  LED2 = LED - 5mm [color="Red (633nm)" package="5 mm [THT]"]
  LED3 = LED - 5mm [color="Yellow (585nm)" package="5 mm [THT]"]
  R1 = Resistor [tolerance=±5% resistance=100 package=THT]

nets:
  N1: L1.1, Q1.E, D2.cathode, D3.anode
  N2: Q1.C, D2.anode
  N3: D3.cathode, C2.+, LED2.anode
  N4: C2.-, R1.Pin_1
  N5: LED2.cathode, LED3.anode
  N6: LED3.cathode, R1.Pin_0

notes:
  +1.5V
  Vout
  GND
