# Fritzing sketch using_npn_stage_and_cap_feedback_bb (saved by Fritzing 0.9.3b)
breadboards: 1

parts:
  HPH1-1400L_Placeholder_2 = BMA180 [package=lga12]
  Q2 = NPN-Transistor [part_number=2N3904 package="TO92 [THT]"]
  LED1 = LED - 5mm [color="Red (633nm)" package="5 mm [THT]"]
  R1 = Resistor [tolerance=±5% resistance=470 package=THT]
  LED2 = LED - 5mm [color="Yellow (585nm)" package="5 mm [THT]"]
  C1 = Ceramic Capacitor [capacitance=10nF package="100 mil [THT, multilayer]"]
  U1 = POT [part_number="Potentiometer - 5kΩ" package=3362u]
  Q4 = NPN-Transistor [part_number=2N3904 package="TO92 [THT]"]
  R2 = Resistor [tolerance=±5% resistance=10k package=THT]

nets:
  N1: HPH1-1400L_Placeholder_2.SCK, Q2.C, LED1.anode, C1.0
  N2: HPH1-1400L_Placeholder_2.SDO, HPH1-1400L_Placeholder_2.VDDIO
  N3: HPH1-1400L_Placeholder_2.SDI, HPH1-1400L_Placeholder_2.NC2
  N4: HPH1-1400L_Placeholder_2.NC3, R2.Pin_1
  N5: Q2.E, LED2.cathode, Q4.E
  N6: Q2.B, Q4.C
  N7: LED1.cathode, LED2.anode
  N8: R1.Pin_0, C1.1
  N9: R1.Pin_1, U1.S
  N10: U1.E, Q4.B, R2.Pin_0

notes:
  CA-H
  +1.5V
  GND
