# Fritzing sketch using_pnp_stage_and_cap_feedback_bb (saved by Fritzing 0.9.3b)
breadboards: 1

parts:
  HPH1-1400L_Placeholder_2 = BMA180 [package=lga12]

nets:
  N1: HPH1-1400L_Placeholder_2.SDO, HPH1-1400L_Placeholder_2.VDDIO
  N2: HPH1-1400L_Placeholder_2.SDI, HPH1-1400L_Placeholder_2.NC2
