# Fritzing sketch inv_sum_amp_with_ch-a_v1_v2-bb (saved by Fritzing 0.9.3b)
breadboards: 1

parts:
  IC1 = IC, DIP package, 14 pins [chip_label=OP484 part_number=OP484]
  R1 = Resistor [tolerance=±5% resistance=100k package=THT]
  R2 = Resistor [tolerance=±5% resistance=470 package=THT]
  R3 = Resistor [tolerance=±5% resistance=100k package=THT]
  R5 = Resistor [tolerance=±5% resistance=100k package=THT]
  C1 = Tantalum Capacitor [capacitance=1μF package="100 mil [THT, tantalum]"]
  R6 = Resistor [tolerance=±5% resistance=220 package=THT]

nets:
  N1: IC1.pin5, C1.-
  N2: IC1.pin6, R1.Pin_0, R3.Pin_0, R5.Pin_1
  N3: IC1.pin7, R5.Pin_0, R6.Pin_1
  N4: R1.Pin_1, R2.Pin_1
  N5: R2.Pin_0, R3.Pin_1, C1.+

notes:
  +2.5V
  CH-B
  CH-A
  GND
  +5V
