# Fritzing sketch sum_of_sine_and_square_waves-bb (saved by Fritzing 0.9.3b)
breadboards: 1

parts:
  IC1 = IC, DIP package, 14 pins [chip_label=OP484 part_number=OP484]
  R1 = Resistor [tolerance=±5% resistance=6.8k package=THT]
  R2 = Resistor [tolerance=±5% resistance=470 package=THT]
  R3 = Resistor [tolerance=±5% resistance=470 package=THT]
  R4 = Resistor [tolerance=±5% resistance=100k package=THT]
  R5 = Resistor [tolerance=±5% resistance=100k package=THT]
  R6 = Resistor [tolerance=±5% resistance=220 package=THT]
  R7 = Resistor [tolerance=±5% resistance=100k package=THT]

nets:
  N1: IC1.pin1, R2.Pin_1
  N2: IC1.pin2, R1.Pin_1
  N3: IC1.pin3, IC1.pin5, R3.Pin_1
  N4: IC1.pin6, R4.Pin_1, R5.Pin_0, R7.Pin_0
  N5: IC1.pin7, R4.Pin_0, R6.Pin_0
  N6: R1.Pin_0, R5.Pin_1
  N7: R2.Pin_0, R3.Pin_0, R7.Pin_1

notes:
  +2.5V
  CH-B
  CH-A
  GND
  +5V
