# Fritzing sketch function_gen_variable_freq_and_waveform_sym_bb (saved by Fritzing 0.9.3b)
breadboards: 1

parts:
  U1 = AD8561 - Ultrafast 7ns Single Supply Comparator [part_number=AD8561]
  U2 = AD8561 - Ultrafast 7ns Single Supply Comparator [part_number=AD8561]
  U3 = AD8561 - Ultrafast 7ns Single Supply Comparator [part_number=AD8561]
  C1 = Ceramic Capacitor [capacitance=100nF package="100 mil [THT, multilayer]"]
  D1 = Rectifier Diode [part_number=1N914 package="300 mil [THT]"]
  D2 = Rectifier Diode [part_number=1N914 package="300 mil [THT]"]
  U4 = POT [part_number="Potentiometer - 1kΩ" package=3362u]
  R1 = Resistor [tolerance=±5% resistance=10k package=THT]
  U5 = POT [part_number="Potentiometer - 1kΩ" package=3362u]
  R2 = Resistor [tolerance=±5% resistance=20k package=THT]
  R3 = Resistor [tolerance=±5% resistance=10k package=THT]
  R4 = Resistor [tolerance=±5% resistance=4.7k package=THT]

nets:
  N1: U1.V+, U2.V+, U3.V+
  N2: U1.-IN, C1.0, D1.anode, D2.cathode
  GND: U1.V-, U1.LATCH, U1.GND, U2.V-, U2.LATCH, U2.GND, U3.V-, U3.LATCH, U3.GND
  N3: U1.OUT, C1.1, R2.Pin_0
  N4: U2.+IN, U5.S
  N5: U2.-IN, U2.OUT, R1.Pin_0
  N6: U3.+IN, R2.Pin_1, R3.Pin_0
  N7: U3.-IN, U5.A
  N8: U3.OUT, U5.E, R3.Pin_1, R4.Pin_0
  N9: D1.cathode, U4.E
  N10: D2.anode, U4.A
  N11: U4.S, R1.Pin_1

notes:
  GND
  +2.5V
  CB-H
  CA-H
  +5V
  R1
  R2
  C1
