# Fritzing sketch schmitt_trigger_bb (saved by Fritzing 0.9.3b)
breadboards: 1

parts:
  U1 = AD8561 - Ultrafast 7ns Single Supply Comparator [part_number=AD8561]
  R1 = Resistor [tolerance=±5% resistance=4.7k package=THT]
  R2 = Resistor [tolerance=±5% resistance=4.7k package=THT]
  R2_2 = Resistor [tolerance=±5% resistance=20k package=THT]
  R1_2 = Resistor [tolerance=±5% resistance=10k package=THT]

nets:
  N1: U1.V+, R1.Pin_0, R2.Pin_0
  N2: U1.-IN, R2_2.Pin_1, R1_2.Pin_0
  N3: U1.V-, U1.LATCH, U1.GND
  N4: U1.OUT, R1.Pin_1, R1_2.Pin_1
  N5: U1.OUTB, R2.Pin_1

notes:
  +2.5V
  CB-H
  CA-V
  GND
  +5V
