# Fritzing sketch simple_function_gen_bb (saved by Fritzing 0.9.3b)
breadboards: 1

parts:
  U1 = AD8561 - Ultrafast 7ns Single Supply Comparator [part_number=AD8561]
  U2 = AD8561 - Ultrafast 7ns Single Supply Comparator [part_number=AD8561]
  C1 = Ceramic Capacitor [capacitance=100nF package="100 mil [THT, multilayer]"]
  R5 = Resistor [tolerance=±5% resistance=4.7k package=THT]
  R1 = Resistor [tolerance=±5% resistance=10k package=THT]
  R1_2 = Resistor [tolerance=±5% resistance=10k package=THT]
  R2 = Resistor [tolerance=±5% resistance=20k package=THT]

nets:
  N1: U1.V+, U2.V+, R5.Pin_1
  N2: U1.-IN, C1.0, R1.Pin_0
  GND: U1.V-, U1.LATCH, U1.GND, U2.V-, U2.LATCH, U2.GND
  N3: U1.OUT, C1.1, R2.Pin_0
  N4: U2.+IN, R1_2.Pin_0, R2.Pin_1
  N5: U2.OUT, R5.Pin_0, R1.Pin_1, R1_2.Pin_1

notes:
  +2.5V
  CB-H
  CA-H
  +5V
  GND
