# Fritzing sketch ad592_bb (saved by Fritzing 0.9.3b)
breadboards: 1

parts:
  U1 = AD22100 - Voltage Output Temperature Sensor with Signal Conditioning [part_number=AD529]
  R1 = Resistor [tolerance=±5% resistance=1k package="0805 [SMD]"]

nets:
  N1: U1.GND, R1.Pin_0

notes:
  GND
  V+
  1+
  1-
  1kΩ
  -
  592
