# Fritzing sketch abpf_gain_bb (saved by Fritzing 0.9.3b)
breadboards: 1

parts:
  U1 = OP27 - Low Noise, Precision Op Amp [part_number=OP27]
  R1 = Resistor [tolerance=±5% resistance=1k package=THT]
  R2 = Resistor [tolerance=±5% resistance=6.8k package=THT]
  R3 = Resistor [tolerance=±5% resistance=2.2k package=THT]
  R4 = Resistor [tolerance=±5% resistance=10k package=THT]
  C1 = Tantalum Capacitor [capacitance=10nF package="100 mil [THT, tantalum]"]
  R5 = Resistor [tolerance=±5% resistance=10k package=THT]
  R6 = Resistor [tolerance=±5% resistance=1k package=THT]
  C2 = Tantalum Capacitor [capacitance=1nF package="100 mil [THT, tantalum]"]

nets:
  N1: U1.-IN, R1.Pin_0, R2.Pin_1
  N2: U1.+IN, C1.-, R5.Pin_0
  N3: U1.OUT, R3.Pin_1, R4.Pin_0, R6.Pin_0
  N4: R1.Pin_1, R4.Pin_1, R5.Pin_1, C2.-
  N5: R2.Pin_0, R3.Pin_0
  N6: R6.Pin_1, C2.+

notes:
  W1
  1+
  Vp
  2+
  Vn
  1-
  2-
  GND
