# Fritzing sketch absf_gain2 (saved by Fritzing 0.9.3b)
breadboards: 1

parts:
  U1 = OP37 - Low Noise, Precision, High Speed Op Amp [part_number=OP37]
  R1 = Resistor [tolerance=±5% resistance=1k package=THT]
  C1 = Tantalum Capacitor [capacitance=1nF package="100 mil [THT, tantalum]"]
  R2 = Resistor [tolerance=±5% resistance=1k package=THT]
  U2 = OP37 - Low Noise, Precision, High Speed Op Amp [part_number=OP37]
  C2 = Tantalum Capacitor [capacitance=1μF package="100 mil [THT, tantalum]"]
  R4 = Resistor [tolerance=±5% resistance=1k package=THT]
  U3 = OP37 - Low Noise, Precision, High Speed Op Amp [part_number=OP37]
  R5 = Resistor [tolerance=±5% resistance=10k package=THT]
  R6 = Resistor [tolerance=±5% resistance=1k package=THT]

nets:
  N1: U1.-IN, U1.OUT, R2.Pin_0
  N2: U1.+IN, R1.Pin_0, C1.-
  N3: U1.-V, U2.-V, U3.-V
  N4: U1.V+, U2.V+, U3.V+
  N5: R1.Pin_1, C2.-, U3.+IN
  N6: C1.+, R6.Pin_1
  N7: R2.Pin_1, R4.Pin_1, U3.-IN, R5.Pin_0
  N8: U2.-IN, U2.OUT, R4.Pin_0
  N9: U2.+IN, C2.+, R6.Pin_0
  N10: U3.OUT, R5.Pin_1

notes:
  1-
  Vp
  Vn
  1+
  2-
  2+
  W1
  GND
