# Fritzing sketch inv_alpf_gain-bb (saved by Fritzing 0.9.3b)
breadboards: 1

parts:
  U1 = OP27 - Low Noise, Precision Op Amp [part_number=OP27]
  R1 = Resistor [tolerance=±5% resistance=1k package=THT]
  R2 = Resistor [tolerance=±5% resistance=10k package=THT]
  C1 = Ceramic Capacitor [capacitance=1nF package="100 mil [THT, multilayer]"]
  R3 = Resistor [tolerance=±5% resistance=10k package=THT]

nets:
  N1: U1.-IN, R1.Pin_1, R2.Pin_0, C1.0
  N2: U1.+IN, R3.Pin_1
  N3: U1.OUT, R2.Pin_1, C1.1, R3.Pin_0

notes:
  1-
  1+
  2-
  2+
  W1
  GND
  Vp
  Vn
