# Fritzing sketch sk_bpf_bb (saved by Fritzing 0.9.3b)
breadboards: 1

parts:
  U1 = OP37 - Low Noise, Precision, High Speed Op Amp [part_number=OP37]
  R1 = Resistor [tolerance=±5% resistance=1k package=THT]
  R2 = Resistor [tolerance=±5% resistance=1k package=THT]
  R3 = Resistor [tolerance=±5% resistance=2k package=THT]
  C1 = Tantalum Capacitor [capacitance=10nF package="100 mil [THT, tantalum]"]
  R4 = Resistor [tolerance=±5% resistance=1k package=THT]
  C2 = Tantalum Capacitor [capacitance=10nF package="100 mil [THT, tantalum]"]
  R5 = Resistor [tolerance=±5% resistance=1k package=THT]

nets:
  N1: U1.-IN, R1.Pin_1, R2.Pin_0
  N2: U1.OUT, R1.Pin_0, R5.Pin_1
  N3: R2.Pin_1, R3.Pin_0, C1.-
  N4: R3.Pin_1, C2.+
  N5: C1.+, R4.Pin_1, C2.-, R5.Pin_0

notes:
  1+
  W1
  Vp
  2+
  Vn
  GND
  1-
  2-
