# Fritzing sketch svf_khn (saved by Fritzing 0.9.3b)
breadboards: 1

parts:
  U1 = OP37 - Low Noise, Precision, High Speed Op Amp [part_number=OP37]
  U2 = OP37 - Low Noise, Precision, High Speed Op Amp [part_number=OP37]
  U3 = OP37 - Low Noise, Precision, High Speed Op Amp [part_number=OP37]
  R1 = Resistor [tolerance=±5% resistance=1k package=THT]
  R2 = Resistor [tolerance=±5% resistance=10k package=THT]
  R3 = Resistor [tolerance=±5% resistance=10k package=THT]
  C1 = Tantalum Capacitor [capacitance=1μF package="100 mil [THT, tantalum]"]
  R4 = Resistor [tolerance=±5% resistance=1k package=THT]
  R5 = Resistor [tolerance=±5% resistance=10k package=THT]
  R6 = Resistor [tolerance=±5% resistance=1k package=THT]
  R7 = Resistor [tolerance=±5% resistance=1k package=THT]
  C2 = Tantalum Capacitor [capacitance=10nF package="100 mil [THT, tantalum]"]

nets:
  N1: U1.-IN, R1.Pin_1, R2.Pin_0, R5.Pin_0, R6.Pin_0
  N2: U1.+IN, R3.Pin_0
  N3: U1.-V, U2.-V, U3.-V
  N4: U1.OUT, R2.Pin_1, R4.Pin_0
  N5: U1.V+, U2.V+, U3.V+
  N6: U2.-IN, C1.-, R4.Pin_1
  N7: U2.+IN, U3.+IN, R6.Pin_1
  N8: U2.OUT, R3.Pin_1, C1.+, R7.Pin_0
  N9: U3.-IN, R7.Pin_1, C2.-
  N10: U3.OUT, R5.Pin_1, C2.+

notes:
  1+
  W1
  Vp
  2+ HP
  BP
  LP
  Vn
  GND
  1-
  2-
