# Fritzing sketch tt_biquad_bb (saved by Fritzing 0.9.3b)
breadboards: 1

parts:
  U1 = OP37 - Low Noise, Precision, High Speed Op Amp [part_number=OP37]
  R1 = Resistor [tolerance=±5% resistance=1k package=THT]
  R2 = Resistor [tolerance=±5% resistance=1k package=THT]
  C1 = Ceramic Capacitor [capacitance=1nF package="100 mil [THT, multilayer]"]
  U2 = OP37 - Low Noise, Precision, High Speed Op Amp [part_number=OP37]
  R3 = Resistor [tolerance=±5% resistance=1k package=THT]
  C2 = Ceramic Capacitor [capacitance=10nF package="100 mil [THT, multilayer]"]
  U3 = OP37 - Low Noise, Precision, High Speed Op Amp [part_number=OP37]
  R4 = Resistor [tolerance=±5% resistance=10k package=THT]
  R5 = Resistor [tolerance=±5% resistance=1k package=THT]
  R6 = Resistor [tolerance=±5% resistance=10k package=THT]

nets:
  N1: U1.-IN, R1.Pin_1, R2.Pin_0, C1.0, R6.Pin_0
  N2: U1.+IN, U2.+IN, U3.+IN
  N3: U1.-V, U2.-V, U3.-V
  N4: U1.OUT, R2.Pin_1, C1.1, R3.Pin_0
  N5: U1.V+, U2.V+, U3.V+
  N6: U2.-IN, R3.Pin_1, C2.0
  N7: U2.OUT, C2.1, R4.Pin_0
  N8: U3.-IN, R4.Pin_1, R5.Pin_0
  N9: U3.OUT, R5.Pin_1, R6.Pin_1

notes:
  1-
  Vp
  Vn
  1+
  2-
  2+
  W1
  GND
