# Fritzing sketch twint_notch_bb (saved by Fritzing 0.9.3b)
breadboards: 1

parts:
  U1 = OP37 - Low Noise, Precision, High Speed Op Amp [part_number=OP37]
  R1 = Resistor [tolerance=±5% resistance=1k package=THT]
  R2 = Resistor [tolerance=±5% resistance=1k package=THT]
  R3 = Resistor [tolerance=±5% resistance=1k package=THT]
  R4 = Resistor [tolerance=±5% resistance=1k package=THT]
  C1 = Capacitor [part_number="1nF (102)" package=cap-pth-small2]
  C2 = Capacitor [part_number="1nF (102)" package=cap-pth-small2]
  C3 = Capacitor [part_number="1nF (102)" package=cap-pth-small2]
  C4 = Capacitor [part_number="1nF (102)" package=cap-pth-small2]
  R5 = Resistor [tolerance=±5% resistance=1k package=THT]
  R6 = Resistor [tolerance=±5% resistance=1k package=THT]
  U2 = OP37 - Low Noise, Precision, High Speed Op Amp [part_number=OP37]
  R7 = Resistor [tolerance=±5% resistance=20k package=THT]

nets:
  N1: U1.-IN, U1.OUT, R6.Pin_0
  N2: U1.+IN, R1.Pin_1, C3.1
  N3: U1.-V, U2.-V
  N4: U1.V+, U2.V+
  N5: R1.Pin_0, R2.Pin_1
  N6: R2.Pin_0, R3.Pin_1, C1.1, C2.1
  N7: R3.Pin_0, R4.Pin_1
  N8: R4.Pin_0, C4.2
  N9: C1.2, C2.2, R5.Pin_1, U2.-IN, U2.OUT
  N10: C3.2, C4.1, R5.Pin_0
  N11: R6.Pin_1, U2.+IN, R7.Pin_1

notes:
  1-
  Vp
  Vn
  1+
  2-
  2+
  W1
  GND
