# Fritzing sketch singlebal_bb (saved by Fritzing 0.9.3b)
breadboards: 1

parts:
  Q1 = NPN-Transistor [package="TO92 [THT]"]
  Q2 = NPN-Transistor [package="TO92 [THT]"]
  Q3 = NPN-Transistor [package="TO92 [THT]"]
  R1 = Resistor [tolerance=±5% resistance=6.8k package=THT]
  R2 = Resistor [tolerance=±5% resistance=6.8k package=THT]
  U1 = OP37 - Low Noise, Precision, High Speed Op Amp [part_number=OP37]
  R3 = Resistor [tolerance=±5% resistance=1k package=THT]
  R4 = Resistor [tolerance=±5% resistance=1k package=THT]

nets:
  N1: Q1.E, R1.Pin_1
  N2: Q1.B, R3.Pin_1
  N3: Q1.C, Q2.C, Q3.E
  N4: Q2.E, R2.Pin_1
  N5: Q2.B, U1.OUT, R4.Pin_0
  N6: Q3.C, U1.+IN
  N7: R1.Pin_0, R2.Pin_0, U1.V+
  N8: U1.-IN, R3.Pin_0, R4.Pin_1

notes:
  Vp
  1+
  W1
  W2
  2+
  GND
  1-
  2-
  M1
  M2
  M3
  R1
  R2
  Vn
