# Fritzing sketch active_half_wave_rect_self_powered_op_amp-bb (saved by Fritzing 0.9.3b)
breadboards: 1

parts:
  R1 = Resistor [tolerance=±5% resistance=10 package=THT]
  R2 = Resistor [tolerance=±5% resistance=47k package=THT]
  R3 = Resistor [tolerance=±5% resistance=1M package=THT]
  Q1 = PNP-Transistor [part_number=ZVP2110A package="TO92 [THT]"]
  U1 = AD8541 - CMOS Rail-to-Rail Op Amp [part_number=AD8541]
  C1 = Electrolytic Capacitor [capacitance=220µF package="100 mil [THT, electrolytic]"]
  R4 = Resistor [tolerance=±5% resistance=2.2k package=THT]

nets:
  N1: R1.Pin_1, R2.Pin_0, Q1.C
  N2: R2.Pin_1, R3.Pin_0, U1.-INA
  N3: R3.Pin_1, Q1.B, U1.OUTA
  N4: Q1.E, U1.+INA, U1.V+, C1.+, R4.Pin_0
  N5: U1.-V, C1.-, R4.Pin_1

notes:
  1-
  1+
  2-
  2+
  W1
  GND
