# Fritzing sketch ad7920_bb (saved by Fritzing 0.9.3b)
breadboards: 1

parts:
  C1 = Electrolytic Capacitor [capacitance=10μF package="0605 [SMD, electrolytic]"]
  IC5 = SO08-EIAJ [chip_label=AD7920 package=SO]

nets:
  N1: C1.-, IC5.7
  N2: C1.+, IC5.1

notes:
  Vp
  DIO2
  DIO1
  DIO0
  GND
  W1
