# Fritzing sketch dual_slope-bb (saved by Fritzing 0.9.3b)
breadboards: 1

parts:
  IC1 = IC, DIP package, 18 pins [chip_label=LTC1043]
  R1 = Resistor [tolerance=±5% resistance=10k package="0603 [SMD]"]
  Q1 = TRANSISTOR_PNP [package=to-92]
  R2 = Resistor [tolerance=±5% resistance=10k package="0603 [SMD]"]
  Q2 = TRANSISTOR_PNP [package=to-92]
  R3 = Resistor [tolerance=±5% resistance=10k package="0603 [SMD]"]
  R4 = Resistor [tolerance=±5% resistance=1M package="0603 [SMD]"]
  U1 = OP37 - Low Noise, Precision, High Speed Op Amp [part_number=OP37]
  C1 = Electrolytic Capacitor [capacitance=1µF package="100 mil [THT, electrolytic]"]
  U2 = TRANSISTOR_NPN_2 [package=to-92]
  R5 = Resistor [tolerance=±5% resistance=100k package="0603 [SMD]"]

nets:
  N1: IC1.pin7, IC1.pin13, IC1.pin17, R1.Pin_0, Q1.C
  N2: IC1.pin8, IC1.pin14
  N3: IC1.pin10, IC1.pin11, R4.Pin_0
  N4: IC1.pin16, R1.Pin_1
  N5: Q1.E, Q2.E, R3.Pin_0
  N6: Q1.B, R2.Pin_1
  N7: Q2.B, R3.Pin_1
  N8: Q2.C, U2.B, R5.Pin_0
  N9: R4.Pin_1, U1.-IN, C1.-, U2.E
  N10: U1.OUT, C1.+, U2.C, R5.Pin_1

notes:
  2N3906
  OP97
  1µF
  ZVN3310
  100kΩ
  1MΩ
  10kΩ
  D0
  D1
  W1
  GND
  Vp
  1+
  Vn
  1-
