# Fritzing sketch sar_adc-bb (saved by Fritzing 0.9.3b)
breadboards: 1

parts:
  IC1 = IC, DIP package, 14 pins [chip_label=OP484]
  R1 = Resistor [tolerance=±5% resistance=22k package="0402 [SMD]"]
  R2 = Resistor [tolerance=±5% resistance=22k package="0402 [SMD]"]
  R3 = Resistor [tolerance=±5% resistance=22k package="0402 [SMD]"]
  R4 = Resistor [tolerance=±5% resistance=10k package="0402 [SMD]"]
  R5 = Resistor [tolerance=±5% resistance=10k package="0402 [SMD]"]
  R6 = Resistor [tolerance=±5% resistance=10k package="0402 [SMD]"]
  R7 = Resistor [tolerance=±5% resistance=22k package="0402 [SMD]"]
  R8 = Resistor [tolerance=±5% resistance=22k package="0402 [SMD]"]
  R9 = Resistor [tolerance=±5% resistance=10k package="0402 [SMD]"]

nets:
  N1: IC1.pin1, IC1.pin6, R9.Pin_0
  N2: IC1.pin2, R9.Pin_1
  N3: IC1.pin3, R6.Pin_1, R8.Pin_1
  N4: R1.Pin_1, R2.Pin_1, R4.Pin_0
  N5: R3.Pin_1, R4.Pin_1, R5.Pin_0
  N6: R5.Pin_1, R6.Pin_0, R7.Pin_1

notes:
  1+
  W1
  Vp
  2+
  D0
  D1
  D2
  D3
  GND
  2-
  10kΩ
  20kΩ
