# Fritzing sketch vf_adc-bb (saved by Fritzing 0.9.3b)
breadboards: 1

parts:
  U1 = AD654 - Low Cost Monolithic Voltage-to-Frequency Converter [part_number=AD654]
  R1 = Resistor [tolerance=±5% resistance=1k package="0603 [SMD]"]
  C1 = Ceramic Capacitor [capacitance="100 nF" package="0805 [SMD, multilayer]"]
  R2 = Resistor [tolerance=±5% resistance=1k package="0603 [SMD]"]
  R3 = Resistor [tolerance=±5% resistance=1k package="0603 [SMD]"]

nets:
  N1: U1.10V, R1.Pin_1
  N2: U1.5V, U1.STROBE, R3.Pin_1
  N3: U1.2p5V, R3.Pin_0
  N4: U1.COMMON, R2.Pin_0
  N5: U1.VBG, C1.1
  N6: U1.CAP, C1.0
  N7: U1.V+, R1.Pin_0

notes:
  GND
  W1
  1-
  Vp
  1+
  1kΩ
  1nF
  AD654
