# Fritzing sketch analog_trigger-bb (saved by Fritzing 0.9.3b)
breadboards: 1

parts:
  U1 = AD8561 - Ultrafast 7ns Single Supply Comparator [part_number=AD8561]
  R1 = Resistor [tolerance=±5% resistance=1M package=THT]
  R2 = Resistor [tolerance=±5% resistance=1k package=THT]
  R3 = Trimmer Potentiometer [maximum_resistance=10kΩ package=THT]
  R4 = Resistor [tolerance=±5% resistance=1k package=THT]
  0_1uF = Capacitor [package=cap-pth-small2]
  IC1 = IC, DIP package, 14 pins [chip_label=HEF4007]
  C2 = Ceramic Capacitor [capacitance=4.7nF package="100 mil [THT, multilayer]"]
  R5 = Resistor [tolerance=±5% resistance=1k package=THT]

nets:
  N1: U1.V+, R2.Pin_0, IC1.pin2, IC1.pin14
  N2: U1.+IN, R1.Pin_0
  N3: U1.-IN, R3.wiper, 0_1uF.2
  N4: U1.V-, R4.Pin_1
  N5: U1.LATCH, U1.GND, 0_1uF.1
  N6: U1.OUT, IC1.pin3
  N7: R1.Pin_1, IC1.pin4, IC1.pin7, C2.1
  N8: R2.Pin_1, R3.leg1
  N9: R3.leg2, R4.Pin_0
  N10: IC1.pin1, IC1.pin5, R5.Pin_0
  N11: IC1.pin6, C2.0, R5.Pin_1
  N12: IC1.pin8, IC1.pin13

notes:
  1-
  1+
  2-
  2+
  W1
  V-
  T1
  Vp
