# Fritzing sketch current_mirror_test-bb (saved by Fritzing 0.9.3b)
breadboards: 1

parts:
  C1 = Electrolytic Capacitor [capacitance=4.7µF package="1010 [SMD, electrolytic]"]
  C2 = Electrolytic Capacitor [capacitance=4.7µF package="1010 [SMD, electrolytic]"]
  U1 = ADTL082 - Dual JFET Input Op Amps [part_number=ADTL082]
  U1_1 = AnalogDevices_ADTL082ARZ_subpart1 [part_number=ADTL082]  # not connected
  R1 = Resistor [tolerance=±5% resistance=1k package="0603 [SMD]"]
  R2 = Resistor [tolerance=±5% resistance=1k package="0603 [SMD]"]
  U2 = SSM2212 - Audio Dual Matched NPN Transistor [part_number=SSM2212]
  U2_1 = AnalogDevices_SSM2212RZ_subpart1 [part_number=SSM2212]  # not connected
  U2_3 = AnalogDevices_SSM2212RZ_subpart3 [part_number=SSM2212]  # not connected

nets:
  N1: C1.-, C2.-, U1.connector3
  N2: C1.+, U1.connector8
  N3: C2.+, U1.connector4
  N4: U1.connector1, U2.connector3, U2.connector6
  N5: U1.connector2, R1.Pin_1, U2.connector1, U2.connector2, U2.connector7
  N6: R2.Pin_0, U2.connector8

notes:
  W2
  1-
  1+
  2-
  2+
  W1
  Vn
  GND
  Vp
