# Fritzing sketch low_input_head_room-bb (saved by Fritzing 0.9.3b)
breadboards: 1

parts:
  R1 = Resistor [tolerance=±5% resistance=47k package=THT]
  R2 = Resistor [tolerance=±5% resistance=100k package=THT]
  Q1 = PNP-Transistor [part_number=2N3906 package="TO92 [THT]"]
  U1 = SSM2212 - Audio Dual Matched NPN Transistor [part_number=SSM2212]
  U1_1 = AnalogDevices_SSM2212RZ_subpart1 [part_number=SSM2212]  # not connected
  U1_3 = AnalogDevices_SSM2212RZ_subpart3 [part_number=SSM2212]  # not connected
  R3 = Resistor [tolerance=±5% resistance=1k package=THT]
  R4 = Resistor [tolerance=±5% resistance=1k package=THT]

nets:
  N1: R1.Pin_0, R2.Pin_1
  N2: R2.Pin_0, Q1.E, U1.connector2, U1.connector7
  N3: Q1.B, U1.connector8, R3.Pin_1
  N4: Q1.C, U1.connector3, U1.connector6
  N5: U1.connector1, R4.Pin_1

notes:
  W2
  1-
  1+
  2-
  2+
  W1
  GND
  Vp
