# Fritzing sketch simple_current_mirror-bb (saved by Fritzing 0.9.3b)
breadboards: 1

parts:
  U1 = SSM2212 - Audio Dual Matched NPN Transistor [part_number=SSM2212]
  U1_1 = AnalogDevices_SSM2212RZ_subpart1 [part_number=SSM2212]  # not connected
  U1_3 = AnalogDevices_SSM2212RZ_subpart3 [part_number=SSM2212]  # not connected
  R1 = Resistor [tolerance=±5% resistance=1k package="0603 [SMD]"]
  R2 = Resistor [tolerance=±5% resistance=1k package="0603 [SMD]"]

nets:
  N1: U1.connector1, U1.connector2, U1.connector7, R1.Pin_1
  N2: U1.connector3, U1.connector6
  N3: U1.connector8, R2.Pin_1

notes:
  W2
  1-
  1+
  2-
  2+
  W1
  GND
