# Fritzing sketch cb_config-bb (saved by Fritzing 0.9.3b)
breadboards: 1

parts:
  R1 = Resistor [tolerance=±5% resistance=10k package="0402 [SMD]"]
  R2 = Resistor [tolerance=±5% resistance=10k package="0402 [SMD]"]
  R5 = Resistor [tolerance=±5% resistance=10k package="0402 [SMD]"]
  C1 = Electrolytic Capacitor [capacitance=4.7µF package="100 mil [THT, electrolytic]"]
  C2 = Electrolytic Capacitor [capacitance=1µF package="100 mil [THT, electrolytic]"]
  U1 = ADTL082 - Dual JFET Input Op Amps [part_number=ADTL082]
  2 = AnalogDevices_ADTL082ARZ_subpart2 [part_number=ADTL082]  # not connected
  1 = AnalogDevices_ADTL082ARZ_subpart1 [part_number=ADTL082]  # not connected
  C3 = Electrolytic Capacitor [capacitance=4.7µF package="100 mil [THT, electrolytic]"]
  2N3904 = TRANSISTOR_NPN [package=to-92-ammo]
  R4 = Resistor [tolerance=±5% resistance=1k package="0402 [SMD]"]
  R6 = Resistor [tolerance=±5% resistance=1k package="0402 [SMD]"]

nets:
  N1: R1.Pin_0, C1.+
  N2: R1.Pin_1, R2.Pin_1, C2.+
  N3: R2.Pin_0, R5.Pin_0, U1.connector2
  N4: R5.Pin_1, U1.connector1
  N5: C1.-, C2.-, U1.connector3, U1.connector5, C3.-
  N6: U1.connector4, C3.+
  N7: U1.connector6, 2N3904.E, R4.Pin_0
  N8: U1.connector7, 2N3904.B
  N9: 2N3904.C, R6.Pin_0

notes:
  Vp
  GND
  Vn
  W1
  2+
  2-
  1+
  1-
  W2
