# Fritzing sketch ce_config-bb (saved by Fritzing 0.9.3b)
breadboards: 1

parts:
  R1 = Resistor [tolerance=±5% resistance=10k package="0402 [SMD]"]
  R2 = Resistor [tolerance=±5% resistance=10k package="0402 [SMD]"]
  R3 = Resistor [tolerance=±5% resistance=10k package="0402 [SMD]"]
  C1 = Electrolytic Capacitor [capacitance=4.7µF package="100 mil [THT, electrolytic]"]
  C2 = Electrolytic Capacitor [capacitance=1µF package="100 mil [THT, electrolytic]"]
  U1 = ADTL082 - Dual JFET Input Op Amps [part_number=ADTL082]
  U1_2 = AnalogDevices_ADTL082ARZ_subpart2 [part_number=ADTL082]  # not connected
  U1_1 = AnalogDevices_ADTL082ARZ_subpart1 [part_number=ADTL082]  # not connected
  C5 = Electrolytic Capacitor [capacitance=4.7µF package="100 mil [THT, electrolytic]"]
  R4 = Resistor [tolerance=±5% resistance=100 package="0402 [SMD]"]
  R5 = Resistor [tolerance=±5% resistance=10k package="0402 [SMD]"]
  Q1 = TRANSISTOR_NPN [part_number=2N3904 package=to-92-ammo]

nets:
  N1: R1.Pin_0, C1.+
  N2: R1.Pin_1, R2.Pin_1, C2.+
  N3: R2.Pin_0, R3.Pin_0, U1.connector2
  N4: R3.Pin_1, U1.connector1
  N5: C1.-, C2.-, U1.connector3, U1.connector5, C5.-
  N6: U1.connector4, C5.+
  N7: U1.connector6, R5.Pin_0, Q1.B
  N8: U1.connector7, Q1.E
  N9: R4.Pin_0, Q1.C

notes:
  W2
  1-
  1+
  2-
  2+
  W1
  Vn
  GND
  Vp
