# Fritzing sketch generate_gummel_plot-bb (saved by Fritzing 0.9.3b)
breadboards: 1

parts:
  Q1 = NPN-Transistor [part_number=2N3904 package="TO92 [THT]"]
  R2 = Resistor [tolerance=±5% resistance=100 package="0805 [SMD]"]
  R1 = Resistor [tolerance=±5% resistance=10k package="0805 [SMD]"]

nets:
  N1: Q1.B, R1.Pin_1
  N2: Q1.C, R2.Pin_0

notes:
  W2
  1-
  1+
  2-
  2+
  W1
  GND
