# Fritzing sketch measure_vbe-bb (saved by Fritzing 0.9.3b)
breadboards: 1

parts:
  U1 = ADTL082 - Dual JFET Input Op Amps [part_number=ADTL082]
  U1_1 = AnalogDevices_ADTL082ARZ_subpart1 [part_number=ADTL082]  # not connected
  C1 = Electrolytic Capacitor [capacitance=4.7µF package="100 mil [THT, electrolytic]"]
  Q1 = TRANSISTOR_NPN [part_number=2N3904 package=to-92-ammo]
  C2 = Electrolytic Capacitor [capacitance=4.7µF package="0405 [SMD, electrolytic]"]
  R1 = Resistor [tolerance=±5% resistance=1k package="1206 [SMD]"]

nets:
  N1: U1.connector1, Q1.B
  N2: U1.connector2, Q1.E, R1.Pin_1
  N3: U1.connector3, C1.-, C2.-
  N4: U1.connector4, C2.+
  N5: U1.connector8, C1.+, Q1.C

notes:
  1-
  1+
  2-
  2+
  W1
  Vn
  GND
  Vp
