# Fritzing sketch loweff_vdrop_bb (saved by Fritzing 0.9.3b)
breadboards: 1

parts:
  Q1 = NPN-Transistor [part_number=2N3904 package="TO92 [THT]"]
  Q2 = PNP-Transistor [part_number=2N3906 package="TO92 [THT]"]
  R1 = Resistor [tolerance=±5% resistance=1k package=THT]
  R2 = Resistor [tolerance=±5% resistance=150k package=THT]

nets:
  N1: Q1.B, Q2.E, R2.Pin_0
  N2: Q1.C, Q2.B, R1.Pin_0

notes:
  Vn
  GND
  2-
  2+
  Vp
  W1
  1+
  1-
