# Fritzing sketch npn_diode_bb (saved by Fritzing 0.9.3b)
breadboards: 1

parts:
  Q1 = NPN-Transistor [part_number=2N3904 package="TO92 [THT]"]
  R1 = Resistor [tolerance=±5% resistance=1k package=THT]

nets:
  N1: Q1.B, Q1.C, R1.Pin_0

notes:
  GND
  1-
  1+
  W1
  2+
  2-
