# Fritzing sketch pnp_emitter_bb (saved by Fritzing 0.9.3b)
breadboards: 1

parts:
  R1 = Resistor [tolerance=±5% resistance=100 package=THT]
  Q1 = PNP-Transistor [part_number=2N3906 package="TO92 [THT]"]

nets:
  N1: R1.Pin_0, Q1.B, Q1.C

notes:
  Vn
  1-
  1+
  W1
  2+
  2-
