# Fritzing sketch balanced_sr_flw-bb (saved by Fritzing 0.9.3b)
breadboards: 1

parts:
  U1 = SSM2212 - Audio Dual Matched NPN Transistor [part_number=SSM2212]
  U1_1 = AnalogDevices_SSM2212RZ_subpart1 [part_number=SSM2212]  # not connected
  U1_3 = AnalogDevices_SSM2212RZ_subpart3 [part_number=SSM2212]  # not connected
  U2 = SSM2220 - Audio Dual Matched PNP Transistor [part_number=SSM2220]
  U2_1 = AnalogDevices_SSM2220S_subpart1 [part_number=SSM2220]  # not connected
  U2_3 = AnalogDevices_SSM2220S_subpart3 [part_number=SSM2220]  # not connected
  0_01uF = Capacitor [package=cap-pth-small2]
  R1 = Resistor [tolerance=±5% resistance=10k package=THT]
  R2 = Resistor [tolerance=±5% resistance=2.2k package=THT]
  R3 = Resistor [tolerance=±5% resistance=2.2k package=THT]
  Q1 = TRANSISTOR_PNP [part_number=2N3906 package=to-92]
  Q2 = TRANSISTOR_NPN [part_number=2N3904 package=to-92-ammo]

nets:
  N1: U1.connector1, 0_01uF.2, R1.Pin_1, Q2.E
  N2: U1.connector2, U1.connector7, U1.connector8, Q1.C
  N3: U1.connector3, U1.connector6
  N4: U2.connector1, U2.connector2, U2.connector7, R3.Pin_1
  N5: U2.connector3, U2.connector6
  N6: U2.connector8, Q1.E, Q2.C
  N7: 0_01uF.1, R1.Pin_0, R2.Pin_0
  N8: R2.Pin_1, R3.Pin_0, Q1.B

notes:
  1-
  1+
  2-
  2+
  W1
  Vn
  GND
  Vp
