# Fritzing sketch compl_fb_flw-bb (saved by Fritzing 0.9.3b)
breadboards: 1

parts:
  Q1 = TRANSISTOR_NPN [part_number=2N3904 package=to-92-ammo]
  Q4 = TRANSISTOR_PNP [part_number=2N3906 package=to-92]
  R1 = Resistor [tolerance=±5% resistance=10k package=THT]
  R2 = Resistor [tolerance=±5% resistance=2.2k package=THT]

nets:
  N1: Q1.E, Q4.C, R2.Pin_1
  N2: Q1.C, Q4.B, R1.Pin_0
  N3: Q4.E, R1.Pin_1

notes:
  1-
  1+
  2-
  2+
  W1
  Vn
  GND
  Vp
