# Fritzing sketch emit_flw-bb (saved by Fritzing 0.9.3b)
breadboards: 1

parts:
  R1 = Resistor [tolerance=±5% resistance=2.2k package=THT]
  Q1 = NPN-Transistor [part_number=2N3904 package="TO92 [THT]"]

nets:
  N1: R1.Pin_1, Q1.E

notes:
  1-
  1+
  2-
  2+
  W1
  Vn
  GND
  Vp
