# Fritzing sketch flw_gain_gr_one-bb (saved by Fritzing 0.9.3b)
breadboards: 1

parts:
  Q5 = TRANSISTOR_NPN [part_number=2N3904 package=to-92-ammo]
  Q6 = TRANSISTOR_PNP [part_number=2N3906 package=to-92]
  R1 = Resistor [tolerance=±5% resistance=1k package=THT]
  R2 = Resistor [tolerance=±5% resistance=1k package=THT]
  R3 = Resistor [tolerance=±5% resistance=2.2k package=THT]

nets:
  N1: Q5.E, R2.Pin_1, R3.Pin_0
  N2: Q5.C, Q6.B, R1.Pin_0
  N3: Q6.E, R1.Pin_1
  N4: Q6.C, R3.Pin_1

notes:
  1-
  1+
  2-
  2+
  W1
  Vn
  GND
  Vp
