# Fritzing sketch low_off_flw-bb (saved by Fritzing 0.9.3b)
breadboards: 1

parts:
  U1 = SSM2212 - Audio Dual Matched NPN Transistor [part_number=SSM2212]
  U1_1 = AnalogDevices_SSM2212RZ_subpart1 [part_number=SSM2212]  # not connected
  U1_3 = AnalogDevices_SSM2212RZ_subpart3 [part_number=SSM2212]  # not connected
  Q1 = PNP-Transistor [part_number=2N3906 package="TO92 [THT]"]
  Q2 = NPN-Transistor [part_number=2N3904 package="TO92 [THT]"]
  R1 = Resistor [tolerance=±5% resistance=10k package=THT]
  R2 = Resistor [tolerance=±5% resistance=6.8k package=THT]
  10nF = Capacitor [package=cap-pth-small2]

nets:
  N1: U1.connector1, U1.connector2, U1.connector7, Q1.C
  N2: U1.connector3, U1.connector6
  N3: U1.connector8, Q2.E
  N4: Q1.E, Q2.B, R1.Pin_1, R2.Pin_0, 10nF.1
  N5: Q2.C, R2.Pin_1
  N6: R1.Pin_0, 10nF.2

notes:
  1-
  1+
  2-
  2+
  W1
  Vn
  GND
  Vp
