# Fritzing sketch out_imp_test-bb (saved by Fritzing 0.9.3b)
breadboards: 1

parts:
  Q1 = NPN-Transistor [part_number=2N3904 package="TO92 [THT]"]
  R1 = Resistor [tolerance=±5% resistance=4.7k package=THT]
  R2 = Resistor [tolerance=±5% resistance=10k package=THT]

nets:
  N1: Q1.E, R1.Pin_1, R2.Pin_0

notes:
  1-
  1+
  2-
  2+
  W1
  Vn
  GND
  Vp
