# Fritzing sketch astable_multivib_bb (saved by Fritzing 0.9.3b)
breadboards: 1

parts:
  RED_LED = LED - 5mm [color="Red (633nm)" package="5 mm [THT]"]
  R1 = Resistor [tolerance=±5% resistance=470 package=THT]
  2N3904 = NPN-Transistor [package="TO92 [THT]"]
  C1 = Electrolytic Capacitor [capacitance=47µF package="100 mil [THT, electrolytic]"]
  R2 = Resistor [tolerance=±5% resistance=20k package=THT]
  2N3904_2 = NPN-Transistor [package="TO92 [THT]"]
  C2 = Electrolytic Capacitor [capacitance=47µF package="100 mil [THT, electrolytic]"]
  R3 = Resistor [tolerance=±5% resistance=20k package=THT]
  R4 = Resistor [tolerance=±5% resistance=470 package=THT]
  GREEN_LED = LED - 5mm [color="Green (560nm)" package="5 mm [THT]"]

nets:
  N1: RED_LED.cathode, R1.Pin_0
  N2: RED_LED.anode, R2.Pin_1, R3.Pin_1, GREEN_LED.anode
  N3: R1.Pin_1, 2N3904.C, C1.-
  N4: 2N3904.E, 2N3904_2.E
  N5: 2N3904.B, C2.+, R3.Pin_0
  N6: C1.+, R2.Pin_0, 2N3904_2.B
  N7: 2N3904_2.C, C2.-, R4.Pin_0
  N8: R4.Pin_1, GREEN_LED.cathode

notes:
  GND
  Vp
  1+
  1-
  2+
  2-
