# Fritzing sketch bistable_multivib_bb (saved by Fritzing 0.9.3b)
breadboards: 1

parts:
  RED_LED = LED - 5mm [color="Red (633nm)" package="5 mm [THT]"]
  R1 = Resistor [tolerance=±5% resistance=470 package=THT]
  2N3904 = NPN-Transistor [package="TO92 [THT]"]
  2N3904_2 = NPN-Transistor [package="TO92 [THT]"]
  R3 = Resistor [tolerance=±5% resistance=47k package=THT]
  R4 = Resistor [tolerance=±5% resistance=470 package=THT]
  GREEN_LED = LED - 5mm [color="Green (560nm)" package="5 mm [THT]"]
  R5 = Resistor [tolerance=±5% resistance=47k package=THT]
  1N914 = Rectifier Diode [part_number=1N4001 package="300 mil [THT]"]
  R6 = Resistor [tolerance=±5% resistance=1k package=THT]
  1N914_2 = Rectifier Diode [part_number=1N4001 package="300 mil [THT]"]
  R7 = Resistor [tolerance=±5% resistance=1k package=THT]

nets:
  N1: RED_LED.cathode, R1.Pin_0
  N2: RED_LED.anode, GREEN_LED.anode
  N3: R1.Pin_1, 2N3904.C, R5.Pin_0
  N4: 2N3904.E, 2N3904_2.E
  N5: 2N3904.B, R3.Pin_1, 1N914_2.cathode
  N6: 2N3904_2.B, R5.Pin_1, 1N914.cathode
  N7: 2N3904_2.C, R3.Pin_0, R4.Pin_0
  N8: R4.Pin_1, GREEN_LED.cathode
  N9: 1N914.anode, R6.Pin_0
  N10: 1N914_2.anode, R7.Pin_1

notes:
  GND
  Vp
  1+
  1-
  2+
  2-
  Set
  Reset
