# Fritzing sketch d_type_flipflop_bb (saved by Fritzing 0.9.3b)
breadboards: 1

parts:
  2N3904 = NPN-Transistor [package="TO92 [THT]"]
  2N3904_2 = NPN-Transistor [package="TO92 [THT]"]
  2N3904_3 = NPN-Transistor [package="TO92 [THT]"]
  R1 = Resistor [tolerance=±0.05% resistance=1k package=THT]
  R2 = Resistor [tolerance=±5% resistance=100k package=THT]
  R3 = Resistor [tolerance=±5% resistance=47k package=THT]
  R4 = Resistor [tolerance=±5% resistance=1k package=THT]
  R5 = Resistor [tolerance=±5% resistance=47k package=THT]
  R6 = Resistor [tolerance=±5% resistance=1k package=THT]
  39pF = Tantalum Capacitor [capacitance="1 μF" package="B 3528 [SMD, tantalum]"]
  39pF_2 = Tantalum Capacitor [capacitance="1 μF" package="B 3528 [SMD, tantalum]"]
  100pF = Tantalum Capacitor [capacitance="1 μF" package="B 3528 [SMD, tantalum]"]
  100pF_2 = Tantalum Capacitor [capacitance="1 μF" package="B 3528 [SMD, tantalum]"]
  D1 = Rectifier Diode [part_number=1N914 package="300 mil [THT]"]
  D2 = Rectifier Diode [part_number=1N914 package="300 mil [THT]"]
  R7 = Resistor [tolerance=±5% resistance=200k package=THT]
  R8 = Resistor [tolerance=±5% resistance=200k package=THT]

nets:
  N1: 2N3904.E, 2N3904_2.E, 2N3904_3.E
  N2: 2N3904.B, R2.Pin_1
  N3: 2N3904.C, R1.Pin_0, R7.Pin_0
  N4: 2N3904_2.C, R3.Pin_1, R4.Pin_0, 39pF_2.+
  N5: 2N3904_3.C, R5.Pin_1, R6.Pin_0
  N6: R1.Pin_1, R4.Pin_1, R6.Pin_1
  N7: R2.Pin_0, R8.Pin_0
  N8: R3.Pin_0, 39pF_2.-, D1.anode
  N9: R5.Pin_0, 39pF.+, D2.anode
  N10: 100pF.-, 100pF_2.-
  N11: 100pF.+, D1.cathode, R8.Pin_1
  N12: 100pF_2.+, D2.cathode, R7.Pin_1

notes:
  Vp
  1+
  1-
  W1
  W2
  GND
  2+
  2-
