# Fritzing sketch divide_by_two_flipflop_bb (saved by Fritzing 0.9.3b)
breadboards: 1

parts:
  2N3904 = NPN-Transistor [package="TO92 [THT]"]
  39pF = Tantalum Capacitor [capacitance=1μF package="100 mil [THT, tantalum]"]
  2N3904_2 = NPN-Transistor [package="TO92 [THT]"]
  39pF_2 = Tantalum Capacitor [capacitance=1μF package="100 mil [THT, tantalum]"]
  R1 = Resistor [tolerance=±5% resistance=47k package=THT]
  R2 = Resistor [tolerance=±5% resistance=1k package=THT]
  R3 = Resistor [tolerance=±5% resistance=47k package=THT]
  R4 = Resistor [tolerance=±5% resistance=1k package=THT]
  R5 = Resistor [tolerance=±5% resistance=200k package=THT]
  R6 = Resistor [tolerance=±5% resistance=200k package=THT]
  D1 = Rectifier Diode [part_number=1N914 package="300 mil [THT]"]
  100pF = Tantalum Capacitor [capacitance=1µF package="100 mil [THT, tantalum]"]
  100pF_2 = Tantalum Capacitor [capacitance=1μF package="100 mil [THT, tantalum]"]
  D2 = Rectifier Diode [part_number=1N914 package="300 mil [THT]"]

nets:
  N1: 2N3904.E, 2N3904_2.E
  N2: 2N3904.B, 39pF_2.+, R3.Pin_0, D1.anode
  N3: 2N3904.C, 39pF.-, R1.Pin_1, R2.Pin_0, R5.Pin_0
  N4: 39pF.+, 2N3904_2.B, R1.Pin_0, D2.anode
  N5: 2N3904_2.C, 39pF_2.-, R3.Pin_1, R4.Pin_0, R6.Pin_0
  N6: R2.Pin_1, R4.Pin_1
  N7: R5.Pin_1, D1.cathode, 100pF.+
  N8: R6.Pin_1, 100pF_2.+, D2.cathode
  N9: 100pF.-, 100pF_2.-

notes:
  Vp
  W1
  1+
  1-
  GND
  2+
  2-
