# Fritzing sketch bjt_stabilized_cs-bb (saved by Fritzing 0.9.3b)
breadboards: 1

parts:
  Q1 = NPN-Transistor [part_number=2N3904 package="TO92 [THT]"]
  R1 = Resistor [tolerance=±5% resistance=100 package=THT]
  R2 = Resistor [tolerance=±5% resistance=2.2k package=THT]
  Q2 = NPN-Transistor [part_number=2N3904 package="TO92 [THT]"]
  R3 = Resistor [tolerance=±5% resistance=4.7k package=THT]

nets:
  N1: Q1.E, Q2.E
  N2: Q1.B, R1.Pin_1, R2.Pin_0
  N3: Q1.C, R1.Pin_0, Q2.B
  N4: Q2.C, R3.Pin_0

notes:
  1-
  1+
  2-
  2+
  W1
  GND
  Vp
