# Fritzing sketch vbe_circuit2-bb (saved by Fritzing 0.9.3b)
breadboards: 1

parts:
  Q1 = NPN-Transistor [part_number=2N3904 package="TO92 [THT]"]
  R1 = Resistor [tolerance=±5% resistance=10k package=THT]
  R2 = Resistor [tolerance=±5% resistance=1k package=THT]
  R3 = Resistor [tolerance=±5% resistance=10k package=THT]
  R4 = Trimmer Potentiometer [maximum_resistance=10kΩ package=THT]

nets:
  N1: Q1.E, R3.Pin_0
  N2: Q1.B, R1.Pin_0, R3.Pin_1
  N3: Q1.C, R4.leg1
  N4: R1.Pin_1, R2.Pin_0, R4.wiper, R4.leg2

notes:
  1-
  1+
  2-
  2+
  W1
  GND
