# Fritzing sketch zero_gain-bb (saved by Fritzing 0.9.3b)
breadboards: 1

parts:
  Q1 = NPN-Transistor [part_number=2N3904 package="SOT-23 [SMD]"]
  R1 = Resistor [tolerance=±5% resistance=47 package="2512 [SMD]"]
  R2 = Resistor [tolerance=±5% resistance=2.2k package="2512 [SMD]"]

nets:
  N1: Q1.0, R1.Pin_1, R2.Pin_0
  N2: Q1.1, R1.Pin_0

notes:
  1-
  1+
  2-
  2+
  W1
  GND
