# Fritzing sketch bpf_bb (saved by Fritzing 0.9.3b)
breadboards: 1

parts:
  L2 = Inductors [package=cr54-kit]
  R2 = Resistor [tolerance=±5% resistance=1k package="2010 [SMD]"]
  C1 = Electrolytic Capacitor [capacitance=1µF package="100 mil [THT, electrolytic]"]

nets:
  N1: L2.1, C1.-
  N2: L2.2, R2.Pin_1, C1.+

notes:
  10mH
  0.047μF
  1kΩ
  1+
  1-
  2+
  2-
  GND
  W1
