# Fritzing sketch bsf_bb (saved by Fritzing 0.9.3b)
breadboards: 1

parts:
  R1 = Resistor [tolerance=±5% resistance=1k package="2512 [SMD]"]
  L1 = Inductors [package=cr54]
  L2 = Inductors [package=cr54]
  C3 = Capacitor [package=cap-pth-small2]

nets:
  N1: R1.Pin_1, L1.2
  N2: L1.1, L2.2
  N3: L2.1, C3.1

notes:
  1kΩ
  0.1μF
  10mH
  GND
  W1
  1+
  2+
  2-
  1-
