# Fritzing sketch buck_bb (saved by Fritzing 0.9.3b)
breadboards: 1

parts:
  R1 = Resistor [tolerance=±5% resistance=22k package="0603 [SMD]"]
  R2 = Resistor [tolerance=±5% resistance=1k package="0603 [SMD]"]
  Q1 = TRANSISTOR_NPN [package=to-92-ammo]
  D1 = Zener Diode [part_number=1N4732A breakdown_voltage=3.6V package="300 mil [THT]"]
  D2 = Zener Diode [part_number=1N4732A breakdown_voltage=3.6V package="300 mil [THT]"]
  IC1 = IC, DIP package, 8 pins [chip_label=LT1054]
  C1 = Electrolytic Capacitor [capacitance=10μF package="0605 [SMD, electrolytic]"]
  C2 = Ceramic Capacitor [capacitance=100nF package="100 mil [THT, multilayer]"]
  C3 = Electrolytic Capacitor [capacitance=10μF package="0605 [SMD, electrolytic]"]
  R3 = Resistor [tolerance=±5% resistance=1 package="0603 [SMD]"]

nets:
  N1: R1.Pin_0, Q1.C
  N2: R1.Pin_1, IC1.pin6
  N3: R2.Pin_1, Q1.B
  N4: Q1.E, D1.anode, IC1.pin3, IC1.pin5, C1.-
  N5: D1.cathode, D2.anode, IC1.pin2, R3.Pin_0
  N6: D2.cathode, IC1.pin8, C1.+
  N7: C2.1, C3.-
  N8: C3.+, R3.Pin_1

notes:
  GND
  D0
  1kΩ
  22kΩ
  Vp
  22uF
  1-
  1N5818
  SHUT DOWN
  CONNECTION
  1+
  SWITCH NODE
  RIPPLE
  1uF
  1Ω
  4, 5, 6, IND. TAPS
  1, 2, 3, IND. TAPS
  2+
  2-
  HPH1-1400L
  2N3904
