# Fritzing sketch first_order_cascaded_rc_bb (saved by Fritzing 0.9.3b)
breadboards: 1

parts:
  R1 = Resistor [tolerance=±5% resistance=1k package="0603 [SMD]"]
  C4 = Capacitor [package=cap-pth-small2]

nets:
  N1: R1.Pin_1, C4.1

notes:
  GND
  1kΩ
  0.1μF
  W1
  1+
  1-
  2-
  2+
