# Fritzing sketch third_order_cascaded_rc_bb (saved by Fritzing 0.9.3b)
breadboards: 1

parts:
  R1 = Resistor [tolerance=±5% resistance=1k package="0603 [SMD]"]
  R2 = Resistor [tolerance=±5% resistance=1k package="0603 [SMD]"]
  R3 = Resistor [tolerance=±5% resistance=1k package="0603 [SMD]"]
  C4 = Capacitor [package=cap-pth-small2]
  C5 = Capacitor [package=cap-pth-small2]
  C6 = Capacitor [package=cap-pth-small2]

nets:
  N1: R1.Pin_1, R2.Pin_0, C4.1
  N2: R2.Pin_1, R3.Pin_0, C5.1
  N3: R3.Pin_1, C6.1
  N4: C4.2, C5.2, C6.2

notes:
  GND
  1kΩ
  0.1μF
  W1
  1+
  1-
  2-
  2+
