# Fritzing sketch clapp_osc-bb (saved by Fritzing 0.9.3b)
breadboards: 1

parts:
  Q1 = TRANSISTOR_NPN [package=to-92-ammo]
  R1 = Resistor [tolerance=±5% resistance=10k package="0402 [SMD]"]
  R2 = Resistor [tolerance=±5% resistance=1k package="0402 [SMD]"]
  C1 = Capacitor [package=cap-pth-small2]
  R3 = Resistor [tolerance=±5% resistance=100 package="0402 [SMD]"]
  C2 = Capacitor [package=cap-pth-small2]
  C3 = Capacitor [package=cap-pth-small2]
  L1 = Inductors [package=cr54-kit]
  L2 = Inductors [package=cr54-kit]
  C4 = Capacitor [package=cap-pth-small2]
  C5 = Capacitor [package=cap-pth-small2]

nets:
  N1: Q1.E, R3.Pin_1, C2.2, C3.1
  N2: Q1.B, R1.Pin_0, R2.Pin_1, C1.2
  N3: Q1.C, C3.2, L1.1, L2.1
  N4: R1.Pin_1, L1.2
  N5: R2.Pin_0, C1.1, C4.2
  N6: R3.Pin_0, C2.1
  N7: L2.2, C4.1, C5.2

notes:
  Vp
  Vn
  GND
  1-
  1+
  2N3904
  0.1uF
  1nF
  4.7nF
  10uH
  100uH
  10nF
  10KΩ
  1KΩ
  100Ω
