# Fritzing sketch cmos_amplifier_hardware_setup_1 (saved by Fritzing 0.9.3b)
breadboards: 1

parts:
  IC1 = IC, DIP package, 14 pins [chip_label=HEF4007]

nets:
  N1: IC1.pin8, IC1.pin13

notes:
  1-
  1+
  2-
  2+
  W1
  GND
  Vp
