# Fritzing sketch cmos_amplifier_hardware_setup_2a (saved by Fritzing 0.9.3b)
breadboards: 1

parts:
  IC1 = IC, DIP package, 14 pins [chip_label=HEF4007]
  R1 = Resistor [tolerance=±5% resistance=100k package=THT]
  R2 = Resistor [tolerance=±5% resistance=100k package=THT]
  C1 = Electrolytic Capacitor [capacitance=22µF package="100 mil [THT, electrolytic]"]
  C2 = Electrolytic Capacitor [capacitance=22µF package="100 mil [THT, electrolytic]"]

nets:
  N1: IC1.pin6, R1.Pin_1, R2.Pin_1
  N2: IC1.pin8, IC1.pin13, R1.Pin_0, C2.+
  N3: R2.Pin_0, C1.-

notes:
  1-
  1+
  2-
  2+
  W1
  GND
  Vp
