# Fritzing sketch cmos_amplifier_hardware_setup_3a (saved by Fritzing 0.9.3b)
breadboards: 1

parts:
  IC1 = IC, DIP package, 14 pins [chip_label=HEF4007]
  C1 = Electrolytic Capacitor [capacitance=1µF package="100 mil [THT, electrolytic]"]
  R1 = Resistor [tolerance=±5% resistance=10k package=THT]
  R2 = Resistor [tolerance=±5% resistance=100k package=THT]
  R3 = Resistor [tolerance=±5% resistance=4.7k package=THT]
  R4 = Resistor [tolerance=±5% resistance=100k package=THT]
  C2 = Electrolytic Capacitor [capacitance=1µF package="100 mil [THT, electrolytic]"]
  R5 = Resistor [tolerance=±5% resistance=100k package=THT]
  C3 = Ceramic Capacitor [capacitance=10pF package="100 mil [THT, multilayer]"]
  C4 = Electrolytic Capacitor [capacitance=22µF package="100 mil [THT, electrolytic]"]
  C5 = Electrolytic Capacitor [capacitance=22µF package="100 mil [THT, electrolytic]"]

nets:
  N1: IC1.pin1, IC1.pin5, C1.+, R4.Pin_1
  N2: IC1.pin2, IC1.pin11, IC1.pin14
  N3: IC1.pin3, R1.Pin_1, R3.Pin_1, R4.Pin_0
  N4: IC1.pin4, IC1.pin7, IC1.pin9
  N5: IC1.pin6, C2.-, R5.Pin_1, C3.1
  N6: IC1.pin8, IC1.pin13, R1.Pin_0, R5.Pin_0, C3.0, C4.+
  N7: IC1.pin10, C1.-, R2.Pin_0
  N8: IC1.pin12, R2.Pin_1, C2.+
  N9: R3.Pin_0, C5.-

notes:
  1-
  1+
  2-
  2+
  W1
  GND
  Vp
