# Fritzing sketch nmos_ron_test_circuit-bb (saved by Fritzing 0.9.3b)
breadboards: 1

parts:
  IC1 = IC, DIP package, 14 pins [chip_label=HEF4007]
  U1 = SSM2212 - Audio Dual Matched NPN Transistor [part_number=SSM2212]
  U1_1 = AnalogDevices_SSM2212RZ_subpart1 [part_number=SSM2212]  # not connected
  U1_3 = AnalogDevices_SSM2212RZ_subpart3 [part_number=SSM2212]  # not connected
  R1 = Resistor [tolerance=±5% resistance=4.7k package=THT]

nets:
  N1: IC1.pin1, IC1.pin12
  N2: IC1.pin2, IC1.pin9, U1.connector1
  N3: IC1.pin3, IC1.pin10, IC1.pin14
  N4: IC1.pin7, U1.connector3, U1.connector6
  N5: U1.connector2, U1.connector7, U1.connector8, R1.Pin_0

notes:
  1-
  1+
  2-
  2+
  W1
  Vn
  GND
  Vp
