# Fritzing sketch dtype_latch_bb (saved by Fritzing 0.9.3b)
breadboards: 1

parts:
  IC1 = IC, DIP package, 14 pins [chip_label=HEF4007]
  ZVP2210A = PNP-Transistor [package="TO92 [THT]"]
  ZVP2210A_2 = PNP-Transistor [package="TO92 [THT]"]
  ZVN2210A = NPN-Transistor [package="TO92 [THT]"]
  ZVN2110A = NPN-Transistor [package="TO92 [THT]"]

nets:
  N1: IC1.pin1, IC1.pin9
  N2: IC1.pin2, IC1.pin5, IC1.pin12, ZVP2210A.B, ZVN2210A.B
  N3: IC1.pin3, IC1.pin6
  N4: IC1.pin4, IC1.pin11, ZVP2210A_2.E, ZVN2110A.E
  N5: IC1.pin7, ZVN2210A.C, ZVN2110A.C
  N6: IC1.pin8, IC1.pin10, IC1.pin13
  N7: IC1.pin14, ZVP2210A.C, ZVP2210A_2.C
  N8: ZVP2210A.E, ZVP2210A_2.B, ZVN2210A.E, ZVN2110A.B

notes:
  2+
  W2
  Vp
  W1
  2-
  GND
