# Fritzing sketch cmos_inv_bb (saved by Fritzing 0.9.3b)
breadboards: 1

parts:
  IC1 = IC, DIP package, 14 pins [chip_label=HEF4007]

nets:
  N1: IC1.pin8, IC1.pin13

notes:
  Vp
  2+
  1+
  W1
  2-
  1-
  GND
