# Fritzing sketch cmos_schmitt_trig_bb (saved by Fritzing 0.9.3b)
breadboards: 1

parts:
  IC1 = IC, DIP package, 14 pins [chip_label=HEF4007]

nets:
  N1: IC1.pin1, IC1.pin7
  N2: IC1.pin2, IC1.pin11, IC1.pin13
  N3: IC1.pin3, IC1.pin12
  N4: IC1.pin4, IC1.pin8, IC1.pin9
  N5: IC1.pin5, IC1.pin14
  N6: IC1.pin6, IC1.pin10

notes:
  Vp
  1+
  1-
  GND
  2+
  W1
  2-
