# Fritzing sketch measure_thres_trans_bb (saved by Fritzing 0.9.3b)
breadboards: 1

parts:
  R1 = Resistor [tolerance=±5% resistance=100 package=THT]
  R2 = Resistor [tolerance=±5% resistance=100 package=THT]
  IC1 = IC, DIP package, 14 pins [chip_label=HEF4007]

nets:
  N1: R1.Pin_1, IC1.pin14
  N2: R2.Pin_0, IC1.pin6
  N3: IC1.pin8, IC1.pin13

notes:
  Vp
  2+
  1+
  W1
  2-
  1-
  GND
