# Fritzing sketch two_in_nand_bb (saved by Fritzing 0.9.3b)
breadboards: 1

parts:
  IC1 = IC, DIP package, 14 pins [chip_label=HEF4007]

nets:
  N1: IC1.pin8, IC1.pin9
  N2: IC1.pin11, IC1.pin14
  N3: IC1.pin12, IC1.pin13

notes:
  Vp
  1+
  1-
  GND
  input B
  input A
