# Fritzing sketch cmos_logic_gate_xor_and_xnor_hardware_setup2_bb (saved by Fritzing 0.9.3b)
breadboards: 1

parts:
  Q1 = PNP-Transistor [part_number=ZVP2110A package="TO92 [THT]"]
  Q2 = NPN-Transistor [part_number=ZVN3310 package="TO92 [THT]"]
  IC1 = IC, DIP package, 14 pins [chip_label=HEF4007]
  Q3 = NPN-Transistor [part_number=ZVN3310 package="TO92 [THT]"]
  Q4 = PNP-Transistor [part_number=ZVP2110A package="TO92 [THT]"]
  C1 = Ceramic Capacitor [capacitance="100 nF" package="0603 [SMD, multilayer]"]
  R1 = Resistor [tolerance=±5% resistance=47k package=THT]
  R2 = Resistor [tolerance=±5% resistance=47k package=THT]
  C2 = Ceramic Capacitor [capacitance="100 nF" package="0603 [SMD, multilayer]"]

nets:
  N1: Q1.E, IC1.pin14, Q4.E
  N2: Q1.B, Q2.B, IC1.pin1, IC1.pin9
  N3: Q1.C, Q2.C, IC1.pin4, IC1.pin11
  N4: Q2.E, IC1.pin7, Q3.E, C1.1, C2.1
  N5: IC1.pin2, IC1.pin5, IC1.pin12, Q3.B, Q4.B, R1.Pin_0
  N6: IC1.pin3, IC1.pin6
  N7: IC1.pin8, IC1.pin10, IC1.pin13
  N8: Q3.C, Q4.C, R2.Pin_0
  N9: C1.0, R1.Pin_1
  N10: R2.Pin_1, C2.0

notes:
  W2
  1-
  1+
  2-
  2+
  W1
  GND
  Vp
  0.001uF
