# Fritzing sketch colpitts_osc-bb (saved by Fritzing 0.9.3b)
breadboards: 1

parts:
  Q1 = TRANSISTOR_NPN [package=to-92-ammo]
  C1 = Capacitor [package=cap-pth-small2]
  C2 = Capacitor [package=cap-pth-small2]
  L1 = Inductors [package=cr54-kit]
  R1 = Resistor [tolerance=±5% resistance=1k package="0402 [SMD]"]
  C3 = Capacitor [package=cap-pth-small2]
  R2 = Resistor [tolerance=±5% resistance=1k package="0402 [SMD]"]
  R3 = Resistor [tolerance=±5% resistance=10k package="0402 [SMD]"]
  C4 = Capacitor [package=cap-pth-small2]

nets:
  N1: Q1.E, C1.2, C2.1, R1.Pin_1
  N2: Q1.B, C3.2, R2.Pin_1, R3.Pin_0
  N3: Q1.C, C1.1, L1.1, C4.1
  N4: C2.2, L1.2, R3.Pin_1
  N5: R1.Pin_0, C3.1, R2.Pin_0

notes:
  Vp
  Vn
  1+
  GND
  1-
  2N3904
  1kΩ
  10kΩ
  1nF
  4.7nF
  0.1uF
  100uH
