# Fritzing sketch alt_ce_amp_test_config-bb (saved by Fritzing 0.9.3b)
breadboards: 1

parts:
  U1 = ADTL082 - Dual JFET Input Op Amps [part_number=ADTL082]
  U1_1 = AnalogDevices_ADTL082ARZ_subpart1 [part_number=ADTL082]  # not connected
  RB = Resistor [tolerance=±5% resistance=1k package="0805 [SMD]"]
  Rpot = TRIMPOT [package=3362u-2]
  Q2 = TRANSISTOR_NPN [part_number=2N3904 package=to-92-ammo]
  RL = Resistor [tolerance=±5% resistance=250 package="2010 [SMD]"]
  R1 = Resistor [tolerance=±5% resistance=1k package="0805 [SMD]"]
  R2 = Resistor [tolerance=±5% resistance=1k package="0805 [SMD]"]
  C1 = Electrolytic Capacitor [capacitance=4.7µF package="100 mil [THT, electrolytic]"]
  C2 = Electrolytic Capacitor [capacitance=4.7µF package="100 mil [THT, electrolytic]"]

nets:
  N1: U1.connector1, Q2.E
  N2: U1.connector2, RB.Pin_1, Q2.B
  N3: U1.connector3, R1.Pin_1, R2.Pin_0
  N4: U1.connector4, C2.+
  N5: U1.connector8, Rpot.CW, RL.Pin_1, C1.+
  N6: RB.Pin_0, Rpot.WIPER
  N7: Rpot.CCW, R2.Pin_1, C1.-, C2.-
  N8: Q2.C, RL.Pin_0

notes:
  1-
  1+
  2-
  2+
  W1
  Vn
  GND
  Vp
