# Fritzing sketch c2_added_inc_ac_gain-bb (saved by Fritzing 0.9.3b)
breadboards: 1

parts:
  2N3904 = NPN-Transistor [package="TO92 [THT]"]
  RL = Resistor [tolerance=±5% resistance=1k package=THT]
  U1 = POT [package=3362u]
  RE = POT [package=3362u]
  RB = Resistor [tolerance=±5% resistance=1k package=THT]
  R2 = Resistor [tolerance=±5% resistance=1k package=THT]
  R1 = Resistor [tolerance=±5% resistance=1k package=THT]
  C1 = Ceramic Capacitor [capacitance=4.7µF package="100 mil [THT, multilayer]"]
  C2 = Ceramic Capacitor [capacitance=4.7µF package="100 mil [THT, multilayer]"]

nets:
  N1: 2N3904.E, RE.S, RE.A, C2.0
  N2: 2N3904.B, RB.Pin_1
  N3: 2N3904.C, RL.Pin_0
  N4: RL.Pin_1, U1.A
  N5: U1.E, RE.E, R2.Pin_1, C2.1
  N6: U1.S, RB.Pin_0, C1.1
  N7: R2.Pin_0, R1.Pin_1, C1.0

notes:
  1-
  1+
  2-
  2+
  W1
  GND
  Vp
