# Fritzing sketch self_biased_config-bb (saved by Fritzing 0.9.3b)
breadboards: 1

parts:
  RL = Resistor [tolerance=±5% resistance=1k package=THT]
  2N3904 = NPN-Transistor [package="TO92 [THT]"]
  R3 = Resistor [tolerance=±5% resistance=4.7k package=THT]
  R4 = Resistor [tolerance=±5% resistance=1.5k package=THT]
  C1 = Ceramic Capacitor [capacitance=4.7µF package="100 mil [THT, multilayer]"]
  R2 = Resistor [tolerance=±5% resistance=1k package=THT]
  R1 = Resistor [tolerance=±5% resistance=1k package=THT]

nets:
  N1: RL.Pin_0, 2N3904.C, R3.Pin_0
  N2: 2N3904.E, R4.Pin_0, R2.Pin_0
  N3: 2N3904.B, R3.Pin_1, R4.Pin_1, C1.1
  N4: C1.0, R2.Pin_1, R1.Pin_0

notes:
  1-
  1+
  2-
  2+
  W1
  GND
  Vp
