# Fritzing sketch csamp_tc_bb (saved by Fritzing 0.9.3b)
breadboards: 1

parts:
  ZVN2110A_placeholder = MOSFET-NCHANNEL [package=to-92]
  R1 = Resistor [tolerance=±5% resistance=470 package=THT]
  R2 = Resistor [tolerance=±5% resistance=68 package=THT]
  C1 = Ceramic Capacitor [capacitance=100nF package="100 mil [THT, multilayer]"]
  R4 = TRIMPOT [package=3362u-2]
  R5 = Resistor [tolerance=±5% resistance=4.7k package=THT]
  R6 = Resistor [tolerance=±5% resistance=1.5k package=THT]
  R7 = Resistor [tolerance=±5% resistance=100 package=THT]

nets:
  N1: ZVN2110A_placeholder.D, R7.Pin_0
  N2: ZVN2110A_placeholder.S, C1.1, R4.WIPER
  N3: ZVN2110A_placeholder.G, R6.Pin_1
  N4: R1.Pin_1, R2.Pin_0, C1.0
  N5: R4.CCW, R5.Pin_1
  N6: R4.CW, R6.Pin_0
  N7: R5.Pin_0, R7.Pin_1
