# Fritzing sketch selfbiased_config_bb (saved by Fritzing 0.9.3b)
breadboards: 1

parts:
  ZVN2110A_placeholder = MOSFET-NCHANNEL [package=to-92]
  R1 = Resistor [tolerance=±5% resistance=220 package=THT]
  R2 = Resistor [tolerance=±5% resistance=220 package=THT]
  C1 = Ceramic Capacitor [capacitance=100nF package="100 mil [THT, multilayer]"]
  R5 = Resistor [tolerance=±5% resistance=220 package=THT]
  R6 = Resistor [tolerance=±5% resistance=220 package=THT]
  R7 = Resistor [tolerance=±5% resistance=220 package=THT]

nets:
  N1: ZVN2110A_placeholder.D, R5.Pin_1, R7.Pin_0
  N2: ZVN2110A_placeholder.S, C1.1, R5.Pin_0, R6.Pin_0
  N3: ZVN2110A_placeholder.G, R2.Pin_1, R6.Pin_1
  N4: R1.Pin_1, R2.Pin_0, C1.0
