# Fritzing sketch ad5626_bipolar_bb (saved by Fritzing 0.9.3b)
breadboards: 1

parts:
  C2 = Ceramic Capacitor [capacitance=100nF package="100 mil [THT, multilayer]"]
  R2 = Resistor [tolerance=±5% resistance=10k package="0402 [SMD]"]
  R3 = Resistor [tolerance=±5% resistance=20k package="0402 [SMD]"]
  R4 = Resistor [tolerance=±5% resistance=470k package="0402 [SMD]"]
  R5 = Resistor [tolerance=±5% resistance=47k package="0402 [SMD]"]
  R6 = Resistor [tolerance=±5% resistance=220 package="0402 [SMD]"]
  R7 = Resistor [tolerance=±5% resistance=10k package="0402 [SMD]"]
  IC2 = SO08 [chip_label=AD5626 package=SO]
  IC3 = IC, DIP package, 14 pins [chip_label=OP484]

nets:
  N1: C2.0, R6.Pin_0, IC2.7
  N2: C2.1, IC2.1, IC3.pin4
  N3: R2.Pin_0, R3.Pin_0, IC3.pin6
  N4: R3.Pin_1, IC3.pin7
  N5: R4.Pin_0, R5.Pin_0, R6.Pin_1
  N6: R4.Pin_1, R5.Pin_1, R7.Pin_1, IC3.pin5
  N7: R7.Pin_0, IC2.8

notes:
  DIO2
  DIO4
  DIO0
  GND
  1+
  Vp
  DIO3
  DIO1
  1-
  0.1 uF
  2-
  2+
  Vn
  10kΩ
  20kΩ
  47kΩ
  470kΩ
  1kΩ
  W1
