# Fritzing sketch ad5626_unipolar_bb (saved by Fritzing 0.9.3b)
breadboards: 1

parts:
  C1 = Electrolytic Capacitor [capacitance=10μF package="0605 [SMD, electrolytic]"]
  C2 = Ceramic Capacitor [capacitance=100nF package="100 mil [THT, multilayer]"]
  R1 = Resistor [tolerance=±5% resistance=2.2k package=THT]
  C3 = Ceramic Capacitor [capacitance=100nF package="100 mil [THT, multilayer]"]
  IC1 = SO08 [chip_label=AD5626 package=SO]

nets:
  N1: C1.-, C2.0, R1.Pin_0, C3.0, IC1.7
  N2: C1.+, C2.1, IC1.1
  N3: R1.Pin_1, C3.1, IC1.8

notes:
  DIO2
  DIO4
  DIO0
  GND
  1+
  0.1 uF
  10 uF
  Vp
  DIO3
  DIO1
  1-
  0.001 uF
  2.2kΩ
