# Fritzing sketch r_2r_ladder-bb (saved by Fritzing 0.9.3b)
breadboards: 1

parts:
  U1 = OP27 - Low Noise, Precision Op Amp [part_number=OP27]
  R1 = Resistor [tolerance=±5% resistance=10k package=THT]
  R2 = Resistor [tolerance=±5% resistance=10k package=THT]
  R3 = Resistor [tolerance=±5% resistance=20k package=THT]
  R4 = Resistor [tolerance=±5% resistance=20k package=THT]
  R5 = Resistor [tolerance=±5% resistance=20k package=THT]
  R6 = Resistor [tolerance=±5% resistance=20k package=THT]
  R7 = Resistor [tolerance=±5% resistance=20k package=THT]
  R8 = Resistor [tolerance=±5% resistance=20k package=THT]
  R9 = Resistor [tolerance=±5% resistance=20k package=THT]
  R10 = Resistor [tolerance=±5% resistance=20k package=THT]
  R11 = Resistor [tolerance=±5% resistance=20k package=THT]
  R12 = Resistor [tolerance=±5% resistance=10k package=THT]
  R13 = Resistor [tolerance=±5% resistance=10k package=THT]
  R18 = Resistor [tolerance=±5% resistance=10k package=THT]
  R19 = Resistor [tolerance=±5% resistance=10k package=THT]
  R20 = Resistor [tolerance=±5% resistance=10k package=THT]
  R21 = Resistor [tolerance=±5% resistance=10k package=THT]
  R22 = Resistor [tolerance=±5% resistance=10k package=THT]

nets:
  N1: U1.-IN, R1.Pin_1, R2.Pin_0
  N2: U1.+IN, R3.Pin_1, R12.Pin_0
  N3: U1.OUT, R2.Pin_1
  N4: R4.Pin_1, R12.Pin_1, R13.Pin_0
  N5: R5.Pin_1, R13.Pin_1, R18.Pin_0
  N6: R6.Pin_1, R18.Pin_1, R21.Pin_0
  N7: R7.Pin_1, R19.Pin_0, R21.Pin_1
  N8: R8.Pin_1, R19.Pin_1, R22.Pin_0
  N9: R9.Pin_1, R20.Pin_0, R22.Pin_1
  N10: R10.Pin_1, R11.Pin_1, R20.Pin_1

notes:
  1-
  1+
  2-
  2+
  W1
  Vn
  GND
  Vp
  D7
  D6
  D5
  D4
  D3
  D2
  D1
  D0
