# Fritzing sketch diff_temp-bb (saved by Fritzing 0.9.3b)
breadboards: 1

parts:
  R1 = Resistor [tolerance=±5% resistance=1k package=THT]
  R2 = Resistor [tolerance=±5% resistance=1k package=THT]
  D1 = Diode [part_number=1N914 package=diode-1n4148]
  D2 = Diode [part_number=1N914 package=diode-1n4148]

nets:
  N1: R1.Pin_0, R2.Pin_0
  N2: D1.C, D2.C

notes:
  1-
  1+
  GND
  Vp
