# Fritzing sketch diff_pair_triangle_sine_conv-bb (saved by Fritzing 0.9.3b)
breadboards: 1

parts:
  U1 = OP27 - Low Noise, Precision Op Amp [part_number=OP27]
  100pF = Ceramic Capacitor [capacitance=10pF package="100 mil [THT, multilayer]"]
  R1 = Resistor [tolerance=±5% resistance=4.7k package=THT]
  R2 = Resistor [tolerance=±5% resistance=4.7k package=THT]
  R3 = Resistor [tolerance=±5% resistance=2.2k package=THT]
  R4 = Resistor [tolerance=±5% resistance=220 package=THT]
  R5 = Resistor [tolerance=±5% resistance=4.7k package=THT]
  U2 = SSM2212 - Audio Dual Matched NPN Transistor [part_number=SSM2212]
  U2_1 = AnalogDevices_SSM2212RZ_subpart1 [part_number=SSM2212]  # not connected
  U2_3 = AnalogDevices_SSM2212RZ_subpart3 [part_number=SSM2212]  # not connected
  R6 = Resistor [tolerance=±5% resistance=4.7k package=THT]
  R7 = Resistor [tolerance=±5% resistance=220 package=THT]
  R8 = Resistor [tolerance=±5% resistance=390 package=THT]
  trimpot_-_500Ω = TRIMPOT [package=3386u]
  R10 = Resistor [tolerance=±5% resistance=10k package=THT]

nets:
  N1: U1.-IN, 100pF.1, R1.Pin_1, R5.Pin_1, U2.connector8
  N2: U1.+IN, R2.Pin_0, U2.connector1, R6.Pin_1
  N3: U1.-V, R10.Pin_1
  N4: U1.OUT, 100pF.0, R1.Pin_0
  N5: U1.V+, R5.Pin_0, R6.Pin_0
  N6: R2.Pin_1, R4.Pin_1, R7.Pin_0
  N7: R3.Pin_1, R4.Pin_0, U2.connector7
  N8: U2.connector2, R7.Pin_1
  N9: U2.connector3, R8.Pin_1, trimpot_-_500Ω.WIPER, trimpot_-_500Ω.CW, R10.Pin_0
  N10: U2.connector6, R8.Pin_0, trimpot_-_500Ω.CCW

notes:
  1-
  1+
  2-
  2+
  W1
  Vn
  GND
  Vp
