# Fritzing sketch triangle_wave_gen-bb (saved by Fritzing 0.9.3b)
breadboards: 1

parts:
  LED1 = LED - 5mm [color="Red (633nm)" package="5 mm [THT]"]
  Q1 = NPN-Transistor [part_number=2N3904 package="TO92 [THT]"]
  trimpot_-_500Ω = TRIMPOT [package=3386u]
  R1 = Resistor [tolerance=±5% resistance=220 package=THT]
  100pF1 = Ceramic Capacitor [capacitance=1µF package="100 mil [THT, multilayer]"]
  R2 = Resistor [tolerance=±5% resistance=6.8k package=THT]
  U1 = AD654 - Low Cost Monolithic Voltage-to-Frequency Converter [part_number=AD654]
  R3 = Resistor [tolerance=±5% resistance=1k package=THT]
  R4 = Resistor [tolerance=±5% resistance=1k package=THT]
  0_01uF = Ceramic Capacitor [package="100 mil [THT, multilayer]"]
  U2 = AD8226 - Rail-to-Rail output Instrumentation Amplifier [part_number=AD8226]
  R5 = Resistor [tolerance=±5% resistance=47k package=THT]

nets:
  N1: LED1.cathode, R1.Pin_1, 100pF1.0, U1.5V, U1.STROBE, R4.Pin_0, U2.-VS
  N2: LED1.anode, Q1.B, R2.Pin_0
  N3: Q1.E, trimpot_-_500Ω.CCW
  N4: Q1.C, R2.Pin_1, U1.V+, R3.Pin_0, U2.+VS
  N5: trimpot_-_500Ω.WIPER, trimpot_-_500Ω.CW, R1.Pin_0, 100pF1.1, U1.COMMON
  N6: U1.10V, R3.Pin_1
  N7: U1.2p5V, R4.Pin_1
  N8: U1.VBG, 0_01uF.1, U2.-IN
  N9: U1.CAP, 0_01uF.0, U2.+IN
  N10: U2.RG#2, R5.Pin_0
  N11: U2.RG#3, R5.Pin_1

notes:
  1-
  1+
  GND
  Vp
  to sine wave generator
