# Fritzing sketch simplified_ring_mod_bb (saved by Fritzing 0.9.3b)
breadboards: 1

parts:
  D1 = Rectifier Diode [part_number=1N914 package="300 mil [THT]"]
  D2 = Rectifier Diode [part_number=1N914 package="300 mil [THT]"]
  D3 = Rectifier Diode [part_number=1N914 package="300 mil [THT]"]
  D4 = Rectifier Diode [part_number=1N914 package="300 mil [THT]"]
  R1 = Resistor [tolerance=±5% resistance=100 package=THT]
  R2 = Resistor [tolerance=±5% resistance=100 package=THT]
  R3 = Resistor [tolerance=±5% resistance=100 package=THT]
  R4 = Resistor [tolerance=±5% resistance=100 package=THT]

nets:
  N1: D1.cathode, D2.anode, R4.Pin_0
  N2: D1.anode, D4.cathode, R1.Pin_1
  N3: D2.cathode, D3.anode, R2.Pin_0
  N4: D3.cathode, D4.anode, R3.Pin_1
  N5: R3.Pin_0, R4.Pin_1

notes:
  W2
  1-
  W1
  1+
  GND
