# Fritzing sketch abs_val2_bb (saved by Fritzing 0.9.3b)
breadboards: 1

parts:
  U1 = ADTL082 - Dual JFET Input Op Amps [part_number=ADTL082]
  U1_1 = AnalogDevices_ADTL082ARZ_subpart1 [part_number=ADTL082]  # not connected
  U1_2 = AnalogDevices_ADTL082ARZ_subpart2 [part_number=ADTL082]  # not connected
  R1 = Resistor [tolerance=±5% resistance=10k package=THT]
  R2 = Resistor [tolerance=±5% resistance=10k package=THT]
  R3 = Resistor [tolerance=±5% resistance=10k package=THT]
  R4 = Resistor [tolerance=±5% resistance=10k package=THT]
  D1 = Rectifier Diode [part_number=1N914 package="300 mil [THT]"]
  D2 = Rectifier Diode [part_number=1N914 package="300 mil [THT]"]
  C1 = Electrolytic Capacitor [capacitance=4.7µF package="100 mil [THT, electrolytic]"]
  R5 = Resistor [tolerance=±5% resistance=10k package=THT]
  C2 = Electrolytic Capacitor [capacitance=4.7µF package="100 mil [THT, electrolytic]"]

nets:
  N1: U1.connector1, D1.cathode, D2.anode
  N2: U1.connector2, R1.Pin_1, R2.Pin_1, R4.Pin_0
  N3: U1.connector3, C2.+
  N4: U1.connector4, C2.-
  N5: U1.connector5, R4.Pin_1, D2.cathode
  N6: U1.connector6, R3.Pin_0, R5.Pin_0
  N7: U1.connector7, R5.Pin_1
  N8: U1.connector8, C1.+
  N9: R2.Pin_0, R3.Pin_1, D1.anode

notes:
  1+
  2+
  2-
  1-
  GND
  Vp
  W1
  Vn
