# Fritzing sketch bridge_rect_bb (saved by Fritzing 0.9.3b)
breadboards: 1

parts:
  R1 = Resistor [tolerance=±5% resistance=4.7k package=THT]
  1N914 = Rectifier Diode [part_number=1N4001 package="300 mil [THT]"]
  1N914_2 = Rectifier Diode [part_number=1N4001 package="300 mil [THT]"]
  1N914_3 = Rectifier Diode [part_number=1N4001 package="300 mil [THT]"]
  1N914_4 = Rectifier Diode [part_number=1N4001 package="300 mil [THT]"]

nets:
  N1: R1.Pin_0, 1N914.cathode, 1N914_4.cathode
  N2: R1.Pin_1, 1N914_2.anode, 1N914_3.anode
  N3: 1N914.anode, 1N914_2.cathode
  N4: 1N914_3.cathode, 1N914_4.anode

notes:
  2-
  1+
  W1
  2+
  1-
  GND
