# Fritzing sketch c_vs_v_diode_bb (saved by Fritzing 0.9.3b)
breadboards: 1

parts:
  R1 = Resistor [tolerance=±5% resistance=1k package=THT]
  1N914 = Rectifier Diode [part_number=1N4001 package="300 mil [THT]"]

nets:
  N1: R1.Pin_1, 1N914.anode

notes:
  W1
  2+
  2-
  1+
  GND
  1-
