# Fritzing sketch dc_restor_bb (saved by Fritzing 0.9.3b)
breadboards: 1

parts:
  1N914 = Rectifier Diode [part_number=1N4001 package="300 mil [THT]"]
  C1 = Ceramic Capacitor [capacitance=0.1µF package="100 mil [THT, multilayer]"]

nets:
  N1: 1N914.anode, C1.1

notes:
  W2
  W1
  1+
  2+
  1-
  2-
  GND
