# Fritzing sketch diode_clamp_bb (saved by Fritzing 0.9.3b)
breadboards: 1

parts:
  R1 = Resistor [tolerance=±5% resistance=10k package=THT]
  1N914 = Rectifier Diode [part_number=1N4001 package="300 mil [THT]"]
  1N914_2 = Rectifier Diode [part_number=1N4001 package="300 mil [THT]"]

nets:
  N1: R1.Pin_1, 1N914.anode, 1N914_2.cathode

notes:
  W2
  W1
  1+
  2+
  GND
  1-
  2-
