# Fritzing sketch doubler_bb (saved by Fritzing 0.9.3b)
breadboards: 1

parts:
  D1 = Rectifier Diode [part_number=1N914 package="300 mil [THT]"]
  D2 = Rectifier Diode [part_number=1N914 package="300 mil [THT]"]
  C1 = Electrolytic Capacitor [capacitance=10µF package="100 mil [THT, electrolytic]"]
  C2 = Electrolytic Capacitor [capacitance=1µF package="100 mil [THT, electrolytic]"]
  R1 = Resistor [tolerance=±5% resistance=10k package=THT]

nets:
  N1: D1.cathode, D2.anode, C2.-, R1.Pin_0
  N2: D1.anode, D2.cathode, C1.+
  N3: C2.+, R1.Pin_1

notes:
  2-
  1-
  GND
  W1
  1+
  2+
