# Fritzing sketch half_wave_bb (saved by Fritzing 0.9.3b)
breadboards: 1

parts:
  R1 = Resistor [tolerance=±5% resistance=4.7k package=THT]
  1N914 = Rectifier Diode [part_number=1N4001 package="300 mil [THT]"]

nets:
  N1: R1.Pin_0, 1N914.cathode

notes:
  W1
  1+
  2+
  1-
  2-
  GND
