# Fritzing sketch precision_half_wav_rect_bb (saved by Fritzing 0.9.3b)
breadboards: 1

parts:
  1N914 = Rectifier Diode [part_number=1N4001 package="300 mil [THT]"]
  D2 = Rectifier Diode [part_number=1N914 package="300 mil [THT]"]
  U4 = ADTL082 - Dual JFET Input Op Amps [part_number=ADTL082]
  U4_1 = AnalogDevices_ADTL082ARZ_subpart1 [part_number=ADTL082]  # not connected
  R1 = Resistor [tolerance=±5% resistance=10k package=THT]
  R2 = Resistor [tolerance=±5% resistance=10k package=THT]
  C1 = Electrolytic Capacitor [capacitance=4.7µF package="100 mil [THT, electrolytic]"]
  C2 = Electrolytic Capacitor [capacitance=4.7µF package="100 mil [THT, electrolytic]"]

nets:
  N1: 1N914.cathode, R2.Pin_0
  N2: 1N914.anode, D2.cathode, U4.connector1, R2.Pin_1
  N3: D2.anode, U4.connector2, R1.Pin_0
  N4: U4.connector3, C2.-
  N5: U4.connector4, C2.+
  N6: U4.connector8, C1.+

notes:
  2+
  2-
  1-
  GND
  Vp
  W1
  1+
  Vn
