# Fritzing sketch var_atten_bb (saved by Fritzing 0.9.3b)
breadboards: 1

parts:
  D2 = Rectifier Diode [part_number=1N4001 package="300 mil [THT]"]
  C1 = Ceramic Capacitor [capacitance=0.1µF package="100 mil [THT, multilayer]"]
  R1 = Resistor [tolerance=±5% resistance=10k package=THT]
  R2 = TRIMPOT [package=trim_pot_pth]
  R3 = Resistor [tolerance=±5% resistance=4.7k package=THT]
  R4 = Resistor [tolerance=±5% resistance=2.2k package=THT]
  C2 = Ceramic Capacitor [capacitance=0.1µF package="100 mil [THT, multilayer]"]

nets:
  N1: D2.cathode, R1.Pin_1, R2.CW
  N2: D2.anode, C1.0, R3.Pin_0, R4.Pin_1
  N3: C1.1, R1.Pin_0
  N4: R4.Pin_0, C2.1

notes:
  1+
  W1
  Vp
  2+
  GND
  2-
  1-
