# Fritzing sketch lt3080 (saved by Fritzing 0.9.3b)
breadboards: 1

parts:
  LM1 = Voltage Regulator - 3.3V [package=TO-220-5]
  R1 = Resistor [tolerance=±5% resistance=1M package="0805 [SMD]"]
  R2 = Resistor [tolerance=±5% resistance=1M package="0805 [SMD]"]
  R3 = Resistor [tolerance=±5% resistance=1M package="0805 [SMD]"]
  C5 = Ceramic Capacitor [capacitance=100nF package="100 mil [THT, multilayer]"]
  C6 = Ceramic Capacitor [capacitance=100nF package="100 mil [THT, multilayer]"]
  C7 = Ceramic Capacitor [capacitance=100nF package="100 mil [THT, multilayer]"]
  C8 = Ceramic Capacitor [capacitance=100nF package="100 mil [THT, multilayer]"]

nets:
  N1: LM1.+Vout, R1.Pin_1, R2.Pin_1, R3.Pin_1
  N2: LM1.GND, C6.0, C7.1
  N3: LM1.Feedback, LM1.ON/OFF, C5.0, C8.1
  N4: R1.Pin_0, R2.Pin_0, R3.Pin_0, C5.1, C6.1, C7.0, C8.0

notes:
  W1
  2+
  GND
  2-
  1MΩ
  0.1uF
  4.7uF
  LT3080
  RLOAD

custom parts:
  Voltage Regulator - 3.3V: 3.3V DC Voltage Regulator LM2575 TO-220-5
