# Fritzing sketch electret_audio_amplifier_bb (saved by Fritzing 0.9.3b)
breadboards: 1

parts:
  U2 = MIC [package=mic_electret_smd]
  R1 = Resistor [tolerance=±5% resistance=2.2k package="0805 [SMD]"]
  C1 = Electrolytic Capacitor [capacitance=47µF package="0605 [SMD, electrolytic]"]
  R2 = Resistor [tolerance=±5% resistance=20k package="0805 [SMD]"]
  R3 = Resistor [tolerance=±5% resistance=20k package="0805 [SMD]"]
  R4 = Resistor [tolerance=±5% resistance=1k package="0805 [SMD]"]
  R5 = Resistor [tolerance=±5% resistance=100 package="0805 [SMD]"]
  C2 = Electrolytic Capacitor [capacitance=10μF package="0605 [SMD, electrolytic]"]
  R6 = Resistor [tolerance=±5% resistance=47 package="0805 [SMD]"]
  U3 = TRANSISTOR_NPN_2 [package=to-92]
  R7 = Resistor [tolerance=±5% resistance=68 package="0805 [SMD]"]
  C3 = Electrolytic Capacitor [capacitance=4.7µF package="0605 [SMD, electrolytic]"]
  C4 = Electrolytic Capacitor [capacitance=10μF package="0605 [SMD, electrolytic]"]
  SPKR1 = Loudspeaker
  IC4 = IC, DIP package, 14 pins [chip_label=OP484]

nets:
  N1: U2.1, C1.-, R3.Pin_1, C2.-, R7.Pin_0, SPKR1.pin1, IC4.pin11
  N2: U2.2, R1.Pin_1, C3.+
  N3: R1.Pin_0, C1.+, R2.Pin_0, U3.E, IC4.pin4
  N4: R2.Pin_1, R3.Pin_0, C3.-, IC4.pin12
  N5: R4.Pin_0, U3.C, R7.Pin_1, C4.+
  N6: R4.Pin_1, R5.Pin_0, IC4.pin13
  N7: R5.Pin_1, C2.+
  N8: R6.Pin_0, U3.B
  N9: R6.Pin_1, IC4.pin14
  N10: C4.-, SPKR1.pin2

notes:
  Vp
  GND
  2.2kΩ
  20kΩ
  47Ω
  100Ω
  1kΩ
  68Ω
  4.7µF
  47µF
  220µF
