# Fritzing sketch electret_audio_amplifier_gain_testbb (saved by Fritzing 0.9.3b)
breadboards: 1

parts:
  C1 = Electrolytic Capacitor [capacitance=47µF package="0605 [SMD, electrolytic]"]
  R2 = Resistor [tolerance=±5% resistance=20k package="0805 [SMD]"]
  R3 = Resistor [tolerance=±5% resistance=20k package="0805 [SMD]"]
  R4 = Resistor [tolerance=±5% resistance=1k package="0805 [SMD]"]
  R5 = Resistor [tolerance=±5% resistance=100 package="0805 [SMD]"]
  C2 = Electrolytic Capacitor [capacitance=10μF package="0605 [SMD, electrolytic]"]
  R6 = Resistor [tolerance=±5% resistance=47 package="0805 [SMD]"]
  U3 = TRANSISTOR_NPN_2 [package=to-92]
  R7 = Resistor [tolerance=±5% resistance=68 package="0805 [SMD]"]
  IC3 = IC, DIP package, 14 pins [chip_label=OP484]

nets:
  N1: C1.-, R3.Pin_1, C2.-, R7.Pin_0, IC3.pin11
  N2: C1.+, R2.Pin_0, U3.E, IC3.pin4
  N3: R2.Pin_1, R3.Pin_0, IC3.pin12
  N4: R4.Pin_0, U3.C, R7.Pin_1
  N5: R4.Pin_1, R5.Pin_0, IC3.pin13
  N6: R5.Pin_1, C2.+
  N7: R6.Pin_0, U3.B
  N8: R6.Pin_1, IC3.pin14

notes:
  Vp
  GND
  20kΩ
  47Ω
  100Ω
  1kΩ
  68Ω
  47µF
  W1
  1+
  2+
  2-
  1-
