# Fritzing sketch bias_env_detector-bb (saved by Fritzing 0.9.3b)
breadboards: 1

parts:
  D1 = Rectifier Diode 10A [part_number=P1000K]
  Q1 = TRANSISTOR_NPN [package=to-92]
  R1 = Resistor [tolerance=±5% resistance=22k package=THT]
  R2 = Resistor [tolerance=±5% resistance=10k package=THT]
  C1 = Electrolytic Capacitor [capacitance=1µF package="100 mil [THT, electrolytic]"]
  C2 = Electrolytic Capacitor [capacitance=1µF package="100 mil [THT, electrolytic]"]
  R3 = Resistor [tolerance=±5% resistance=1.5k package=THT]

nets:
  N1: D1.cathode, Q1.B, C1.-
  N2: D1.anode, R1.Pin_0, R2.Pin_1
  N3: Q1.E, C2.+, R3.Pin_1
  N4: Q1.C, R1.Pin_1
  N5: R2.Pin_0, C2.-, R3.Pin_0

notes:
  1+
  W1
  Vp
  GND
  2-
  2+
  1-
  1.5kΩ
  20kΩ
  10kΩ
  2N3904
  1N914
  1µF
