# Fritzing sketch ext_env_detector-bb (saved by Fritzing 0.9.3b)
breadboards: 1

parts:
  C1 = Electrolytic Capacitor [capacitance=1µF package="100 mil [THT, electrolytic]"]
  R1 = Resistor [tolerance=±5% resistance=1k package="0402 [SMD]"]
  D1 = Rectifier Diode [part_number=1N4001 package="Melf DO-213 AB [SMD]"]
  C2 = Electrolytic Capacitor [capacitance=1µF package="100 mil [THT, electrolytic]"]
  R2 = Resistor [tolerance=±5% resistance=1k package="0402 [SMD]"]
  D2 = Rectifier Diode [part_number=1N4001 package="Melf DO-213 AB [SMD]"]

nets:
  N1: C1.-, R1.Pin_0, D1.cathode
  N2: C1.+, R1.Pin_1, C2.-, R2.Pin_1
  N3: D1.anode, D2.cathode
  N4: C2.+, R2.Pin_0, D2.anode

notes:
  1KΩ
  1N914
  1µF
  1+
  W1
  GND
  1-
  2+
  2-
