# Fritzing sketch float_curr_src_vn-bb (saved by Fritzing 0.9.3b)
breadboards: 1

parts:
  U1 = SSM2212 - Audio Dual Matched NPN Transistor [part_number=SSM2212]
  U1_1 = AnalogDevices_SSM2212RZ_subpart1 [part_number=SSM2212]  # not connected
  U1_3 = AnalogDevices_SSM2212RZ_subpart3 [part_number=SSM2212]  # not connected
  U2 = SSM2220 - Audio Dual Matched PNP Transistor [part_number=SSM2220]
  U2_1 = AnalogDevices_SSM2220S_subpart1 [part_number=SSM2220]  # not connected
  U2_3 = AnalogDevices_SSM2220S_subpart3 [part_number=SSM2220]  # not connected
  Q1 = TRANSISTOR_NPN [part_number=2N3904 package=to-92-ammo]
  Q6 = TRANSISTOR_PNP [part_number=2N3906 package=to-92]
  R1 = Resistor [tolerance=±5% resistance=100 package=THT]
  R2 = Trimmer Potentiometer [maximum_resistance=10kΩ package=THT]

nets:
  N1: U1.connector1, U1.connector2, U2.connector8, Q6.C
  N2: U1.connector3, R2.wiper, R2.leg2
  N3: U1.connector6, Q1.E, R2.leg1
  N4: U1.connector7, Q1.B
  N5: U1.connector8, U2.connector1, U2.connector2, U2.connector7, Q1.C, Q6.B
  N6: U2.connector3, U2.connector6, Q6.E, R1.Pin_0

notes:
  1-
  1+
  2-
  2+
  W1
  Vn
