# Fritzing sketch float_curr_src_vp-bb (saved by Fritzing 0.9.3b)
breadboards: 1

parts:
  U2_3 = AnalogDevices_SSM2212RZ_subpart3 [part_number=SSM2212]  # not connected
  U2 = SSM2212 - Audio Dual Matched NPN Transistor [part_number=SSM2212]
  U2_1 = AnalogDevices_SSM2212RZ_subpart1 [part_number=SSM2212]  # not connected
  U3_3 = AnalogDevices_SSM2220S_subpart3 [part_number=SSM2220]  # not connected
  U3 = SSM2220 - Audio Dual Matched PNP Transistor [part_number=SSM2220]
  U3_1 = AnalogDevices_SSM2220S_subpart1 [part_number=SSM2220]  # not connected
  Q5 = TRANSISTOR_NPN [part_number=2N3904 package=to-92-ammo]
  Q6 = TRANSISTOR_PNP [part_number=2N3906 package=to-92]
  R3 = Trimmer Potentiometer [maximum_resistance=10kΩ package=THT]
  R4 = Resistor [tolerance=±5% resistance=100 package=THT]

nets:
  N1: U2.connector1, U2.connector2, U2.connector7, U3.connector8, Q5.B, Q6.C
  N2: U2.connector3, R3.wiper, R3.leg2, R4.Pin_1
  N3: U2.connector6, Q5.E, R3.leg1
  N4: U2.connector8, U3.connector1, U3.connector2, U3.connector7, Q5.C, Q6.B
  N5: U3.connector3, U3.connector6, Q6.E

notes:
  1-
  1+
  2-
  2+
  W1
  Vp
