# Fritzing sketch freq_resp_bjt_bb (saved by Fritzing 0.9.3b)
breadboards: 1

parts:
  R1 = Resistor [tolerance=±5% resistance=470 package="0805 [SMD]"]
  R2 = Resistor [tolerance=±5% resistance=47 package="0805 [SMD]"]
  R3 = Resistor [tolerance=±5% resistance=68 package="0805 [SMD]"]
  R4 = Resistor [tolerance=±5% resistance=1.5k package="0805 [SMD]"]
  C1 = Ceramic Capacitor [capacitance="100 nF" package="1206 [SMD, multilayer]"]
  R5 = Resistor [tolerance=±5% resistance=4.7k package="0805 [SMD]"]
  Q1 = NPN-Transistor [package="TO92 [THT]"]
  C2 = Ceramic Capacitor [capacitance="100 nF" package="1206 [SMD, multilayer]"]
  C3 = Ceramic Capacitor [capacitance="100 nF" package="1206 [SMD, multilayer]"]
  R6 = Resistor [tolerance=±5% resistance=470 package="0805 [SMD]"]
  R7 = Resistor [tolerance=±5% resistance=1k package="0805 [SMD]"]
  C4 = Ceramic Capacitor [capacitance="100 nF" package="1206 [SMD, multilayer]"]
  R8 = Resistor [tolerance=±5% resistance=100 package="0805 [SMD]"]

nets:
  N1: R1.Pin_1, R2.Pin_0, R3.Pin_0
  N2: R2.Pin_1, C1.0
  N3: R3.Pin_1, R4.Pin_1
  N4: R4.Pin_0, C1.1, R5.Pin_0, Q1.B, C2.0
  N5: R5.Pin_1, R6.Pin_1
  N6: Q1.E, C4.0, R8.Pin_0
  N7: Q1.C, C2.1, C3.0, R6.Pin_0
  N8: C3.1, R7.Pin_0
  N9: R7.Pin_1, C4.1, R8.Pin_1

notes:
  2+
  Vp
  1+
  W1
  GND
  1-
  2-
  CB
  CF
  CC
  2N3904
  RE
  RB1
  RB2
  68Ω
  Rs
  470Ω
  CE
  RC
  RL
