# Fritzing sketch 3stage_amp-bb (saved by Fritzing 0.9.3b)
breadboards: 1

parts:
  C1 = Electrolytic Capacitor [capacitance=22µF package="100 mil [THT, electrolytic]"]
  R1 = Resistor [tolerance=±5% resistance=100k package=THT]
  Q1 = PNP-Transistor [part_number=2N3906 package="TO92 [THT]"]
  U1 = SSM2212 - Audio Dual Matched NPN Transistor [part_number=SSM2212]
  U1_1 = AnalogDevices_SSM2212RZ_subpart1 [part_number=SSM2212]  # not connected
  U1_3 = AnalogDevices_SSM2212RZ_subpart3 [part_number=SSM2212]  # not connected
  R2 = Resistor [tolerance=±5% resistance=1.5k package=THT]
  R3 = Resistor [tolerance=±5% resistance=10k package=THT]
  R4 = Resistor [tolerance=±5% resistance=6.8k package=THT]
  R5 = Resistor [tolerance=±5% resistance=47k package=THT]
  C2 = Electrolytic Capacitor [capacitance=1µF package="100 mil [THT, electrolytic]"]
  Q2 = NPN-Transistor [part_number=2N3904 package="TO92 [THT]"]
  C3 = Ceramic Capacitor [capacitance=47nF package="100 mil [THT, multilayer]"]
  R6 = Resistor [tolerance=±5% resistance=470k package=THT]
  R7 = Resistor [tolerance=±5% resistance=1k package=THT]
  R8 = Resistor [tolerance=±5% resistance=470k package=THT]
  C4 = Electrolytic Capacitor [capacitance=22µF package="100 mil [THT, electrolytic]"]
  R9 = Resistor [tolerance=±5% resistance=10k package=THT]

nets:
  N1: C1.-, R1.Pin_0
  N2: R1.Pin_1, U1.connector2, R8.Pin_0
  N3: Q1.E, U1.connector8, R4.Pin_0, R7.Pin_1
  N4: Q1.B, R3.Pin_0
  N5: Q1.C, Q2.B, C3.0, R6.Pin_0
  N6: U1.connector1, R2.Pin_1, R3.Pin_1
  N7: U1.connector3, U1.connector6, R5.Pin_0, C2.+
  N8: U1.connector7, R9.Pin_1
  N9: R2.Pin_0, R4.Pin_1
  N10: R5.Pin_1, C2.-, Q2.E, C3.1, R6.Pin_1
  N11: Q2.C, R7.Pin_0
  N12: R8.Pin_1, C4.+
  N13: C4.-, R9.Pin_0

notes:
  1-
  1+
  2-
  2+
  W1
  Vn
  GND
  Vp
