# Fritzing sketch amp_unity_gain-bb (saved by Fritzing 0.9.3b)
breadboards: 1

parts:
  U1 = SSM2220 - Audio Dual Matched PNP Transistor [part_number=SSM2220]
  U1_1 = AnalogDevices_SSM2220S_subpart1 [part_number=SSM2220]  # not connected
  U1_3 = AnalogDevices_SSM2220S_subpart3 [part_number=SSM2220]  # not connected
  U2 = SSM2212 - Audio Dual Matched NPN Transistor [part_number=SSM2212]
  U2_1 = AnalogDevices_SSM2212RZ_subpart1 [part_number=SSM2212]  # not connected
  U2_3 = AnalogDevices_SSM2212RZ_subpart3 [part_number=SSM2212]  # not connected
  Q1 = NPN-Transistor [part_number=2N3904 package="TO92 [THT]"]
  Q2 = NPN-Transistor [part_number=2N3904 package="TO92 [THT]"]
  Q3 = NPN-Transistor [part_number=2N3904 package="TO92 [THT]"]
  Q4 = npn-Powertransistor [part_number=TIP31C package="TO220 [THT]"]
  R1 = Resistor [tolerance=±5% resistance=10k package=THT]
  R2 = Resistor [tolerance=±5% resistance=4.7k package=THT]

nets:
  N1: U1.connector1, U1.connector2, U1.connector7, U2.connector1
  N2: U1.connector3, U1.connector6, Q1.C
  N3: U1.connector8, U2.connector8, Q1.B
  N4: U2.connector3, U2.connector6, Q3.C
  N5: U2.connector7, Q1.E, Q2.C
  N6: Q2.E, Q3.E, Q4.emitter
  N7: Q2.B, Q3.B, Q4.base, Q4.collector, R1.Pin_0
  N8: R1.Pin_1, R2.Pin_0

notes:
  1-
  1+
  2-
  2+
  W1
  Vn
  GND
  Vp
