# Fritzing sketch hartley_osc-bb (saved by Fritzing 0.9.3b)
breadboards: 1

parts:
  R1 = Resistor [tolerance=±5% resistance=1k package=THT]
  R2 = Resistor [tolerance=±5% resistance=10k package=THT]
  Q1 = TRANSISTOR_NPN [package=to-92]
  L1 = Inductors [package=cr54]
  L2 = Inductors [package=cr54]
  C2 = Capacitor [package=cap-pth-small2]
  R3 = Resistor [tolerance=±5% resistance=100 package=THT]
  C3 = Capacitor [package=cap-pth-small2]
  C4 = Capacitor [package=cap-pth-small2]
  C5 = Capacitor [package=cap-pth-small2]

nets:
  N1: R1.Pin_0, R3.Pin_0, C3.1
  N2: R1.Pin_1, R2.Pin_0, Q1.B, C2.1, C3.2
  N3: R2.Pin_1, L2.2, C4.2
  N4: Q1.E, R3.Pin_1
  N5: Q1.C, L1.2, C4.1, C5.1
  N6: L1.1, L2.1, C2.2

notes:
  1-
  GND
  Vn
  Vp
  1+
  0.1uF
  0.01uF
  4.7nF
  2N3904
  10uH
  100uH
  1kΩ
  100Ω
  10kΩ
