# Fritzing sketch heartbeat_bb (saved by Fritzing 0.9.3b)
breadboards: 1

parts:
  U1 = OP482 - Low Power, High Speed JFET Quad Operational Amplifier [part_number=OP482]
  LED1 = LED - 5mm [color="Infrared (940nm)" package="5 mm [THT]"]
  LED2 = LED - 5mm [color="Blue (430nm)" package="5 mm [THT]"]
  R1 = Resistor [tolerance=±5% resistance=1k package=THT]
  R2 = Resistor [tolerance=±5% resistance=470 package=THT]
  R3 = Resistor [tolerance=±5% resistance=10k package=THT]
  R4 = Resistor [tolerance=±5% resistance=47k package=THT]
  C2 = Electrolytic Capacitor [capacitance=1µF package="100 mil [THT, electrolytic]"]
  R5 = Resistor [tolerance=±5% resistance=100 package=THT]
  C1 = Capacitor Polarized [package=cpol-radial-100uf-25v]
  C3 = Electrolytic Capacitor [capacitance=1µF package="100 mil [THT, electrolytic]"]
  R6 = Resistor [tolerance=±5% resistance=47k package=THT]

nets:
  N1: U1.OUTA, R3.Pin_0, R4.Pin_0
  N2: U1.-INA, R3.Pin_1, C1.+
  N3: U1.+INA, U1.+INC, LED1.cathode, LED2.cathode, C2.-
  N4: U1.V+, R1.Pin_0, R2.Pin_0
  N5: U1.+INB, R4.Pin_1, C2.+
  N6: U1.-INB, U1.OUTB, R5.Pin_0
  N7: U1.OUTC, C3.+, R6.Pin_0
  N8: U1.-INC, R5.Pin_1, C3.-, R6.Pin_1
  N9: LED1.anode, R1.Pin_1, C1.-
  N10: LED2.anode, R2.Pin_1

notes:
  Vp
  1+
  1-
  GND
  Vn
  470Ω
  1kΩ
  IR LED
  Photo-Tr
  47uF
  10kΩ
  47kΩ
  1uF
  100Ω
