# Fritzing sketch inductor_test_circuit-bb (saved by Fritzing 0.9.3b)
breadboards: 1

parts:
  L1 = Inductors [package=cr54]
  R1 = Resistor [tolerance=±5% resistance=200 package=THT]
  R2 = Resistor [tolerance=±5% resistance=200 package=THT]

nets:
  N1: L1.1, R2.Pin_0
  N2: L1.2, R1.Pin_1

notes:
  1-
  1+
  2-
  2+
  W1
  GND
