# Fritzing sketch led_single_emitter-bb (saved by Fritzing 0.9.3b)
breadboards: 1

parts:
  LED = LED - 5mm [color="Red (633nm)" package="5 mm [THT]"]
  Q1 = NPN-Transistor [part_number=2N3904 package="TO92 [THT]"]
  R1 = Resistor [tolerance=±5% resistance=100k package=THT]

nets:
  N1: LED.cathode, R1.Pin_0
  N2: LED.anode, Q1.B
  N3: Q1.C, R1.Pin_1

notes:
  1-
  1+
  GND
  Vp
