# Fritzing sketch loop_gain-bb (saved by Fritzing 0.9.3b)
breadboards: 1

parts:
  U1 = Transformer [package=transformer_smd]
  U2 = OP37 - Low Noise, Precision, High Speed Op Amp [part_number=OP37]
  R1 = Resistor [tolerance=±5% resistance=1k package="2010 [SMD]"]
  R2 = Resistor [tolerance=±5% resistance=1k package="2010 [SMD]"]
  R3 = Resistor [tolerance=±5% resistance=10 package="2010 [SMD]"]
  R4 = Resistor [tolerance=±5% resistance=10 package="2010 [SMD]"]
  R5 = Resistor [tolerance=±5% resistance=100 package="2010 [SMD]"]

nets:
  N1: U1.1, R2.Pin_1, R3.Pin_0
  N2: U1.2, R4.Pin_0, R5.Pin_0
  N3: U1.3, R1.Pin_0, R4.Pin_1
  N4: U1.4, U2.OUT, R3.Pin_1
  N5: U2.-IN, R1.Pin_1, R2.Pin_0

notes:
  GND
  1-
  2-
  1+
  Vp
  2+
  W1
  Vn
  1kΩ
  10Ω
  100Ω
  HPH1-1400L
