# Fritzing sketch loudspeaker_imp_bb (saved by Fritzing 0.9.3b)
breadboards: 1

parts:
  SP1 = SPEAKER [package=pcb_mount_speaker]
  R2 = Resistor [tolerance=±5% resistance=100 package="0402 [SMD]"]

nets:
  N1: SP1.-, R2.Pin_0

notes:
  100Ω
  GND
  1-
  2-
  1+
  W1
  2+
