# Fritzing sketch rc_lpf_bb (saved by Fritzing 0.9.3b)
breadboards: 1

parts:
  R2 = Resistor [tolerance=±5% resistance=1k package="2010 [SMD]"]
  C2 = Electrolytic Capacitor [capacitance=1μF package="0405 [SMD, electrolytic]"]

nets:
  N1: R2.Pin_1, C2.+

notes:
  1μF
  1kΩ
  W1
  GND
  1+
  1-
  2-
  2+
