# Fritzing sketch rl_hpf_bb (saved by Fritzing 0.9.3b)
breadboards: 1

parts:
  R2 = Resistor [tolerance=±5% resistance=1k package="2010 [SMD]"]
  L2 = Inductors [package=cr54]

nets:
  N1: R2.Pin_1, L2.2

notes:
  1kΩ
  W1
  GND
  1+
  1-
  2-
  2+
  10 mH
