# Fritzing sketch ad22151_sensor_bb (saved by Fritzing 0.9.3b)
breadboards: 1

parts:
  R1 = Resistor [tolerance=±5% resistance=100 package=THT]
  R4 = Resistor [tolerance=±5% resistance=100 package=THT]
  R5 = Resistor [tolerance=±5% resistance=100 package=THT]
  U1 = AD22151 - Linear Output Magnetic Field Sensor [part_number=AD22151]
  C1 = Ceramic Capacitor [capacitance=0.1µF package="100 mil [THT, multilayer]"]
  R6 = Resistor [tolerance=±5% resistance=470 package=THT]
  R7 = Resistor [tolerance=±5% resistance=470 package=THT]
  C2 = Electrolytic Capacitor [capacitance=10µF package="100 mil [THT, electrolytic]"]
  R8 = Resistor [tolerance=±5% resistance=100k package=THT]
  L1 = Inductors [package=cr54-kit]

nets:
  N1: R1.Pin_0, R4.Pin_0, R5.Pin_0
  N2: R1.Pin_1, R4.Pin_1, R5.Pin_1
  N3: U1.TC2, U1.TC3
  N4: U1.GND, C2.-, L1.1
  N5: U1.OUTPUT, C1.1, R8.Pin_1
  N6: U1.GAIN, C1.0, R6.Pin_1, R7.Pin_1, R8.Pin_0
  N7: U1.REF, R6.Pin_0, R7.Pin_0
  N8: U1.VCC, C2.+

notes:
  W1
  GND
  V+
  100Ω
  100 uH
  10 uF
  470Ω
  100 kΩ
  200 kΩ
  0.1 uF
  AD22151
  1+
  1-
