# Fritzing sketch nmos_simple_current_mirror-bb (saved by Fritzing 0.9.3b)
breadboards: 1

parts:
  R1 = Resistor [tolerance=±5% resistance=1k package="0603 [SMD]"]
  R2 = Resistor [tolerance=±5% resistance=1k package="0603 [SMD]"]
  Q1 = TRANSISTOR_NPN [part_number=ZVN3310A package=to-92]
  Q2 = TRANSISTOR_NPN [part_number=ZVN3310A package=to-92]

nets:
  N1: R1.Pin_1, Q1.E, Q1.B, Q2.B, Q2.C
  N2: R2.Pin_1, Q2.E

notes:
  W2
  1-
  1+
  2-
  2+
  W1
  GND
