# Fritzing sketch common_mode_gain_mos-bb (saved by Fritzing 0.9.3b)
breadboards: 1

parts:
  Q2 = TRANSISTOR_NPN [part_number=ZVN2110A package=to-92]
  R1 = Resistor [tolerance=±5% resistance=10k package=THT]
  R2 = Resistor [tolerance=±5% resistance=10k package=THT]
  Q3 = TRANSISTOR_NPN [part_number=ZVN2110A package=to-92]
  R3 = Resistor [tolerance=±5% resistance=4.7k package=THT]
  R4 = Resistor [tolerance=±5% resistance=10k package=THT]

nets:
  N1: Q2.E, R1.Pin_1, Q3.E
  N2: Q2.B, Q3.B
  N3: Q2.C, R2.Pin_0
  N4: R1.Pin_0, R3.Pin_1
  N5: R2.Pin_1, R4.Pin_1
  N6: Q3.C, R4.Pin_0

notes:
  Vn
  1-
  1+
  2-
  2+
  W1
  GND
  Vp
