# Fritzing sketch diff_pair_tail_cs_mos-bb (saved by Fritzing 0.9.3b)
breadboards: 1

parts:
  0_1uF = Capacitor [package=cap-pth-small2]
  R1 = Resistor [tolerance=±5% resistance=1k package=THT]
  R2 = Resistor [tolerance=±5% resistance=100 package=THT]
  0_1uF_2 = Capacitor [package=cap-pth-small2]
  R3 = Resistor [tolerance=±5% resistance=1k package=THT]
  R4 = Resistor [tolerance=±5% resistance=100 package=THT]
  R5 = Resistor [tolerance=±5% resistance=4.7k package=THT]
  Q3 = TRANSISTOR_NPN [part_number=ZVN2110A package=to-92-ammo]
  Q4 = TRANSISTOR_NPN [part_number=ZVN2110A package=to-92-ammo]
  Q5 = TRANSISTOR_NPN [part_number=ZVN2110A package=to-92-ammo]
  R6 = Resistor [tolerance=±5% resistance=10k package=THT]
  Q6 = TRANSISTOR_NPN [part_number=2N3904 package=to-92-ammo]
  R7 = Resistor [tolerance=±5% resistance=10k package=THT]
  R8 = Resistor [tolerance=±5% resistance=10k package=THT]

nets:
  N1: 0_1uF.1, R1.Pin_1, R2.Pin_0, Q5.B
  N2: 0_1uF.2, R2.Pin_1, 0_1uF_2.1, R4.Pin_1, R5.Pin_0
  N3: 0_1uF_2.2, R3.Pin_1, R4.Pin_0, Q6.B
  N4: R5.Pin_1, R6.Pin_0
  N5: Q3.E, Q4.E
  N6: Q3.B, Q3.C, Q4.B, R6.Pin_1
  N7: Q4.C, Q5.E, Q6.E
  N8: Q5.C, R7.Pin_0
  N9: Q6.C, R8.Pin_0
  N10: R7.Pin_1, R8.Pin_1

notes:
  W2
  1-
  1+
  2-
  2+
  W1
  Vn
  GND
  Vp
