# Fritzing sketch diff_pair_tail_res_mos-bb (saved by Fritzing 0.9.3b)
breadboards: 1

parts:
  0_1uF = Capacitor [package=cap-pth-small2]
  R1 = Resistor [tolerance=±5% resistance=1k package=THT]
  R2 = Resistor [tolerance=±5% resistance=100 package=THT]
  R3 = Resistor [tolerance=±5% resistance=1k package=THT]
  R4 = Resistor [tolerance=±5% resistance=100 package=THT]
  Q3 = TRANSISTOR_NPN [part_number=ZVN2110A package=to-92-ammo]
  R5 = Resistor [tolerance=±5% resistance=10k package=THT]
  R6 = Resistor [tolerance=±5% resistance=10k package=THT]
  R7 = Resistor [tolerance=±5% resistance=10k package=THT]
  R8 = Resistor [tolerance=±5% resistance=4.7k package=THT]
  Q4 = TRANSISTOR_NPN [part_number=ZVN2110A package=to-92-ammo]
  0_1uF_2 = Capacitor [package=cap-pth-small2]

nets:
  N1: 0_1uF.1, R1.Pin_1, R2.Pin_0, Q3.B
  N2: 0_1uF.2, R2.Pin_1, R4.Pin_1, 0_1uF_2.1
  N3: R3.Pin_1, R4.Pin_0, Q4.B, 0_1uF_2.2
  N4: Q3.E, R5.Pin_1, Q4.E
  N5: Q3.C, R6.Pin_0
  N6: R5.Pin_0, R8.Pin_1
  N7: R6.Pin_1, R7.Pin_1
  N8: R7.Pin_0, Q4.C

notes:
  W2
  1-
  1+
  2-
  2+
  W1
  Vn
  GND
  Vp
