# Fritzing sketch nmos_diode_bb (saved by Fritzing 0.9.3b)
breadboards: 1

parts:
  R1 = Resistor [tolerance=±5% resistance=100 package=THT]
  IC1 = IC, DIP package, 14 pins [chip_label=CD4007UBE]

nets:
  N1: R1.Pin_0, IC1.pin6, IC1.pin8

notes:
  GND
  1-
  1+
  2-
  W1
  2+
  Vn
