# Fritzing sketch pmos_diode_bb (saved by Fritzing 0.9.3b)
breadboards: 1

parts:
  R1 = Resistor [tolerance=±5% resistance=100 package=THT]
  Q1 = MOSFET-NCHANNEL [package=to-92]

nets:
  N1: R1.Pin_0, Q1.S, Q1.G

notes:
  1-
  1+
  2-
  W1
  2+
  Vp
  ZVP2110A
