# Fritzing sketch imp_mos_src_flw-bb (saved by Fritzing 0.9.3b)
breadboards: 1

parts:
  IC1 = IC, DIP package, 14 pins [chip_label=CD4007]
  R1 = Resistor [tolerance=±5% resistance=2.2k package=THT]
  R2 = Resistor [tolerance=±5% resistance=1k package=THT]
  Q1 = NPN-Transistor [part_number=ZVN2110A package="TO92 [THT]"]

nets:
  N1: IC1.pin3, IC1.pin6, IC1.pin8, R1.Pin_0
  N2: IC1.pin4, IC1.pin7
  N3: IC1.pin5, Q1.E
  N4: R1.Pin_1, R2.Pin_0

notes:
  1-
  1+
  2-
  Vn
  2+
  W1
  GND
  Vp
