# Fritzing sketch mos_src_flw-bb (saved by Fritzing 0.9.3b)
breadboards: 1

parts:
  Q1 = NPN-Transistor [part_number=ZVN2110A package="TO92 [THT]"]
  R1 = Resistor [tolerance=±5% resistance=2.2k package=THT]

nets:
  N1: Q1.E, R1.Pin_1

notes:
  1-
  1+
  2-
  2+
  W1
  GND
  Vp
  Vn
