# Fritzing sketch nmos_stabilized_cs-bb (saved by Fritzing 0.9.3b)
breadboards: 1

parts:
  ZVN2210A = NPN-Transistor [package="TO92 [THT]"]
  ZVN2210A_2 = NPN-Transistor [package="TO92 [THT]"]
  R1 = Resistor [tolerance=±5% resistance=100 package=THT]
  R2 = Resistor [tolerance=±5% resistance=68 package=THT]
  R3 = Resistor [tolerance=±5% resistance=2.2k package=THT]
  R4 = Resistor [tolerance=±5% resistance=4.7k package=THT]

nets:
  N1: ZVN2210A.E, ZVN2210A_2.E
  N2: ZVN2210A.B, ZVN2210A_2.B, R2.Pin_1, R3.Pin_0
  N3: ZVN2210A.C, R1.Pin_0
  N4: ZVN2210A_2.C, R4.Pin_0
  N5: R1.Pin_1, R2.Pin_0

notes:
  GND
  2-
  1-
  W1
  1+
  2+
  Vp
