# Fritzing sketch nmos_zero_gain-bb (saved by Fritzing 0.9.3b)
breadboards: 1

parts:
  Q1 = NPN-Transistor [part_number=ZVN2110A package="TO92 [THT]"]
  R1 = Resistor [tolerance=±5% resistance=100 package=THT]
  R2 = Resistor [tolerance=±5% resistance=68 package=THT]
  R3 = Resistor [tolerance=±5% resistance=2.2k package=THT]

nets:
  N1: Q1.B, R2.Pin_1, R3.Pin_0
  N2: Q1.C, R1.Pin_0
  N3: R1.Pin_1, R2.Pin_0

notes:
  1-
  1+
  2+
  W1
  GND
  2-
