# Fritzing sketch led_volt_reg-bb (saved by Fritzing 0.9.3b)
breadboards: 1

parts:
  U1 = OP482 - Low Power, High Speed JFET Quad Operational Amplifier [part_number=OP482]
  0_01uF = Ceramic Capacitor [capacitance=100nF package="100 mil [THT, multilayer]"]
  LED(a) = LED - 5mm [color="Green (555nm)" package="5 mm [THT]"]
  R1 = Resistor [tolerance=±5% resistance=4.7k package=THT]
  R2 = Resistor [tolerance=±5% resistance=20k package=THT]
  R3 = Resistor [tolerance=±5% resistance=20k package=THT]
  LED(b) = LED - 5mm [color="Green (555nm)" package="5 mm [THT]"]
  0_01uF_2 = Ceramic Capacitor [capacitance=100nF package="100 mil [THT, multilayer]"]
  R4 = Resistor [tolerance=±5% resistance=1.5k package=THT]
  R5 = Resistor [tolerance=±5% resistance=1.5k package=THT]

nets:
  N1: U1.V+, R1.Pin_0, R5.Pin_0
  N2: U1.OUTC, R2.Pin_1
  N3: U1.-INC, R2.Pin_0, R3.Pin_1
  N4: U1.+INC, U1.+IND, LED(a).cathode, 0_01uF_2.1
  N5: U1.-IND, 0_01uF.0, R1.Pin_1, LED(b).anode
  N6: U1.OUTD, 0_01uF.1, LED(b).cathode
  N7: LED(a).anode, R3.Pin_0, 0_01uF_2.0, R4.Pin_1
  N8: R4.Pin_0, R5.Pin_1

notes:
  1-
  1+
  GND
  Vp
  2+
  2-
  Vn
