# Fritzing sketch led_volt_reg_example1-bb (saved by Fritzing 0.9.3b)
breadboards: 1

parts:
  Q1 = NPN-Transistor [part_number=2N3904 package="TO92 [THT]"]
  Q2 = NPN-Transistor [part_number=2N3904 package="TO92 [THT]"]
  Q3 = NPN-Transistor [part_number=2N3904 package="TO92 [THT]"]
  U1 = OP482 - Low Power, High Speed JFET Quad Operational Amplifier [part_number=OP482]
  R1 = Resistor [tolerance=±5% resistance=2.2k package=THT]
  R2 = Resistor [tolerance=±5% resistance=4.7k package=THT]
  R3 = Resistor [tolerance=±5% resistance=100 package=THT]
  R4 = Trimmer Potentiometer [maximum_resistance=10kΩ package=THT]

nets:
  N1: Q1.E, Q2.E, Q3.E, U1.OUTD
  N2: Q1.C, Q2.B, R1.Pin_0, R3.Pin_0, R3.Pin_1
  N3: Q2.C, Q3.B, R4.wiper
  N4: Q3.C, U1.-IND, R1.Pin_1, R2.Pin_0, R4.leg2
  N5: U1.V+, R2.Pin_1

notes:
  1-
  1+
  Vn
  GND
  Vp
