# Fritzing sketch led_volt_reg_example2-bb (saved by Fritzing 0.9.3b)
breadboards: 1

parts:
  U1 = OP482 - Low Power, High Speed JFET Quad Operational Amplifier [part_number=OP482]
  Q3 = NPN-Transistor [part_number=2N3904 package="TO92 [THT]"]
  Q1_Q2 = SSM2212 - Audio Dual Matched NPN Transistor [part_number=SSM2212]
  Q1_Q2_1 = AnalogDevices_SSM2212RZ_subpart1 [part_number=SSM2212]  # not connected
  Q1_Q2_3 = AnalogDevices_SSM2212RZ_subpart3 [part_number=SSM2212]  # not connected
  R1 = Resistor [tolerance=±5% resistance=100 package=THT]
  R2 = Resistor [tolerance=±5% resistance=2.2k package=THT]
  Q4 = NPN-Transistor [part_number=2N3904 package="TO92 [THT]"]
  R3 = Trimmer Potentiometer [maximum_resistance=10kΩ package=THT]
  R4 = Resistor [tolerance=±5% resistance=4.7k package=THT]
  C1 = Tantalum Capacitor [capacitance=1nF package="C 6032 [SMD, tantalum]"]

nets:
  N1: U1.V+, Q4.C, R4.Pin_1, C1.+
  N2: U1.-IND, Q3.C, R2.Pin_1, Q4.E, R3.leg2
  N3: U1.OUTD, Q3.E, Q1_Q2.connector3, Q1_Q2.connector6
  N4: Q3.B, Q1_Q2.connector1, R3.wiper
  N5: Q1_Q2.connector2, Q1_Q2.connector8, R1.Pin_0
  N6: Q1_Q2.connector7, R1.Pin_1, R2.Pin_0
  N7: Q4.B, R4.Pin_0, C1.-

notes:
  1-
  1+
  Vn
  GND
  Vp
  4.7kΩ
