# Fritzing sketch nmos_id_vs_vgs-bb (saved by Fritzing 0.9.3b)
breadboards: 1

parts:
  Q1 = NPN-Transistor [package="TO92 [THT]"]
  R1 = Resistor [tolerance=±5% resistance=100 package="0805 [SMD]"]

nets:
  N1: Q1.C, R1.Pin_0

notes:
  Vp
  2+
  2-
  W1
  1+
  1-
  GND
  100Ω
  ZVN2110A
