# Fritzing sketch ohm_law_bb (saved by Fritzing 0.9.3b)
breadboards: 1

parts:
  R1 = Resistor [tolerance=±5% resistance=470 package=THT]
  LED1 = smd LED [color="Red (633nm)" package="0805 [SMD]"]

nets:
  N1: R1.Pin_1, LED1.cathode

notes:
  V+
  GND
  470Ω
  +2
  -1
  -2
  +1
