# Fritzing sketch inv_hys_com-bb (saved by Fritzing 0.9.3b)
breadboards: 1

parts:
  R2 = Resistor [tolerance=±5% resistance=10k package=THT]
  R3 = Resistor [tolerance=±5% resistance=10k package=THT]
  U2 = OP37 - Low Noise, Precision, High Speed Op Amp [part_number=OP37]
  R1 = Resistor [tolerance=±5% resistance=10k package=THT]

nets:
  N1: R2.Pin_0, U2.+IN, R1.Pin_0
  N2: R2.Pin_1, R3.Pin_1
  N3: R3.Pin_0, U2.OUT, R1.Pin_1

notes:
  GND
  Vp
  1+
  2-
  1-
  2+
  Vn
  W1
  10KΩ
