# Fritzing sketch non_inv_hys_com-bb (saved by Fritzing 0.9.3b)
breadboards: 1

parts:
  R1 = Resistor [tolerance=±0.05% resistance=22k package=THT]
  R2 = Resistor [tolerance=±5% resistance=10k package=THT]
  R3 = Resistor [tolerance=±5% resistance=10k package=THT]
  U2 = OP37 - Low Noise, Precision, High Speed Op Amp [part_number=OP37]

nets:
  N1: R1.Pin_0, R2.Pin_0, U2.+IN
  N2: R1.Pin_1, R3.Pin_0, U2.OUT
  N3: R3.Pin_1, U2.-IN

notes:
  GND
  Vp
  1+
  2-
  1-
  2+
  Vn
  W1
  10KΩ
  20KΩ
