# Fritzing sketch optic_indicator_vlevel-bb (saved by Fritzing 0.9.3b)
breadboards: 1

parts:
  U1 = ADTL082 - Dual JFET Input Op Amps [part_number=ADTL082]
  U1_1 = AnalogDevices_ADTL082ARZ_subpart1 [part_number=ADTL082]  # not connected
  U1_2 = AnalogDevices_ADTL082ARZ_subpart2 [part_number=ADTL082]  # not connected
  R1 = Resistor [tolerance=±5% resistance=470 package="1206 [SMD]"]
  LED1 = LED - 5mm [color="Red (633nm)" package="5 mm [THT]"]
  LED2 = LED - 5mm [color="Green (565nm)" package="5 mm [THT]"]
  R2 = Resistor [tolerance=±5% resistance=470 package="1206 [SMD]"]
  R3 = Resistor [tolerance=±5% resistance=470 package="1206 [SMD]"]
  LED3 = LED - 5mm [color="Yellow (585nm)" package="5 mm [THT]"]
  R4 = Resistor [tolerance=±5% resistance=22k package="1206 [SMD]"]
  R5 = Resistor [tolerance=±5% resistance=22k package="1206 [SMD]"]
  R6 = Resistor [tolerance=±5% resistance=10k package="1206 [SMD]"]

nets:
  N1: U1.connector1, LED1.cathode, R2.Pin_1
  N2: U1.connector2, R4.Pin_0, R5.Pin_1
  N3: U1.connector3, U1.connector5
  N4: U1.connector6, R5.Pin_0, R6.Pin_1
  N5: U1.connector7, LED2.cathode, R3.Pin_1
  N6: U1.connector8, R1.Pin_1
  N7: R1.Pin_0, LED1.anode
  N8: LED2.anode, R2.Pin_0
  N9: R3.Pin_0, LED3.anode
  N10: LED3.cathode, R4.Pin_1

notes:
  Vp
  W1
  GND
  W2
  Vn
  20kΩ
  10kΩ
  470Ω
  D1
  D2
  D3
