# Fritzing sketch simple_comp-bb (saved by Fritzing 0.9.3b)
breadboards: 1

parts:
  R3 = Resistor [tolerance=±5% resistance=10k package=THT]
  U2 = OP37 - Low Noise, Precision, High Speed Op Amp [part_number=OP37]

nets:
  N1: R3.Pin_0, U2.OUT

notes:
  GND
  Vp
  1+
  2-
  1-
  2+
  Vn
  W2
  10KΩ
  W1
