# Fritzing sketch opamp_settling_time-bb (saved by Fritzing 0.9.3b)
breadboards: 1

parts:
  U1 = OP27 - Low Noise, Precision Op Amp [part_number=OP27]
  R1 = Resistor [tolerance=±5% resistance=10k package="2512 [SMD]"]
  R2 = Resistor [tolerance=±5% resistance=10k package="2512 [SMD]"]
  R3 = Trimmer Potentiometer [maximum_resistance=10kΩ package=THT]
  D1 = Zener Diode [part_number=1N4732A breakdown_voltage=3.6V package="300 mil [THT]"]
  D2 = Zener Diode [part_number=1N4732A breakdown_voltage=3.6V package="300 mil [THT]"]

nets:
  N1: U1.-IN, R1.Pin_1, R2.Pin_0
  N2: U1.OUT, R2.Pin_1, R3.leg2
  N3: R1.Pin_0, R3.leg1
  N4: R3.wiper, D1.cathode, D2.anode
  N5: D1.anode, D2.cathode

notes:
  Vn
  GND
  2+
  2-
  1-
  1+
  Vp
  W1
  10kΩ
  1N914
