# Fritzing sketch optocoupler-bb (saved by Fritzing 0.9.3b)
breadboards: 1

parts:
  LED1 = LED - 5mm [color="Infrared (940nm)" part_number=QED123 package="5 mm [THT]"]
  LED2 = LED - 5mm [color="Blue (430nm)" part_number=QSD123 package="5 mm [THT]"]
  R1 = Resistor [tolerance=±5% resistance=2.2k package=THT]
  R2 = Resistor [tolerance=±5% resistance=2.2k package=THT]

nets:
  N1: LED1.cathode, LED2.cathode
  N2: LED1.anode, R2.Pin_1
  N3: LED2.anode, R1.Pin_0

notes:
  1-
  1+
  2-
  2+
  W1
  GND
  Vp
