# Fritzing sketch v_to_i_led_drive-bb (saved by Fritzing 0.9.3b)
breadboards: 1

parts:
  U1 = OP27 - Low Noise, Precision Op Amp [part_number=OP27]
  R1 = Resistor [tolerance=±5% resistance=2.2k package=THT]
  LED2 = LED - 5mm [color="Infrared (940nm)" part_number=QED123 package="5 mm [THT]"]
  LED3 = LED - 5mm [color="Blue (430nm)" part_number=QSD123 package="5 mm [THT]"]
  R2 = Resistor [tolerance=±5% resistance=2.2k package=THT]

nets:
  N1: U1.-IN, R1.Pin_1, LED2.anode
  N2: U1.+IN, R2.Pin_1
  N3: U1.OUT, LED2.cathode
  N4: U1.V+, LED3.anode
  N5: LED3.cathode, R2.Pin_0

notes:
  1-
  1+
  2-
  2+
  W1
  Vn
  GND
  Vp
