# Fritzing sketch push_pull_out_stage-bb (saved by Fritzing 0.9.3b)
breadboards: 1

parts:
  Q1 = NPN-Transistor [part_number=2N3904 package="SOT-23 [SMD]"]
  R1 = Resistor [tolerance=±5% resistance=100 package=THT]
  Q2 = PNP-Transistor [part_number=2N3906 package="TO92 [THT]"]
  R2 = Resistor [tolerance=±5% resistance=100 package=THT]
  R3 = Resistor [tolerance=±5% resistance=2.2k package=THT]

nets:
  N1: Q1.2, Q2.E, R3.Pin_0
  N2: Q1.0, Q2.B
  N3: Q1.1, R1.Pin_1
  N4: Q2.C, R2.Pin_0

notes:
  1-
  1+
  2-
  2+
  W1
  Vn
  GND
  Vp
