# Fritzing sketch push_pull_out_stage_zero_cross_dist_elim-bb (saved by Fritzing 0.9.3b)
breadboards: 1

parts:
  U1 = SSM2212 - Audio Dual Matched NPN Transistor [part_number=SSM2212]
  U1_1 = AnalogDevices_SSM2212RZ_subpart1 [part_number=SSM2212]  # not connected
  U1_3 = AnalogDevices_SSM2212RZ_subpart3 [part_number=SSM2212]  # not connected
  U2 = SSM2220 - Audio Dual Matched PNP Transistor [part_number=SSM2220]
  U2_1 = AnalogDevices_SSM2220S_subpart1 [part_number=SSM2220]  # not connected
  U2_3 = AnalogDevices_SSM2220S_subpart3 [part_number=SSM2220]  # not connected
  R1 = Resistor [tolerance=±5% resistance=10k package=THT]
  R2 = Resistor [tolerance=±5% resistance=100 package=THT]
  R3 = Resistor [tolerance=±5% resistance=10k package=THT]
  R4 = Resistor [tolerance=±5% resistance=100 package=THT]
  R5 = Resistor [tolerance=±5% resistance=2.2k package=THT]

nets:
  N1: U1.connector1, R2.Pin_1
  N2: U1.connector2, U1.connector7, U1.connector8, R1.Pin_1
  N3: U1.connector3, U2.connector3, R5.Pin_0
  N4: U1.connector6, U2.connector6
  N5: U2.connector1, R4.Pin_1
  N6: U2.connector2, U2.connector7, U2.connector8, R3.Pin_1
  N7: R1.Pin_0, R2.Pin_0
  N8: R3.Pin_0, R4.Pin_0

notes:
  1-
  1+
  2-
  2+
  W1
  Vn
  GND
  Vp
