# Fritzing sketch apltz_bb (saved by Fritzing 0.9.3b)
breadboards: 1

parts:
  R1 = Resistor [tolerance=±5% resistance=10k package=THT]
  Q1 = NPN-Transistor [part_number=2N3904 package="TO92 [THT]"]
  R2 = Resistor [tolerance=±5% resistance=4.7k package=THT]
  L1 = Inductors [package=cr54-kit]
  C2 = Ceramic Capacitor [capacitance=10pF package="100 mil [THT, multilayer]"]
  R3 = Resistor [tolerance=±5% resistance=4.7k package=THT]
  Q2 = NPN-Transistor [part_number=2N3904 package="TO92 [THT]"]

nets:
  N1: R1.Pin_1, Q1.E, Q2.E
  N2: Q1.B, R2.Pin_0
  N3: Q1.C, L1.2, C2.1, R3.Pin_0
  N4: R2.Pin_1, L1.1, C2.0, Q2.C
  N5: R3.Pin_1, Q2.B

notes:
  Vn
  2-
  1-
  2+
  1+
  GND
  100pF
  100uH
