# Fritzing sketch complete_pll-bb (saved by Fritzing 0.9.3b)
breadboards: 1

parts:
  VCC1 = Battery block 9V
  Q1 = PNP-Transistor [part_number=ZVP2110A package="TO92 [THT]"]
  IC1 = IC, DIP package, 14 pins [chip_label=HEF4007]
  Q2 = NPN-Transistor [part_number=ZVN2110A package="TO92 [THT]"]
  R1 = Resistor [tolerance=±5% resistance=2.2k package=THT]
  U1 = AD654 - Low Cost Monolithic Voltage-to-Frequency Converter [part_number=AD654]
  R2 = Resistor [tolerance=±5% resistance=10k package=THT]
  100pF = Capacitor [package=cap-pth-small2]
  R3 = Resistor [tolerance=±5% resistance=4.7k package=THT]
  C2 = Ceramic Capacitor [capacitance=4.7nF package="100 mil [THT, multilayer]"]

nets:
  N1: VCC1.-, IC1.pin7, Q2.E, U1.5V, U1.STROBE, R2.Pin_1, C2.0
  N2: VCC1.+, U1.VBG, 100pF.2
  N3: Q1.E, IC1.pin14, R1.Pin_0
  N4: Q1.B, IC1.pin1, IC1.pin9, Q2.B
  N5: Q1.C, IC1.pin4, IC1.pin11, Q2.C
  N6: IC1.pin2, IC1.pin5, IC1.pin12, R3.Pin_0
  N7: IC1.pin3, IC1.pin6, R1.Pin_1, U1.10V
  N8: IC1.pin8, IC1.pin10, IC1.pin13
  N9: U1.2p5V, R2.Pin_0
  N10: U1.CAP, 100pF.1
  N11: R3.Pin_1, C2.1

notes:
  1-
  1+
  2-
  2+
  W1
  GND
  Vp
