# Fritzing sketch polyphase_amp-bb (saved by Fritzing 0.9.3b)
breadboards: 1

parts:
  Q1 = NPN-Transistor [part_number=2N3904 package="TO92 [THT]"]
  Q2 = NPN-Transistor [part_number=2N3904 package="TO92 [THT]"]
  R1 = Resistor [tolerance=±5% resistance=10 package=THT]
  R2 = Resistor [tolerance=±5% resistance=470 package=THT]
  R3 = Resistor [tolerance=±5% resistance=1k package=THT]
  R4 = Resistor [tolerance=±5% resistance=1k package=THT]
  R5 = Resistor [tolerance=±5% resistance=10k package=THT]
  R6 = Resistor [tolerance=±5% resistance=470 package=THT]
  R7 = Resistor [tolerance=±5% resistance=10 package=THT]
  R8 = Resistor [tolerance=±5% resistance=1k package=THT]
  U1 = SSM2212 - Audio Dual Matched NPN Transistor [part_number=SSM2212]
  U1_1 = AnalogDevices_SSM2212RZ_subpart1 [part_number=SSM2212]  # not connected
  U1_3 = AnalogDevices_SSM2212RZ_subpart3 [part_number=SSM2212]  # not connected
  C1 = Ceramic Capacitor [capacitance=100nF package="100 mil [THT, multilayer]"]
  C2 = Ceramic Capacitor [capacitance=1nF package="100 mil [THT, multilayer]"]
  R9 = Resistor [tolerance=±5% resistance=150 package=THT]
  L4 = Inductors [part_number=100uH package=cr54]
  L5 = Inductors [part_number=100uH package=cr54]
  C3 = Ceramic Capacitor [capacitance=1nF package="100 mil [THT, multilayer]"]
  R10 = Resistor [tolerance=±5% resistance=150 package=THT]
  C4 = Ceramic Capacitor [capacitance=100nF package="100 mil [THT, multilayer]"]

nets:
  N1: Q1.E, Q2.E
  N2: Q1.B, Q1.C, Q2.B, R3.Pin_0
  N3: Q2.C, R1.Pin_0, R7.Pin_0
  N4: R1.Pin_1, U1.connector6
  N5: R2.Pin_0, R6.Pin_0, R9.Pin_0, R10.Pin_1
  N6: R2.Pin_1, U1.connector8, L4.2, C3.0
  N7: R3.Pin_1, R4.Pin_0, R8.Pin_1, C1.0
  N8: R4.Pin_1, R5.Pin_0, U1.connector7
  N9: R6.Pin_1, U1.connector1, C2.1, L5.1
  N10: R7.Pin_1, U1.connector3
  N11: R8.Pin_0, U1.connector2, C1.1
  N12: C2.0, L4.1
  N13: L5.2, C3.1, R10.Pin_0, C4.0

notes:
  1-
  1+
  2-
  2+
  W1
  GND
  Vn
  Vp
  0.1uF
  n1
  n2
  n3
  n4
