# Fritzing sketch simp_first_order_pf-bb (saved by Fritzing 0.9.3b)
breadboards: 1

parts:
  C1 = Ceramic Capacitor [capacitance=1nF package="100 mil [THT, multilayer]"]
  R1 = Resistor [tolerance=±5% resistance=1k package=THT]
  R2 = Resistor [tolerance=±5% resistance=1k package=THT]
  C2 = Ceramic Capacitor [capacitance=1nF package="100 mil [THT, multilayer]"]

nets:
  N1: C1.0, R1.Pin_0
  N2: C1.1, R2.Pin_0
  N3: R1.Pin_1, C2.0
  N4: R2.Pin_1, C2.1

notes:
  1-
  1+
  2-
  2+
  W1
  GND
