# Fritzing sketch apulse_bb (saved by Fritzing 0.9.3b)
breadboards: 1

parts:
  C1 = Ceramic Capacitor [capacitance=1µF package="100 mil [THT, multilayer]"]
  Q1 = NPN-Transistor [part_number=2N3904 package="TO92 [THT]"]
  R1 = Resistor [tolerance=±5% resistance=470k package=THT]
  L1 = Inductors [part_number=100uH package=cr54]
  C2 = Ceramic Capacitor [capacitance=100nF package="100 mil [THT, multilayer]"]

nets:
  N1: C1.1, Q1.B, R1.Pin_0
  N2: Q1.E, L1.1, C2.0
  N3: Q1.C, R1.Pin_1
  N4: L1.2, C2.1

notes:
  1-
  1+
  2-
  2+
  W1
  GND
  Vp
  100pF
  0.1uF
