# Fritzing sketch pwm_carrier-bb (saved by Fritzing 0.9.3b)
breadboards: 1

parts:
  U1 = IC, DIP package, 8 pins [chip_label=OP97]
  R2 = Resistor [tolerance=±5% resistance=1k package="0402 [SMD]"]

nets:
  N1: U1.pin4, R2.Pin_1
  N2: U1.pin6, R2.Pin_0

notes:
  1kΩ
  W2
  W1
  Vp
  GND
  2+
  1+
  2-
  1-
