# Fritzing sketch pwm_dc_multivibr-bb (saved by Fritzing 0.9.3b)
breadboards: 1

parts:
  U1 = IC, DIP package, 8 pins [chip_label=OP97]
  R2 = Resistor [tolerance=±5% resistance=10k package=THT]
  R3 = Resistor [tolerance=±5% resistance=47k package=THT]
  R4 = Resistor [tolerance=±5% resistance=2.2k package=THT]
  R5 = Resistor [tolerance=±5% resistance=2.2k package=THT]
  C1 = Capacitor [package=cap-pth-small2]
  D3 = Rectifier Diode 10A [part_number=P1000K]
  D4 = Rectifier Diode 10A [part_number=P1000K]
  R6 = Trimmer Potentiometer [maximum_resistance=10kΩ package=THT]

nets:
  N1: U1.pin2, C1.2, D3.cathode, D4.anode
  N2: U1.pin3, R2.Pin_0, R3.Pin_1
  N3: U1.pin4, R5.Pin_0
  N4: U1.pin6, R2.Pin_1, R6.wiper
  N5: U1.pin7, R4.Pin_0
  N6: R3.Pin_0, R4.Pin_1, R5.Pin_1, C1.1
  N7: D3.anode, R6.leg1
  N8: D4.cathode, R6.leg2

notes:
  Vp
  GND
  1+
  1-
  Vn
  10kΩ
  2.2kΩ
  47kΩ
  0.1uF
  1N914
  2+
  2-
