# Fritzing sketch pwm_ref_voltage-bb (saved by Fritzing 0.9.3b)
breadboards: 1

parts:
  U1 = IC, DIP package, 8 pins [chip_label=OP97]
  R1 = Resistor [tolerance=±5% resistance=10k package=THT]
  R2 = Resistor [tolerance=±5% resistance=10k package=THT]
  R3 = Resistor [tolerance=±5% resistance=47k package=THT]
  R4 = Resistor [tolerance=±5% resistance=2.2k package=THT]
  R5 = Resistor [tolerance=±5% resistance=2.2k package=THT]
  C1 = Capacitor [package=cap-pth-small2]

nets:
  N1: U1.pin2, R3.Pin_1, C1.2
  N2: U1.pin3, R1.Pin_0
  N3: U1.pin4, R5.Pin_0
  N4: U1.pin6, R1.Pin_1, R2.Pin_1
  N5: U1.pin7, R4.Pin_0
  N6: R2.Pin_0, R3.Pin_0, R4.Pin_1, R5.Pin_1, C1.1

notes:
  Vp
  GND
  1+
  1-
  Vn
