# Fritzing sketch regulator_v2-bb (saved by Fritzing 0.9.3b)
breadboards: 1

parts:
  U1 = SSM2212 - Audio Dual Matched NPN Transistor [part_number=SSM2212]
  U1_1 = AnalogDevices_SSM2212RZ_subpart1 [part_number=SSM2212]  # not connected
  U1_3 = AnalogDevices_SSM2212RZ_subpart3 [part_number=SSM2212]  # not connected
  R1 = Resistor [tolerance=±5% resistance=2.2k package=THT]
  R2 = Resistor [tolerance=±5% resistance=100 package=THT]
  Q3 = TRANSISTOR_NPN [part_number=2N3904 package=to-92]
  R3 = Trimmer Potentiometer [maximum_resistance=10kΩ package=THT]
  Q4 = TRANSISTOR_NPN [part_number=2N3904 package=to-92]
  R4 = Resistor [tolerance=±5% resistance=4.7k package=THT]
  1nF = Capacitor [package=cap-pth-small2]

nets:
  N1: U1.connector1, U1.connector7
  N2: U1.connector2, R2.Pin_0, Q3.C
  N3: U1.connector3, U1.connector6, R1.Pin_1, Q3.E, R3.leg2, Q4.E
  N4: U1.connector8, Q4.B, R4.Pin_0, 1nF.2
  N5: R1.Pin_0, R2.Pin_1, Q3.B
  N6: Q4.C, R4.Pin_1, 1nF.1

notes:
  1-
  1+
  2-
  2+
  W1
  GND
