# Fritzing sketch paralel_RLC_bb (saved by Fritzing 0.9.3b)
breadboards: 1

parts:
  R1 = Resistor [tolerance=±5% resistance=100 package=THT]
  R2 = Resistor [tolerance=±5% resistance=1k package=THT]
  C1 = Electrolytic Capacitor [capacitance=1µF package="100 mil [THT, electrolytic]"]
  L1 = Inductors [package=cr54]
  L2 = Inductors [package=cr54]

nets:
  N1: R1.Pin_1, R2.Pin_0, C1.+, L1.2
  N2: R2.Pin_1, C1.-, L2.1
  N3: L1.1, L2.2

notes:
  GND
  +1
  W1
  -1
  +2
  -2
  100 Ω
  1 kΩ
  10 mH
  1 uF
