# Fritzing sketch band_gap_shunt_reg-bb (saved by Fritzing 0.9.3b)
breadboards: 1

parts:
  U1 = SSM2212 - Audio Dual Matched NPN Transistor [part_number=SSM2212]
  U1_1 = AnalogDevices_SSM2212RZ_subpart1 [part_number=SSM2212]  # not connected
  U1_2 = AnalogDevices_SSM2212RZ_subpart2 [part_number=SSM2212]  # not connected
  U1_3 = AnalogDevices_SSM2212RZ_subpart3 [part_number=SSM2212]  # not connected
  R1 = Resistor [tolerance=±5% resistance=100 package="1206 [SMD]"]
  R2 = Resistor [tolerance=±5% resistance=2.2k package="2010 [SMD]"]
  R3 = Resistor [tolerance=±5% resistance=1k package="2010 [SMD]"]
  R4 = Trimmer Potentiometer [maximum_resistance=10kΩ package=THT]
  Q1 = NPN-Transistor [part_number=2N3904 package="TO92 [THT]"]

nets:
  N1: U1.connector2, U1.connector7
  N2: U1.connector3, U1.connector5, R1.Pin_0, Q1.E
  N3: U1.connector4, R4.wiper, Q1.C
  N4: R1.Pin_1, R2.Pin_0
  N5: R2.Pin_1, R3.Pin_0, R4.leg2, Q1.B

notes:
  1+
  2+
  W1
  GND
