# Fritzing sketch circuit_emulate_scr-bb (saved by Fritzing 0.9.3b)
breadboards: 1

parts:
  R1 = Resistor [tolerance=±5% resistance=1k package=THT]
  R2 = Resistor [tolerance=±5% resistance=100k package=THT]
  Q1 = NPN-Transistor [part_number=2N3904 package="TO92 [THT]"]
  Q2 = PNP-Transistor [part_number=2N3906 package="TO92 [THT]"]
  R3 = Resistor [tolerance=±5% resistance=100k package=THT]
  R4 = Resistor [tolerance=±5% resistance=1k package=THT]

nets:
  N1: R1.Pin_1, R2.Pin_0, Q1.E
  N2: R2.Pin_1, Q1.B, Q2.E, R3.Pin_1
  N3: Q1.C, Q2.B, R3.Pin_0
  N4: Q2.C, R4.Pin_0

notes:
  W2
  1-
  1+
  2-
  2+
  W1
  GND
