# Fritzing sketch non_inv_amp-bb (saved by Fritzing 0.9.3b)
breadboards: 1

parts:
  U1 = OP37 - Low Noise, Precision, High Speed Op Amp [part_number=OP37]
  R1 = Resistor [tolerance=±5% resistance=1k package="0402 [SMD]"]
  R2 = Resistor [tolerance=±5% resistance=1k package="0402 [SMD]"]
  R3 = Resistor [tolerance=±5% resistance=10k package="0402 [SMD]"]

nets:
  N1: U1.-IN, R1.Pin_0, R2.Pin_1
  N2: U1.OUT, R1.Pin_1, R3.Pin_0
  N3: R2.Pin_0, R3.Pin_1

notes:
  1-
  1+
  2-
  2+
  W1
  Vn
  GND
  Vp
