# Fritzing sketch unity_gain_follower-bb (saved by Fritzing 0.9.3b)
breadboards: 1

parts:
  U1 = OP37 - Low Noise, Precision, High Speed Op Amp [part_number=OP37]

nets:
  N1: U1.-IN, U1.OUT

notes:
  1-
  1+
  2-
  2+
  W1
  Vn
  GND
  Vp
