# Fritzing sketch lt1054_2_to_1-bb (saved by Fritzing 0.9.3b)
breadboards: 1

parts:
  C1 = Electrolytic Capacitor [capacitance=10μF package="0605 [SMD, electrolytic]"]
  U1 = IC, DIP package, 8 pins [chip_label=IC]
  C2 = Electrolytic Capacitor [capacitance=10μF package="0605 [SMD, electrolytic]"]
  R1 = Resistor [tolerance=±5% resistance=1k package="2512 [SMD]"]
  R2 = Resistor [tolerance=±5% resistance=1 package="2512 [SMD]"]
  D1 = Rectifier Diode [part_number=1N4001 package="300 mil [THT]"]
  D2 = Rectifier Diode [part_number=1N4001 package="300 mil [THT]"]
  Q1 = NPN-Transistor [part_number=2N3904 package="TO92 [THT]"]
  R3 = Resistor [tolerance=±5% resistance=22k package="2512 [SMD]"]
  C3 = Ceramic Capacitor [capacitance=100nF package="100 mil [THT, multilayer]"]
  R4 = Resistor [tolerance=±5% resistance=47 package="2512 [SMD]"]  # not connected
  L1 = Inductors [package=cooper_up4b]

nets:
  N1: C1.+, R2.Pin_1, C3.1
  N2: U1.pin2, D1.anode, D2.cathode, L1.2
  N3: U1.pin3, C2.-, D2.anode, Q1.E
  N4: U1.pin6, R3.Pin_1
  N5: U1.pin8, C2.+, D1.cathode
  N6: R1.Pin_1, Q1.B
  N7: R2.Pin_0, L1.pin_5, L1.pin_8
  N8: Q1.C, R3.Pin_0
  N9: L1.1, L1.pin_4
  N10: L1.pin_3, L1.pin_6
  N11: L1.pin_7, L1.pin_10
  N12: L1.pin_9, L1.pin_12

notes:
  SHUT DOWN
  CONNECTION
  LT1054
  22kΩ
  22uF
  Vp
  1+
  1-
  2-
  2+
  GND
  IND. TAPS
  D0
  OSC. OVERRIDE
  SELECT TAP 1-6
  (SWITCH NODE)
  1kΩ
  1Ω
  (RIPPLE)
  1uF
  HPH1-1400L
  (or Arduino PWM)
  47Ω
  4
  5
  6
  1
  2
  3

custom parts:
  Inductors: Inductors Basic Inductor/Choke - 0603 and 1206. Footprints are not proven and vary greatly between part numbers.
