# Fritzing sketch lt1054_doubler_breadboard-bb (saved by Fritzing 0.9.3b)
breadboards: 1

parts:
  U1 = IC, DIP package, 8 pins [chip_label=IC]
  C2 = Electrolytic Capacitor [capacitance=10μF package="0605 [SMD, electrolytic]"]
  C3 = Electrolytic Capacitor [capacitance=10μF package="0605 [SMD, electrolytic]"]
  R1 = Resistor [tolerance=±5% resistance=1k package="2512 [SMD]"]
  C4 = Electrolytic Capacitor [capacitance=10μF package="0605 [SMD, electrolytic]"]
  D1 = Zener Diode [part_number=1N4732A breakdown_voltage=3.6V package="300 mil [THT]"]
  D2 = Zener Diode [part_number=1N4732A breakdown_voltage=3.6V package="300 mil [THT]"]

nets:
  N1: U1.pin2, C4.+
  N2: U1.pin3, C2.-, C3.+, R1.Pin_1
  N3: U1.pin8, C2.+, D1.anode
  N4: C3.-, R1.Pin_0, D2.cathode
  N5: C4.-, D1.cathode, D2.anode

notes:
  SHUT DOWN
  CONNECTION
  LT1054
  1kΩ
  47uF
  22uF
  Vp
  1+
  1-
  2-
  GND
  2+
  1N914
