# Fritzing sketch lt1054_inverter_breadboard-bb (saved by Fritzing 0.9.3b)
breadboards: 1

parts:
  C1 = Electrolytic Capacitor [capacitance=10μF package="0605 [SMD, electrolytic]"]
  U1 = IC, DIP package, 8 pins [chip_label=IC]
  C2 = Electrolytic Capacitor [capacitance=10μF package="0605 [SMD, electrolytic]"]
  C3 = Electrolytic Capacitor [capacitance=10μF package="0605 [SMD, electrolytic]"]
  R1 = Resistor [tolerance=±5% resistance=1k package="2512 [SMD]"]

nets:
  N1: C1.-, U1.pin2
  N2: C1.+, U1.pin4
  N3: U1.pin3, C2.-
  N4: U1.pin5, C3.-, R1.Pin_0
  N5: U1.pin8, C2.+
  N6: C3.+, R1.Pin_1

notes:
  SHUT DOWN
  CONNECTION
  LT1054
  1kΩ
  47uF
  22uF
  Vp
  1+
  1-
  2-
  2+
  GND
