# Fritzing sketch tmp01_2_bb (saved by Fritzing 0.9.3b)
breadboards: 1

parts:
  U1 = TMP01 - Low Power, Programmable Temperature Controller [part_number=TMP01]
  R1 = Resistor [tolerance=±5% resistance=10k package="0603 [SMD]"]
  R2 = Resistor [tolerance=±5% resistance=470 package="0603 [SMD]"]
  LED1 = smd LED [color="Red (633nm)" package="1206 [SMD]"]
  R3 = Resistor [tolerance=±5% resistance=470 package="0603 [SMD]"]
  LED3 = smd LED [color="Blue (430nm)" package="1206 [SMD]"]
  R4 = Resistor [tolerance=±5% resistance=220k package="0603 [SMD]"]
  R5 = Resistor [tolerance=±5% resistance=220k package="0603 [SMD]"]
  R6 = Resistor [tolerance=±5% resistance=220k package="0603 [SMD]"]

nets:
  N1: U1.10V, R4.Pin_0
  N2: U1.5V, R4.Pin_1, R5.Pin_0
  N3: U1.2p5V, R5.Pin_1, R6.Pin_0
  N4: U1.COMMON, U1.V+, R1.Pin_0, R2.Pin_0, R3.Pin_0, R6.Pin_1
  N5: U1.VBG, U1.CAP, R1.Pin_1, LED1.cathode, LED3.cathode
  N6: R2.Pin_1, LED1.anode
  N7: R3.Pin_1, LED3.anode

notes:
  GND
  1+
  V+
  1-
  TMP01
  LED1
  LED2
  470Ω
  10KΩ
  200KΩ
