# Fritzing sketch window_comp_bb (saved by Fritzing 0.9.3b)
breadboards: 1

parts:
  U1 = AD8561 - Ultrafast 7ns Single Supply Comparator [part_number=AD8561]
  U2 = AD8561 - Ultrafast 7ns Single Supply Comparator [part_number=AD8561]
  R1 = Resistor [tolerance=±5% resistance=10k package="2010 [SMD]"]
  R2 = Resistor [tolerance=±5% resistance=10k package="2010 [SMD]"]
  R3 = Resistor [tolerance=±5% resistance=10k package="2010 [SMD]"]
  C1 = Capacitor [package=cap-pth-small2]
  D1 = P1000K [part_number=P1000K]
  D2 = P1000K [part_number=P1000K]
  R4 = Resistor [tolerance=±5% resistance=22k package="2010 [SMD]"]
  Q1 = NPN-Transistor [package="SOT-23 [SMD]"]
  R5 = Resistor [tolerance=±5% resistance=470 package="2010 [SMD]"]
  LED1 = LED - 3mm [color="Red (633nm)" package="3 mm [THT]"]

nets:
  N1: U1.V+, U2.V+, C1.2, R5.Pin_0
  N2: U1.+IN, R1.Pin_1, R2.Pin_0
  N3: U1.-IN, U2.+IN
  GND: U1.V-, U1.LATCH, U1.GND, U2.V-, U2.LATCH, U2.GND, R1.Pin_0, Q1.1
  N4: U1.OUT, D2.anode
  N5: U2.-IN, R2.Pin_1, R3.Pin_0
  N6: U2.OUT, D1.anode
  N7: D1.cathode, D2.cathode, R4.Pin_1
  N8: R4.Pin_0, Q1.0
  N9: Q1.2, LED1.cathode
  N10: R5.Pin_1, LED1.anode

notes:
  V+
  2+
  1+
  W1
  2-
  1-
  GND
  470Ω
  20kΩ
  10kΩ
  2N3904
  1N914
  0.1uF
  AD8561
  W2
