# Fritzing sketch tilt_sensor_ADXL327_LED_bb (saved by Fritzing 0.9.3b)
breadboards: 1

parts:
  C3 = Capacitor [part_number="0.1 u" package=cap-pth-large]
  C4 = Capacitor [part_number="0.047 u" package=cap-pth-large]
  C5 = Capacitor [part_number="0.047 u" package=cap-pth-large]
  U2 = AD8561 - Ultrafast 7ns Single Supply Comparator [part_number=AD8561]
  U3 = AD8561 - Ultrafast 7ns Single Supply Comparator [part_number=AD8561]
  LED1 = LED - 3mm [color="Red (633nm)" package="3 mm [THT]"]
  LED2 = LED - 3mm [color="Yellow (595nm)" package="3 mm [THT]"]
  LED3 = LED - 3mm [color="Yellow (595nm)" package="3 mm [THT]"]
  R2 = Resistor [tolerance=±5% resistance=100 package="2010 [SMD]"]
  R3 = Resistor [tolerance=±5% resistance=100 package="2010 [SMD]"]
  LED4 = LED - 3mm [color="Red (633nm)" package="3 mm [THT]"]
  R4 = Resistor [tolerance=±5% resistance=100 package="2010 [SMD]"]
  U4 = ADXL327 - Small, Low Power, #-Axis +/-2G Accelerometer [part_number=ADXL327]
  R5 = Resistor [tolerance=±5% resistance=100 package="2010 [SMD]"]

nets:
  N1: C3.1, U4.VS#15
  N2: C3.2, C4.2, C5.2, LED1.cathode, LED2.cathode, LED3.cathode, LED4.cathode, U4.COM#3
  N3: C4.1, U3.+IN, U4.XOUT
  N4: C5.1, U2.+IN, U4.YOUT
  N5: U2.V+, U3.V+
  N6: U2.-IN, U3.-IN
  N7: U2.V-, U3.V-
  N8: U2.LATCH, U2.GND
  N9: U2.OUT, R5.Pin_1
  N10: U2.OUTB, R4.Pin_1
  N11: U3.LATCH, U3.GND
  N12: U3.OUT, R3.Pin_1
  N13: U3.OUTB, R2.Pin_1
  N14: LED1.anode, R5.Pin_0
  N15: LED2.anode, R4.Pin_0
  N16: LED3.anode, R2.Pin_0
  N17: R3.Pin_0, LED4.anode

notes:
  100 Ω
  +1
  V+
  0.1 uF
  0.047uF
  LED
  ADXL327
  V-
  W2
  W1
  GND
  -1
  +2
  -2
