# Fritzing sketch tilt_sensor_ADXL327_bb (saved by Fritzing 0.9.3b)
breadboards: 1

parts:
  C3 = Capacitor [part_number="0.1 u" package=cap-pth-large]
  C4 = Capacitor [part_number="0.047 u" package=cap-pth-large]
  C5 = Capacitor [part_number="0.047 u" package=cap-pth-large]
  U4 = ADXL327 - Small, Low Power, #-Axis +/-2G Accelerometer [part_number=ADXL327]

nets:
  N1: C3.1, U4.VS#14
  N2: C3.2, C4.2, C5.2, U4.COM#3
  N3: C4.1, U4.XOUT
  N4: C5.1, U4.YOUT

notes:
  +1
  0.1 uF
  0.047uF
  ADXL327
  GND
  -1
  +2
  -2
  V+
