# Fritzing sketch trans_coupled_amp_bb (saved by Fritzing 0.9.3b)
breadboards: 1

parts:
  2N3904 = NPN-Transistor [package="TO92 [THT]"]
  R1 = Resistor [tolerance=±5% resistance=10k package=THT]
  R2 = Resistor [tolerance=±5% resistance=20k package=THT]
  R4 = Resistor [tolerance=±5% resistance=47 package=THT]
  C1 = Tantalum Capacitor [capacitance=10µF package="100 mil [THT, tantalum]"]
  part = Transformer [package=transformer]  # not connected
  HPH1-1400L = BMA180 [package=lga12]
  R5 = Resistor [tolerance=±5% resistance=100 package=THT]
  C2 = Tantalum Capacitor [capacitance=1μF package="100 mil [THT, tantalum]"]

nets:
  N1: 2N3904.E, R4.Pin_1, C1.+
  N2: 2N3904.B, R1.Pin_1, R2.Pin_0, C2.+
  N3: 2N3904.C, HPH1-1400L.VDDIO
  N4: R1.Pin_0, R4.Pin_0, C1.-
  N5: R2.Pin_1, HPH1-1400L.NC
  N6: HPH1-1400L.VDD, HPH1-1400L.NC3
  N7: HPH1-1400L.VSS, HPH1-1400L.NC2
  N8: HPH1-1400L.INT, HPH1-1400L.SDO
  N9: HPH1-1400L.CSB, HPH1-1400L.SCK
  N10: HPH1-1400L.NC1, R5.Pin_1
  N11: HPH1-1400L.SDI, R5.Pin_0

notes:
  Vn
  1+
  W1
  Vp
  2+
  GND
  1-
  2-
