# Fritzing sketch trans_stepup_bb (saved by Fritzing 0.9.3b)
breadboards: 1

parts:
  HPH1-1400L_placeholder = BMA180 [package=lga12]
  R1 = Resistor [tolerance=±5% resistance=400 package=THT]
  R2 = Resistor [tolerance=±5% resistance=100 package=THT]
  U12 = mystery part, 3 pins [chip_label=?]
  U13 = mystery part, 3 pins [chip_label=?]
  U14 = mystery part, 3 pins [chip_label=?]

nets:
  N1: HPH1-1400L_placeholder.VDD, U12.pin1, U13.pin1, U14.pin1
  N2: HPH1-1400L_placeholder.VSS, R2.Pin_1, U12.pin2, U13.pin2, U14.pin2
  N3: HPH1-1400L_placeholder.INT, U12.pin3, U13.pin3, U14.pin3
  N4: HPH1-1400L_placeholder.NC1, HPH1-1400L_placeholder.SCK, R1.Pin_1
  N5: HPH1-1400L_placeholder.SDO, HPH1-1400L_placeholder.VDDIO
  N6: HPH1-1400L_placeholder.NC2, R1.Pin_0

notes:
  GND
  1+
  1-
  2-
  2+
  W1
