# Fritzing sketch transtc_bb (saved by Fritzing 0.9.3b)
breadboards: 1

parts:
  R1 = Resistor [tolerance=±5% resistance=100 package=THT]
  R2 = Resistor [tolerance=±5% resistance=100 package=THT]
  U12 = mystery part, 3 pins [chip_label=?]
  U13 = mystery part, 3 pins [chip_label=?]
  HPH1-1400L_placeholder = BMA180 [package=lga12]

nets:
  N1: R1.Pin_0, HPH1-1400L_placeholder.NC3
  N2: R1.Pin_1, HPH1-1400L_placeholder.NC1, HPH1-1400L_placeholder.SCK
  N3: R2.Pin_1, HPH1-1400L_placeholder.NC
  N4: U12.pin1, U12.pin3, U13.pin1, U13.pin3, HPH1-1400L_placeholder.VDD, HPH1-1400L_placeholder.INT
  N5: U12.pin2, U13.pin2, HPH1-1400L_placeholder.VSS, HPH1-1400L_placeholder.CSB
  N6: HPH1-1400L_placeholder.SDO, HPH1-1400L_placeholder.VDDIO
  N7: HPH1-1400L_placeholder.SDI, HPH1-1400L_placeholder.NC2

notes:
  2+
  2-
  1-
  GND
  1+
  W1
