# Fritzing sketch transient_response_RC_series_bb (saved by Fritzing 0.9.3b)
breadboards: 1

parts:
  C1 = Electrolytic Capacitor [capacitance=1µF package="100 mil [THT, electrolytic]"]
  R1 = Resistor [tolerance=±5% resistance=2.2k package=THT]

nets:
  N1: C1.+, R1.Pin_1

notes:
  W1
  +2
  -2
  -1
  GND
  +1
  2.2kΩ
  1 uF
