# Fritzing sketch transient_response_RL_series_bb (saved by Fritzing 0.9.3b)
breadboards: 1

parts:
  R1 = Resistor [tolerance=±5% resistance=100 package=THT]
  L1 = Inductors [package=cr54-kit]

nets:
  N1: R1.Pin_0, L1.2

notes:
  W1
  +2
  -2
  -1
  V+
  +1
  100 Ω
  10 uH
