# Fritzing sketch ttl_two_in_nand_bb (saved by Fritzing 0.9.3b)
breadboards: 1

parts:
  2N3904 = NPN-Transistor [package="TO92 [THT]"]
  2N3904_2 = NPN-Transistor [package="TO92 [THT]"]
  U1 = SSM2212 - Audio Dual Matched NPN Transistor [part_number=SSM2212]
  U1_1 = AnalogDevices_SSM2212RZ_subpart1 [part_number=SSM2212]  # not connected
  U1_3 = AnalogDevices_SSM2212RZ_subpart3 [part_number=SSM2212]  # not connected
  D1 = Rectifier Diode [part_number=1N914 package="300 mil [THT]"]
  R1 = Resistor [tolerance=±5% resistance=2.2k package=THT]
  R2 = Resistor [tolerance=±5% resistance=100 package=THT]
  R3 = Resistor [tolerance=±5% resistance=100k package=THT]
  R4 = Resistor [tolerance=±5% resistance=470 package=THT]
  2N3904_3 = NPN-Transistor [package="TO92 [THT]"]

nets:
  N1: 2N3904.B, 2N3904_2.B, R3.Pin_1, 2N3904_3.B
  N2: 2N3904.C, 2N3904_3.C
  N3: 2N3904_2.E, U1.connector2, R4.Pin_0
  N4: 2N3904_2.C, U1.connector7, R1.Pin_0
  N5: U1.connector1, D1.cathode
  N6: U1.connector3, R4.Pin_1
  N7: U1.connector6, D1.anode
  N8: U1.connector8, R2.Pin_1
  N9: R1.Pin_1, R2.Pin_0, R3.Pin_0

notes:
  W1
  1+
  Vp
  2+
  1-
  2-
  GND
  W2
  2.2kΩ
