# Fritzing sketch ef_tuned_amplifier-bb (saved by Fritzing 0.9.3b)
breadboards: 1

parts:
  R1 = Resistor [tolerance=±5% resistance=2.2k package=THT]
  C1 = Capacitor [package=cap-pth-small2]
  R2 = Resistor [tolerance=±5% resistance=1k package=THT]
  C2 = Capacitor [package=cap-pth-small2]
  L1 = Inductors [package=cr54]
  Q1 = NPN-Transistor [package="SOT-23 [SMD]"]
  R3 = Resistor [tolerance=±5% resistance=1k package=THT]

nets:
  N1: R1.Pin_1, C1.1, R2.Pin_0
  N2: C1.2, C2.1, L1.1
  N3: R2.Pin_1, C2.2, L1.2, Q1.0
  N4: Q1.1, R3.Pin_0

notes:
  Vn
  Vp
  W1
  1+
  2+
  1-
  2-
  GND
  2.2kΩ
  1kΩ
  100uF
  1nF
  2N3904
