# Fritzing sketch quad_amplifier-bb (saved by Fritzing 0.9.3b)
breadboards: 1

parts:
  C1 = Capacitor [package=cap-pth-small2]
  R2 = Resistor [tolerance=±5% resistance=470 package=THT]
  C2 = Capacitor [package=cap-pth-small2]
  L1 = Inductors [package=cr54]
  Q1 = NPN-Transistor [package="SOT-23 [SMD]"]
  R3 = Resistor [tolerance=±5% resistance=1k package=THT]
  R4 = Resistor [tolerance=±5% resistance=470 package=THT]
  Q2 = NPN-Transistor [package="SOT-23 [SMD]"]
  R5 = Resistor [tolerance=±5% resistance=1k package=THT]

nets:
  N1: C1.1, R4.Pin_0
  N2: C1.2, R2.Pin_0, C2.1, L1.1, Q1.0
  N3: R2.Pin_1, C2.2, L1.2
  N4: Q1.2, Q2.2
  N5: Q1.1, R3.Pin_0
  N6: R3.Pin_1, R5.Pin_1
  N7: R4.Pin_1, Q2.0
  N8: Q2.1, R5.Pin_0

notes:
  Vn
  Vp
  W1
  1+
  2+
  1-
  2-
  GND
  1kΩ
  100uF
  1nF
  2N3904
  470Ω
