# Fritzing sketch added_2pole_hpf_bb (saved by Fritzing 0.9.3b)
breadboards: 1

parts:
  2N3904 = NPN-Transistor [package="TO92 [THT]"]
  R1 = Resistor [tolerance=±5% resistance=1M package=THT]
  C1 = Ceramic Capacitor [capacitance=0.1µF package="100 mil [THT, multilayer]"]
  R4 = Resistor [tolerance=±5% resistance=3.9k package=THT]
  100uH = Inductors [package=cr54]
  C2 = Ceramic Capacitor [capacitance=1nF package="100 mil [THT, multilayer]"]
  C3 = Ceramic Capacitor [capacitance=0.1µF package="100 mil [THT, multilayer]"]
  R5 = Resistor [tolerance=±5% resistance=100 package=THT]
  R6 = Resistor [tolerance=±5% resistance=1.3k package=THT]
  R7 = Resistor [tolerance=±5% resistance=1.5k package=THT]
  C4 = Ceramic Capacitor [capacitance=100nF package="100 mil [THT, multilayer]"]
  R8 = Resistor [tolerance=±5% resistance=10k package=THT]

nets:
  N1: 2N3904.E, R5.Pin_1, R6.Pin_1
  N2: 2N3904.B, R7.Pin_1, C4.0, R8.Pin_0
  N3: R1.Pin_0, C3.1
  N4: C1.0, R4.Pin_1
  N5: C1.1, R6.Pin_0, C4.1
  N6: 100uH.1, C2.1, R8.Pin_1
  N7: 100uH.2, C2.0, C3.0
  N8: R5.Pin_0, R7.Pin_0

notes:
  Vn
  W1
  1+
  Vp
  2+
  2-
  1-
  GND
