# Fritzing sketch ce_tuned_amp_bb (saved by Fritzing 0.9.3b)
breadboards: 1

parts:
  2N3904 = NPN-Transistor [package="TO92 [THT]"]
  R1 = Resistor [tolerance=±5% resistance=10k package=THT]
  C1 = Ceramic Capacitor [capacitance=0.1µF package="100 mil [THT, multilayer]"]
  R2 = Resistor [tolerance=±5% resistance=100 package=THT]
  R3 = Resistor [tolerance=±5% resistance=1.5k package=THT]
  R4 = Resistor [tolerance=±5% resistance=3.9k package=THT]
  100uH = Inductors [package=cr54]
  C2 = Ceramic Capacitor [capacitance=1nF package="100 mil [THT, multilayer]"]
  C3 = Ceramic Capacitor [capacitance=0.1µF package="100 mil [THT, multilayer]"]
  R5 = Resistor [tolerance=±5% resistance=1M package=THT]

nets:
  N1: 2N3904.E, R2.Pin_0
  N2: 2N3904.B, R1.Pin_0, C1.1, R3.Pin_0
  N3: 2N3904.C, 100uH.2, C2.0, C3.0
  N4: R1.Pin_1, 100uH.1, C2.1
  N5: C1.0, R4.Pin_1
  N6: R2.Pin_1, R3.Pin_1
  N7: C3.1, R5.Pin_0

notes:
  Vn
  W1
  1+
  Vp
  2+
  2-
  1-
  GND
