# Fritzing sketch diff_amp_stage_single_ended_load_bb (saved by Fritzing 0.9.3b)
breadboards: 1

parts:
  U1 = SSM2212 - Audio Dual Matched NPN Transistor [part_number=SSM2212]
  U1_1 = AnalogDevices_SSM2212RZ_subpart1 [part_number=SSM2212]  # not connected
  U1_3 = AnalogDevices_SSM2212RZ_subpart3 [part_number=SSM2212]  # not connected
  R1 = Resistor [tolerance=±5% resistance=2.2k package=THT]
  R2 = Resistor [tolerance=±5% resistance=1k package=THT]
  2N3904 = NPN-Transistor [package="TO92 [THT]"]
  R3 = Resistor [tolerance=±5% resistance=100 package=THT]
  R4 = Resistor [tolerance=±5% resistance=2.2k package=THT]
  R5 = Resistor [tolerance=±5% resistance=4.7k package=THT]
  R6 = Resistor [tolerance=±5% resistance=1k package=THT]
  C1 = Ceramic Capacitor [capacitance=0.1µF package="100 mil [THT, multilayer]"]
  100uH = Inductors [package=cr54]
  C2 = Ceramic Capacitor [capacitance=1nF package="100 mil [THT, multilayer]"]
  C3 = Ceramic Capacitor [capacitance=0.1µF package="100 mil [THT, multilayer]"]
  R7 = Resistor [tolerance=±5% resistance=1M package=THT]

nets:
  N1: U1.connector1, 100uH.1, C2.0, C3.0
  N2: U1.connector2, R6.Pin_1, C1.0
  N3: U1.connector3, U1.connector6, 2N3904.C
  N4: U1.connector7, R1.Pin_1, R2.Pin_1
  N5: U1.connector8, 100uH.2, C2.1
  N6: R2.Pin_0, R5.Pin_1
  N7: 2N3904.E, R3.Pin_1
  N8: 2N3904.B, R4.Pin_1, R5.Pin_0
  N9: R3.Pin_0, R4.Pin_0
  N10: R6.Pin_0, C1.1, R7.Pin_0
  N11: C3.1, R7.Pin_1

notes:
  Vn
  W1
  Vp
  GND
  2-
  1-
  1+
