# Fritzing sketch var_gain_amp_crl-bb (saved by Fritzing 0.9.3b)
breadboards: 1

parts:
  U1 = OP37 - Low Noise, Precision, High Speed Op Amp [part_number=OP37]
  R1 = Resistor [tolerance=±5% resistance=10k package="0402 [SMD]"]
  R2 = Resistor [tolerance=±5% resistance=10k package="0402 [SMD]"]
  R3 = Resistor [tolerance=±5% resistance=10k package="0402 [SMD]"]
  U2 = TRANSISTOR_NPN_2 [package=to-92]
  R4 = Resistor [tolerance=±5% resistance=10k package="0402 [SMD]"]
  R5 = Resistor [tolerance=±5% resistance=1k package="0402 [SMD]"]

nets:
  N1: U1.-IN, R2.Pin_0, R3.Pin_1, R4.Pin_1
  N2: U1.OUT, R1.Pin_0, R2.Pin_1
  N3: R1.Pin_1, R3.Pin_0, U2.C
  N4: U2.B, R5.Pin_1
  N5: U2.E, R4.Pin_0

notes:
  W2
  Vp
  2+
  1+
  W1
  Vn
  GND
  2-
  1-
  10kΩ
  1kΩ
  OP97
  2N3904
