# Fritzing sketch var_gain_amp_pot-bb (saved by Fritzing 0.9.3b)
breadboards: 1

parts:
  U1 = OP37 - Low Noise, Precision, High Speed Op Amp [part_number=OP37]
  R1 = Resistor [tolerance=±5% resistance=10k package="0402 [SMD]"]
  R2 = Resistor [tolerance=±5% resistance=10k package="0402 [SMD]"]
  R6 = Trimmer Potentiometer [maximum_resistance=10kΩ package=THT]
  R7 = Resistor [tolerance=±5% resistance=10k package="0402 [SMD]"]

nets:
  N1: U1.-IN, R2.Pin_0, R7.Pin_1
  N2: U1.+IN, R6.wiper
  N3: U1.OUT, R1.Pin_0, R2.Pin_1
  N4: R1.Pin_1, R6.leg2
  N5: R6.leg1, R7.Pin_0

notes:
  Vp
  2+
  1+
  W1
  Vn
  GND
  2-
  1-
  10kΩ
  OP97
