# Fritzing sketch setup_meas_cm-bb (saved by Fritzing 0.9.3b)
breadboards: 1

parts:
  C1 = Tantalum Capacitor [capacitance=39pF package="D 7343 [SMD, tantalum]"]
  R1 = Resistor [tolerance=±5% resistance=10k package="2512 [SMD]"]

nets:
  N1: C1.+, R1.Pin_0

notes:
  1-
  1+
  2-
  2+
  W1
  GND
