# Fritzing sketch setup_meas_diode_cap-bb (saved by Fritzing 0.9.3b)
breadboards: 1

parts:
  R1 = Resistor [tolerance=±5% resistance=10k package="2512 [SMD]"]
  D1 = Rectifier Diode [part_number=1N4001 package="300 mil [THT]"]

nets:
  N1: R1.Pin_0, D1.anode

notes:
  1-
  1+
  2-
  2+
  W1
  GND
