# Fritzing sketch zener_reg_bb (saved by Fritzing 0.9.3b)
breadboards: 1

parts:
  R1 = Resistor [tolerance=±5% resistance=1k package=THT]
  D1 = Rectifier Diode [part_number=1N4735 package="300 mil [THT]"]
  RL = Resistor [tolerance=±5% resistance=100 package=THT]

nets:
  N1: R1.Pin_1, D1.cathode, RL.Pin_0
  N2: D1.anode, RL.Pin_1

notes:
  Vn
  1-
  W1
  2+
  2-
